// Logisim project data.circ as structural Verilog: 27 circuits, main circuit ◆海明传输测试1
module \国标转区位码  (
  input  [15:0] GB2312,
  output [6:0] \区号 ,
  output [6:0] \位号 
);

  wire [15:0] subtractor_1_out;
  wire [15:7] adder_1_out;

  // Probe on GB2312
  // Probe on {adder_1_out[15], \区号 , adder_1_out[7], \位号 }
  Adder #(.width(16)) adder_1 (
    .a(GB2312), .b(16'hdfe0), .out({adder_1_out[15], \区号 , adder_1_out[7], \位号 }));  // open: cin, cout
  Subtractor #(.width(16)) subtractor_1 (.a(GB2312), .b(16'h2020), .out(subtractor_1_out));  // open: bin, bout
  // Probe on subtractor_1_out
  // Probe on \区号 
  // Probe on \位号 

  // Notes on the sheet:
  //   请勿增改引脚，请勿修改子电路封装
  //   输入引脚区
  //   请在下方利用上方输入输出引脚的隧道标签信号构建电路，ctrl+d复制选择组件
  //   华中科技大学计算机学院 计算机组成原理课程组
  //   要求用加法器完成
  //   输出引脚区
  //   探测区
endmodule

module \汉字显示  (
  output [15:0] out_1
);

  wire button_1_out, \时钟_out ;
  wire [6:0] \国标转区位码_1_位号 , \国标转区位码_1_区号 ;
  wire [7:0] counter_1_q;
  wire [31:0] \字库_1_out_3 , \字库_1_out_4 , \字库_1_out_5 , \字库_1_out_6 , \字库_1_out_7 , \字库_1_out_8 ,
       \字库_1_out_9 , \字库_1_out_10 , \字库_1_out_11 , \字库_1_out_12 , \字库_1_out_13 , \字库_1_out_14 ,
       \字库_1_out_15 , \字库_1_out_16 , \字库_1_out_17 , \字库_1_out_18 , \字库_1_out_19 , \字库_1_out_20 ,
       \字库_1_out_21 , \字库_1_out_22 , \字库_1_out_23 , \字库_1_out_24 , \字库_1_out_25 , \字库_1_out_26 ,
       \字库_1_out_27 , \字库_1_out_28 , \字库_1_out_29 , \字库_1_out_30 , \字库_1_out_31 , \字库_1_out_32 ,
       \字库_1_out_33 , \字库_1_out_34 ;

  // Probe on out_1
  Counter #(.width(8), .max('hff), .ongoal("wrap"), .trigger("rising"), .behavior("old")) counter_1 (
    .Q(counter_1_q), .clk(\时钟_out ), .clr(button_1_out));  // open: load, D, count, carry, preset
  Clock #(.highDuration(1), .lowDuration(1)) \u_时钟  (.out(\时钟_out ));
  Button button_1 (.out(button_1_out));
  ROM #(.addrWidth(8), .dataWidth(16), .Select("high")) rom_1 (.addr(counter_1_q), .data(out_1));
  \国标转区位码  \u_国标转区位码_1  (.\位号 (\国标转区位码_1_位号 ), .\区号 (\国标转区位码_1_区号 ), .GB2312(out_1));
  \字库  \u_字库_1  (
    .out_3(\字库_1_out_3 ), .out_4(\字库_1_out_4 ), .out_5(\字库_1_out_5 ), .out_6(\字库_1_out_6 ),
    .out_7(\字库_1_out_7 ), .out_8(\字库_1_out_8 ), .out_9(\字库_1_out_9 ), .out_10(\字库_1_out_10 ),
    .out_11(\字库_1_out_11 ), .out_12(\字库_1_out_12 ), .out_13(\字库_1_out_13 ), .out_14(\字库_1_out_14 ),
    .out_15(\字库_1_out_15 ), .out_16(\字库_1_out_16 ), .out_17(\字库_1_out_17 ), .out_18(\字库_1_out_18 ),
    .out_19(\字库_1_out_19 ), .out_20(\字库_1_out_20 ), .out_21(\字库_1_out_21 ), .out_22(\字库_1_out_22 ),
    .out_23(\字库_1_out_23 ), .out_24(\字库_1_out_24 ), .out_25(\字库_1_out_25 ), .out_26(\字库_1_out_26 ),
    .out_27(\字库_1_out_27 ), .out_28(\字库_1_out_28 ), .out_29(\字库_1_out_29 ), .out_30(\字库_1_out_30 ),
    .out_31(\字库_1_out_31 ), .out_32(\字库_1_out_32 ), .out_33(\字库_1_out_33 ), .out_34(\字库_1_out_34 ),
    .\区号 (\国标转区位码_1_区号 ), .\位号 (\国标转区位码_1_位号 ));
  DotMatrix #(.inputtype("row"), .matrixcols(32), .matrixrows(32), .persist(0), .dotshape("circle")) dotmatrix_1 (
    .row0(\字库_1_out_3 ), .row1(\字库_1_out_4 ), .row2(\字库_1_out_5 ), .row3(\字库_1_out_6 ), .row4(\字库_1_out_7 ),
    .row5(\字库_1_out_8 ), .row6(\字库_1_out_9 ), .row7(\字库_1_out_10 ), .row8(\字库_1_out_11 ),
    .row9(\字库_1_out_12 ), .row10(\字库_1_out_13 ), .row11(\字库_1_out_14 ), .row12(\字库_1_out_15 ),
    .row13(\字库_1_out_16 ), .row14(\字库_1_out_17 ), .row15(\字库_1_out_18 ), .row16(\字库_1_out_19 ),
    .row17(\字库_1_out_20 ), .row18(\字库_1_out_21 ), .row19(\字库_1_out_22 ), .row20(\字库_1_out_23 ),
    .row21(\字库_1_out_24 ), .row22(\字库_1_out_25 ), .row23(\字库_1_out_26 ), .row24(\字库_1_out_27 ),
    .row25(\字库_1_out_28 ), .row26(\字库_1_out_29 ), .row27(\字库_1_out_30 ), .row28(\字库_1_out_31 ),
    .row29(\字库_1_out_32 ), .row30(\字库_1_out_33 ), .row31(\字库_1_out_34 ));

  // Notes on the sheet:
  //   计数器
  //   GB2312
  //   请在上面的ROM存储器中存100个成句的汉字
  //   实现国标转区位码电路，使得系统每个时钟正确显示一个汉字
  //   contents of rom_1 (hex, n*v repeats v):
  //   a3b0 a3b2 a3b3 a3b4 a3b5 a3c1 a3c2 a3c3 a3c4 a3c5 a3c6 a3c7 a3e1 a3e2 a3e3 a3e4 a3e5 a3e6 a3e7 c7e1
  //   c7e1 b5c4 ced2 d7df c1cb a3ac d5fd c8e7 ced2 c7e1 c7e1 b5c4 c0b4 a3bb ced2 c7e1 c7e1 b5c4 d5d0 cad6
  //   a3ac d7f7 b1f0 cef7 ccec b5c4 d4c6 b2ca a1a3 c4c7 bad3 c5cf b5c4 bdf0 c1f8 a3ac cac7 cfa6 d1f4 d6d0
  //   b5c4 d0c2 c4ef a3bb b2a8 b9e2 c0ef b5c4 d1de d3b0 a3ac d4da ced2 b5c4 d0c4 cdb7 b5b4 d1fa a1a3
endmodule

// 偶校验编码
module \偶校验编码  (
  input  [15:0] \原始数据 ,
  output [16:0] \偶校验编码 
);

  wire xor_1_out, xor_2_out, xor_3_out, xor_4_out, xor_5_out, xor_6_out, xor_7_out, xor_8_out, xor_9_out,
       xor_10_out, xor_11_out, xor_12_out, xor_13_out, xor_14_out;

  xor xor_1 (xor_1_out, \原始数据 [0], \原始数据 [1]);
  xor xor_2 (xor_2_out, \原始数据 [2], \原始数据 [3]);
  xor xor_3 (xor_3_out, \原始数据 [4], \原始数据 [5]);
  xor xor_4 (xor_4_out, \原始数据 [6], \原始数据 [7]);
  xor xor_5 (xor_5_out, \原始数据 [8], \原始数据 [9]);
  xor xor_6 (xor_6_out, \原始数据 [10], \原始数据 [11]);
  xor xor_7 (xor_7_out, \原始数据 [12], \原始数据 [13]);
  xor xor_8 (xor_8_out, \原始数据 [14], \原始数据 [15]);
  xor xor_9 (xor_9_out, xor_1_out, xor_2_out);
  xor xor_10 (xor_10_out, xor_3_out, xor_4_out);
  xor xor_11 (xor_11_out, xor_5_out, xor_6_out);
  xor xor_12 (xor_12_out, xor_7_out, xor_8_out);
  xor xor_13 (xor_13_out, xor_9_out, xor_10_out);
  xor xor_14 (xor_14_out, xor_11_out, xor_12_out);
  xor xor_15 (\偶校验编码 [16], xor_13_out, xor_14_out);

  assign \偶校验编码 [15:0] = \原始数据 ;

  // Other names for the same wires on the sheet: D1 = \原始数据 [0]; Data[15:0] = \原始数据 ;
  //   校验码[16:0] = {\偶校验编码 [16], \原始数据 }; D2 = \原始数据 [1]; D3 = \原始数据 [2]; D4 = \原始数据 [3]; D5 = \原始数据 [4];
  //   D6 = \原始数据 [5]; D7 = \原始数据 [6]; D8 = \原始数据 [7]; D9 = \原始数据 [8]; D10 = \原始数据 [9]; D11 = \原始数据 [10];
  //   D12 = \原始数据 [11]; D13 = \原始数据 [12]; D14 = \原始数据 [13]; D15 = \原始数据 [14]; D16 = \原始数据 [15]

  // Notes on the sheet:
  //   输入引脚区
  //   请勿增改引脚，请勿修改子电路封装
  //   电路功能：实现16位数据位的偶校验编码，输入：16位数据；输出：17位校验码（数据位+校验位）
  //   请在下方利用上方输入输出引脚的隧道信号构建电路，ctrl+d复制选择部件
  //   输出引脚区
endmodule

// 偶校验检错
module \偶校验检错  (
  input  [16:0] \偶校验编码 ,
  output \检错位 ,
  output [15:0] \数据位 
);

  wire xor_1_out, xor_2_out, xor_3_out, xor_4_out, xor_5_out, xor_6_out, xor_7_out, xor_8_out, xor_9_out,
       xor_10_out, xor_11_out, xor_12_out, xor_13_out, xor_14_out, xor_15_out;

  xor xor_1 (xor_1_out, \偶校验编码 [0], \偶校验编码 [1]);
  xor xor_2 (xor_2_out, \偶校验编码 [2], \偶校验编码 [3]);
  xor xor_3 (xor_3_out, \偶校验编码 [4], \偶校验编码 [5]);
  xor xor_4 (xor_4_out, \偶校验编码 [6], \偶校验编码 [7]);
  xor xor_5 (xor_5_out, \偶校验编码 [8], \偶校验编码 [9]);
  xor xor_6 (xor_6_out, \偶校验编码 [10], \偶校验编码 [11]);
  xor xor_7 (xor_7_out, \偶校验编码 [12], \偶校验编码 [13]);
  xor xor_8 (xor_8_out, \偶校验编码 [14], \偶校验编码 [15]);
  xor xor_9 (xor_9_out, xor_1_out, xor_2_out);
  xor xor_10 (xor_10_out, xor_3_out, xor_4_out);
  xor xor_11 (xor_11_out, xor_5_out, xor_6_out);
  xor xor_12 (xor_12_out, xor_7_out, xor_8_out);
  xor xor_13 (xor_13_out, xor_9_out, xor_10_out);
  xor xor_14 (xor_14_out, xor_11_out, xor_12_out);
  xor xor_15 (xor_15_out, xor_13_out, xor_14_out);
  xor xor_16 (\检错位 , xor_15_out, \偶校验编码 [16]);

  assign \数据位  = \偶校验编码 [15:0];

  // Other names for the same wires on the sheet: D1 = \偶校验编码 [0]; 偶校验码[16:0] = \偶校验编码 ; D2 = \偶校验编码 [1];
  //   D3 = \偶校验编码 [2]; D4 = \偶校验编码 [3]; D5 = \偶校验编码 [4]; D6 = \偶校验编码 [5]; D7 = \偶校验编码 [6]; D8 = \偶校验编码 [7];
  //   D9 = \偶校验编码 [8]; D10 = \偶校验编码 [9]; D11 = \偶校验编码 [10]; D12 = \偶校验编码 [11]; D13 = \偶校验编码 [12]; D14 = \偶校验编码 [13];
  //   D15 = \偶校验编码 [14]; D16 = \偶校验编码 [15]; P1 = \偶校验编码 [16]

  // Notes on the sheet:
  //   输入引脚区
  //   请勿增改引脚，请勿修改子电路封装
  //   电路功能：实现17位偶校验编码的检错以及数据提取。输入：17位校验码；输出：检错位、数据位
  //   请在下方利用上方输入输出引脚的隧道信号构建电路，ctrl+d复制选择部件
  //   输出引脚区
endmodule

// 海明编码
module \海明编码  (
  input  [15:0] \原始数据 ,
  output [21:0] \海明码 
);

  // Probe on \原始数据 
  xor xor_1 (\海明码 [21], \原始数据 [15], \原始数据 [14], \原始数据 [12], \原始数据 [11], \原始数据 [9], \原始数据 [7], \原始数据 [5], \原始数据 [4], \原始数据 [2], \原始数据 [0]);
  xor xor_2 (\海明码 [20], \原始数据 [15], \原始数据 [13], \原始数据 [12], \原始数据 [10], \原始数据 [9], \原始数据 [6], \原始数据 [5], \原始数据 [3], \原始数据 [2]);
  xor xor_3 (\海明码 [18], \原始数据 [14], \原始数据 [13], \原始数据 [12], \原始数据 [8], \原始数据 [7], \原始数据 [6], \原始数据 [5], \原始数据 [1], \原始数据 [0]);
  xor xor_4 (\海明码 [14], \原始数据 [11], \原始数据 [10], \原始数据 [9], \原始数据 [8], \原始数据 [7], \原始数据 [6], \原始数据 [5]);
  xor xor_5 (\海明码 [6], \原始数据 [4], \原始数据 [3], \原始数据 [2], \原始数据 [1], \原始数据 [0]);
  xor xor_6 (\海明码 [0], \海明码 [21], \海明码 [20], \海明码 [18], \海明码 [14], \海明码 [6], \原始数据 [15], \原始数据 [14], \原始数据 [13], \原始数据 [12], \原始数据 [11], \原始数据 [10], \原始数据 [9], \原始数据 [8], \原始数据 [7], \原始数据 [6], \原始数据 [5], \原始数据 [4], \原始数据 [3], \原始数据 [2], \原始数据 [1], \原始数据 [0]);
  // Probe on {\海明码 [21:20], \原始数据 [15], \海明码 [18], \原始数据 [14:12], \海明码 [14], \原始数据 [11:5], \海明码 [6], \原始数据 [4:0], \海明码 [0]}
  // Probe on {\海明码 [0], \原始数据 [0], \原始数据 [1], \原始数据 [2], \原始数据 [3], \原始数据 [4], \海明码 [6], \原始数据 [5], \原始数据 [6], \原始数据 [7], \原始数据 [8], \原始数据 [9], \原始数据 [10], \原始数据 [11], \海明码 [14], \原始数据 [12], \原始数据 [13], \原始数据 [14], \海明码 [18], \原始数据 [15], \海明码 [20], \海明码 [21]}

  assign {\海明码 [19], \海明码 [17:15], \海明码 [13:7], \海明码 [5:1]} = \原始数据 ;

  // Other names for the same wires on the sheet: P1 = \海明码 [21]; P2 = \海明码 [20]; D1 = \原始数据 [15]; Data[15:0] = \原始数据 ;
  //   P3 = \海明码 [18]; D2 = \原始数据 [14]; D3 = \原始数据 [13]; D4 = \原始数据 [12]; P4 = \海明码 [14]; D5 = \原始数据 [11];
  //   D6 = \原始数据 [10]; D7 = \原始数据 [9]; D8 = \原始数据 [8]; D9 = \原始数据 [7]; D10 = \原始数据 [6]; D11 = \原始数据 [5];
  //   P5 = \海明码 [6]; D12 = \原始数据 [4]; D13 = \原始数据 [3]; D14 = \原始数据 [2]; D15 = \原始数据 [1]; D16 = \原始数据 [0];
  //   P6 = \海明码 [0]

  // Notes on the sheet:
  //   输入引脚区
  //   请勿增改引脚，请勿修改子电路封装
  //   电路功能：海明编码电路，可检两位错同时纠一位错，输入：16位数据；输出：22位海明码（数据位+校验位）
  //   请在下方利用上方输入输出引脚的隧道信号构建电路，ctrl+d复制选择部件
  //   输出引脚区
endmodule

// 海明解码
module \海明解码  (
  input  [21:0] \海明码 ,
  output \无错误 ,
  output \_1位错 ,
  output \_2位错 ,
  output [15:0] \纠错后数据 
);

  wire and_3_out, and_4_out, decoder_1_out0, G1, G2, G3, G4, G5, G6;
  wire [21:0] decoder_1_out22, xor_6_out;

  xor xor_1 (G1, \海明码 [21], \海明码 [1], \海明码 [19], \海明码 [3], \海明码 [17], \海明码 [5], \海明码 [15], \海明码 [7], \海明码 [13], \海明码 [9], \海明码 [11]);
  xor xor_2 (G2, \海明码 [20], \海明码 [3], \海明码 [19], \海明码 [4], \海明码 [16], \海明码 [15], \海明码 [7], \海明码 [12], \海明码 [8], \海明码 [11]);
  xor xor_3 (G3, \海明码 [18], \海明码 [1], \海明码 [17], \海明码 [2], \海明码 [16], \海明码 [15], \海明码 [7], \海明码 [10], \海明码 [8], \海明码 [9]);
  xor xor_4 (G4, \海明码 [14], \海明码 [7], \海明码 [13], \海明码 [8], \海明码 [9], \海明码 [12], \海明码 [10], \海明码 [11]);
  xor xor_5 (G5, \海明码 [6], \海明码 [1], \海明码 [5], \海明码 [4], \海明码 [2], \海明码 [3]);
  xnor xnor_1 (G6, \海明码 [21], \海明码 [0], \海明码 [20], \海明码 [1], \海明码 [19], \海明码 [2], \海明码 [18], \海明码 [3], \海明码 [17], \海明码 [4], \海明码 [16], \海明码 [15], \海明码 [5], \海明码 [14], \海明码 [6], \海明码 [13], \海明码 [7], \海明码 [12], \海明码 [8], \海明码 [11], \海明码 [9], \海明码 [10]);
  Decoder #(.select(5), .tristate("false"), .disabled("Z"), .enable("false")) decoder_1 (
    .out0(decoder_1_out0), .out1(decoder_1_out22[21]), .out2(decoder_1_out22[20]),
    .out3(decoder_1_out22[19]), .out4(decoder_1_out22[18]), .out5(decoder_1_out22[17]),
    .out6(decoder_1_out22[16]), .out7(decoder_1_out22[15]), .out8(decoder_1_out22[14]),
    .out9(decoder_1_out22[13]), .out10(decoder_1_out22[12]), .out11(decoder_1_out22[11]),
    .out12(decoder_1_out22[10]), .out13(decoder_1_out22[9]), .out14(decoder_1_out22[8]),
    .out15(decoder_1_out22[7]), .out16(decoder_1_out22[6]), .out17(decoder_1_out22[5]),
    .out18(decoder_1_out22[4]), .out19(decoder_1_out22[3]), .out20(decoder_1_out22[2]),
    .out21(decoder_1_out22[1]), .out22(decoder_1_out22[0]), .sel({G5, G4, G3, G2, G1}));  // open: out23, out24, out25, out26, out27, out28, out29, out30, out31
  and and_1 (\_2位错 , ~decoder_1_out0, G6);  // AND_Gate
  and and_2 (\无错误 , decoder_1_out0, G6);
  and and_3 (and_3_out, ~decoder_1_out0, ~G6);  // AND_Gate
  or or_1 (\_1位错 , and_3_out, and_4_out);
  and and_4 (and_4_out, decoder_1_out0, ~G6);  // AND_Gate
  // Probe on {xor_6_out[21:20], \纠错后数据 [15], xor_6_out[18], \纠错后数据 [14:12], xor_6_out[14], \纠错后数据 [11:5], xor_6_out[6], \纠错后数据 [4:0], xor_6_out[0]}
  assign {xor_6_out[21:20], \纠错后数据 [15], xor_6_out[18], \纠错后数据 [14:12], xor_6_out[14], \纠错后数据 [11:5], xor_6_out[6], \纠错后数据 [4:0], xor_6_out[0]} = decoder_1_out22 ^ \海明码 ;  // XOR_Gate xor_6, 22 bits wide

  // Other names for the same wires on the sheet: P6 = \海明码 [0]; D16 = \海明码 [1]; D15 = \海明码 [2]; D14 = \海明码 [3];
  //   D13 = \海明码 [4]; D12 = \海明码 [5]; P5 = \海明码 [6]; D11 = \海明码 [7]; D10 = \海明码 [8]; D9 = \海明码 [9]; D8 = \海明码 [10];
  //   D7 = \海明码 [11]; D6 = \海明码 [12]; D5 = \海明码 [13]; P4 = \海明码 [14]; D4 = \海明码 [15]; D3 = \海明码 [16]; D2 = \海明码 [17];
  //   P3 = \海明码 [18]; D1 = \海明码 [19]; P2 = \海明码 [20]; P1 = \海明码 [21]

  // Notes on the sheet:
  //   输入引脚区
  //   输出引脚区
  //   请勿增改引脚，请勿修改子电路封装
  //   输入：22位海明码；输出：纠错后的数据、错误模式
  //   请在下方利用上方输入输出引脚的隧道信号构建电路，ctrl+d复制选择部件
  //   电路功能：实现22位海明码的数据解码，能判断1位错，2位错，无错误，1位错自动纠错。
endmodule

// CRC编码
module \CRC编码  (
  input  [15:0] \原始数据 ,
  output [21:0] \CRC校验码 
);

  wire [4:0] multiplexer_1_out, multiplexer_2_out, multiplexer_3_out, multiplexer_4_out, multiplexer_5_out,
       multiplexer_6_out, multiplexer_7_out, multiplexer_8_out, multiplexer_9_out, multiplexer_10_out,
       multiplexer_11_out, multiplexer_12_out, multiplexer_13_out, multiplexer_14_out, multiplexer_15_out,
       multiplexer_16_out;

  Multiplexer #(.select(1), .width(5), .disabled("Z"), .enable("false")) multiplexer_1 (
    .in0({5{1'b0}}), .in1(5'b01100), .out(multiplexer_1_out), .sel(\原始数据 [15]));
  Multiplexer #(.select(1), .width(5), .disabled("Z"), .enable("false")) multiplexer_2 (
    .in0({5{1'b0}}), .in1(5'b00110), .out(multiplexer_2_out), .sel(\原始数据 [14]));
  Multiplexer #(.select(1), .width(5), .disabled("Z"), .enable("false")) multiplexer_3 (
    .in0({5{1'b0}}), .in1(5'b00011), .out(multiplexer_3_out), .sel(\原始数据 [13]));
  Multiplexer #(.select(1), .width(5), .disabled("Z"), .enable("false")) multiplexer_4 (
    .in0({5{1'b0}}), .in1(5'b10011), .out(multiplexer_4_out), .sel(\原始数据 [12]));
  Multiplexer #(.select(1), .width(5), .disabled("Z"), .enable("false")) multiplexer_5 (
    .in0({5{1'b0}}), .in1(5'b11101), .out(multiplexer_5_out), .sel(\原始数据 [9]));
  Multiplexer #(.select(1), .width(5), .disabled("Z"), .enable("false")) multiplexer_6 (
    .in0({5{1'b0}}), .in1(5'b11011), .out(multiplexer_6_out), .sel(\原始数据 [11]));
  Multiplexer #(.select(1), .width(5), .disabled("Z"), .enable("false")) multiplexer_7 (
    .in0({5{1'b0}}), .in1({5{1'b1}}), .out(multiplexer_7_out), .sel(\原始数据 [10]));
  Multiplexer #(.select(1), .width(5), .disabled("Z"), .enable("false")) multiplexer_8 (
    .in0({5{1'b0}}), .in1(5'b11100), .out(multiplexer_8_out), .sel(\原始数据 [8]));
  Multiplexer #(.select(1), .width(5), .disabled("Z"), .enable("false")) multiplexer_9 (
    .in0({5{1'b0}}), .in1(5'b01110), .out(multiplexer_9_out), .sel(\原始数据 [7]));
  Multiplexer #(.select(1), .width(5), .disabled("Z"), .enable("false")) multiplexer_10 (
    .in0({5{1'b0}}), .in1(5'b00111), .out(multiplexer_10_out), .sel(\原始数据 [6]));
  Multiplexer #(.select(1), .width(5), .disabled("Z"), .enable("false")) multiplexer_11 (
    .in0({5{1'b0}}), .in1(5'b10001), .out(multiplexer_11_out), .sel(\原始数据 [5]));
  Multiplexer #(.select(1), .width(5), .disabled("Z"), .enable("false")) multiplexer_12 (
    .in0({5{1'b0}}), .in1(5'b11010), .out(multiplexer_12_out), .sel(\原始数据 [4]));
  Multiplexer #(.select(1), .width(5), .disabled("Z"), .enable("false")) multiplexer_13 (
    .in0({5{1'b0}}), .in1(5'b01101), .out(multiplexer_13_out), .sel(\原始数据 [3]));
  Multiplexer #(.select(1), .width(5), .disabled("Z"), .enable("false")) multiplexer_14 (
    .in0({5{1'b0}}), .in1(5'b01010), .out(multiplexer_14_out), .sel(\原始数据 [1]));
  Multiplexer #(.select(1), .width(5), .disabled("Z"), .enable("false")) multiplexer_15 (
    .in0({5{1'b0}}), .in1(5'b00101), .out(multiplexer_15_out), .sel(\原始数据 [0]));
  Multiplexer #(.select(1), .width(5), .disabled("Z"), .enable("false")) multiplexer_16 (
    .in0({5{1'b0}}), .in1(5'b10100), .out(multiplexer_16_out), .sel(\原始数据 [2]));
  assign \CRC校验码 [4:0] = multiplexer_14_out ^ multiplexer_13_out ^ multiplexer_11_out ^ multiplexer_9_out ^ multiplexer_5_out ^ multiplexer_6_out ^ multiplexer_3_out ^ multiplexer_1_out ^ multiplexer_2_out ^ multiplexer_4_out ^ multiplexer_7_out ^ multiplexer_8_out ^ multiplexer_10_out ^ multiplexer_12_out ^ multiplexer_16_out ^ multiplexer_15_out;  // XOR_Gate xor_1, 5 bits wide
  // Probe on 5'b00101
  xor xor_2 (\CRC校验码 [21], \原始数据 [0], \原始数据 [1], \原始数据 [2], \原始数据 [3], \原始数据 [4], \原始数据 [5], \原始数据 [6], \原始数据 [7], \原始数据 [8], \原始数据 [9], \原始数据 [10], \原始数据 [11], \原始数据 [12], \原始数据 [13], \原始数据 [14], \原始数据 [15], \CRC校验码 [0], \CRC校验码 [1], \CRC校验码 [2], \CRC校验码 [3], \CRC校验码 [4]);

  assign \CRC校验码 [20:5] = \原始数据 ;

  // Other names for the same wires on the sheet: CRC编码[21:0] = {\CRC校验码 [21], \原始数据 , \CRC校验码 [4:0]};
  //   P1 = \CRC校验码 [0]; P2 = \CRC校验码 [1]; P3 = \CRC校验码 [2]; P4 = \CRC校验码 [3]; P5 = \CRC校验码 [4]; D1 = \原始数据 [0];
  //   Data[15:0] = \原始数据 ; D2 = \原始数据 [1]; D3 = \原始数据 [2]; D4 = \原始数据 [3]; D5 = \原始数据 [4]; D6 = \原始数据 [5];
  //   D7 = \原始数据 [6]; D8 = \原始数据 [7]; D9 = \原始数据 [8]; D10 = \原始数据 [9]; D11 = \原始数据 [10]; D12 = \原始数据 [11];
  //   D13 = \原始数据 [12]; D14 = \原始数据 [13]; P6 = \CRC校验码 [21]; D15 = \原始数据 [14]; D16 = \原始数据 [15]

  // Notes on the sheet:
  //   输入引脚区
  //   数据位
  //   请勿增改引脚，请勿修改子电路封装
  //   电路功能：CRC编码电路，可检两位错同时纠一位错，输入：16位数据；输出：22位CRC编码（数据位+校验位）
  //   请在下方利用上方输入输出引脚的隧道信号构建电路，ctrl+d复制选择部件
  //   输出引脚区
  //   CRC校验和
  //   总偶校验
endmodule

// CRC解码
module \CRC解码  (
  input  [21:0] \CRC编码 ,
  output \无错误 ,
  output \_1位错 ,
  output \_2位错 ,
  output [15:0] \纠错后数据 
);

  wire and_1_out, and_2_out, nor_1_out, nor_2_out, nor_3_out, nor_4_out, nor_5_out, nor_6_out, nor_7_out,
       nor_8_out, nor_9_out, nor_10_out, nor_11_out, nor_12_out, nor_13_out, nor_14_out, nor_15_out,
       nor_16_out, or_1_out, \总校验位错 ;
  wire [4:0] multiplexer_1_out, multiplexer_2_out, multiplexer_3_out, multiplexer_4_out, multiplexer_5_out,
       multiplexer_6_out, multiplexer_7_out, multiplexer_8_out, multiplexer_9_out, multiplexer_10_out,
       multiplexer_11_out, multiplexer_12_out, multiplexer_13_out, multiplexer_14_out, multiplexer_15_out,
       multiplexer_16_out, xor_1_out, xor_3_out, xor_6_out, xor_7_out, xor_9_out, xor_10_out, xor_13_out,
       xor_15_out, xor_16_out, xor_19_out, xor_20_out, xor_23_out, xor_24_out, xor_25_out, xor_28_out,
       xor_29_out, xor_32_out, xor_34_out;

  Multiplexer #(.select(1), .width(5), .disabled("Z"), .enable("false")) multiplexer_1 (
    .in0({5{1'b0}}), .in1(5'b01100), .out(multiplexer_1_out), .sel(\CRC编码 [20]));
  Multiplexer #(.select(1), .width(5), .disabled("Z"), .enable("false")) multiplexer_2 (
    .in0({5{1'b0}}), .in1(5'b00110), .out(multiplexer_2_out), .sel(\CRC编码 [19]));
  assign xor_1_out = xor_23_out ^ 5'b01100;  // XOR_Gate xor_1, 5 bits wide
  nor nor_1 (nor_1_out, xor_1_out[4], xor_1_out[3], xor_1_out[2], xor_1_out[1], xor_1_out[0]);
  xor xor_2 (\纠错后数据 [15], \CRC编码 [20], nor_1_out);
  Multiplexer #(.select(1), .width(5), .disabled("Z"), .enable("false")) multiplexer_3 (
    .in0({5{1'b0}}), .in1(5'b00011), .out(multiplexer_3_out), .sel(\CRC编码 [18]));
  Multiplexer #(.select(1), .width(5), .disabled("Z"), .enable("false")) multiplexer_4 (
    .in0({5{1'b0}}), .in1(5'b10011), .out(multiplexer_4_out), .sel(\CRC编码 [17]));
  assign xor_3_out = xor_23_out ^ 5'b00110;  // XOR_Gate xor_3, 5 bits wide
  nor nor_2 (nor_2_out, xor_3_out[4], xor_3_out[3], xor_3_out[2], xor_3_out[1], xor_3_out[0]);
  xor xor_4 (\纠错后数据 [13], \CRC编码 [18], nor_4_out);
  xor xor_5 (\纠错后数据 [14], \CRC编码 [19], nor_2_out);
  Multiplexer #(.select(1), .width(5), .disabled("Z"), .enable("false")) multiplexer_5 (
    .in0({5{1'b0}}), .in1(5'b11011), .out(multiplexer_5_out), .sel(\CRC编码 [16]));
  Multiplexer #(.select(1), .width(5), .disabled("Z"), .enable("false")) multiplexer_6 (
    .in0({5{1'b0}}), .in1({5{1'b1}}), .out(multiplexer_6_out), .sel(\CRC编码 [15]));
  assign xor_6_out = xor_23_out ^ 5'b00011;  // XOR_Gate xor_6, 5 bits wide
  assign xor_7_out = xor_23_out ^ 5'b10011;  // XOR_Gate xor_7, 5 bits wide
  nor nor_3 (nor_3_out, xor_7_out[4], xor_7_out[3], xor_7_out[2], xor_7_out[1], xor_7_out[0]);
  nor nor_4 (nor_4_out, xor_6_out[4], xor_6_out[3], xor_6_out[2], xor_6_out[1], xor_6_out[0]);
  xor xor_8 (\纠错后数据 [12], \CRC编码 [17], nor_3_out);
  Multiplexer #(.select(1), .width(5), .disabled("Z"), .enable("false")) multiplexer_7 (
    .in0({5{1'b0}}), .in1(5'b01110), .out(multiplexer_7_out), .sel(\CRC编码 [12]));
  Multiplexer #(.select(1), .width(5), .disabled("Z"), .enable("false")) multiplexer_8 (
    .in0({5{1'b0}}), .in1(5'b11101), .out(multiplexer_8_out), .sel(\CRC编码 [14]));
  Multiplexer #(.select(1), .width(5), .disabled("Z"), .enable("false")) multiplexer_9 (
    .in0({5{1'b0}}), .in1(5'b00111), .out(multiplexer_9_out), .sel(\CRC编码 [11]));
  Multiplexer #(.select(1), .width(5), .disabled("Z"), .enable("false")) multiplexer_10 (
    .in0({5{1'b0}}), .in1(5'b11100), .out(multiplexer_10_out), .sel(\CRC编码 [13]));
  assign xor_9_out = xor_23_out ^ 5'b11011;  // XOR_Gate xor_9, 5 bits wide
  assign xor_10_out = xor_23_out ^ {5{1'b1}};  // XOR_Gate xor_10, 5 bits wide
  nor nor_5 (nor_5_out, xor_9_out[4], xor_9_out[3], xor_9_out[2], xor_9_out[1], xor_9_out[0]);
  nor nor_6 (nor_6_out, xor_10_out[4], xor_10_out[3], xor_10_out[2], xor_10_out[1], xor_10_out[0]);
  xor xor_11 (\纠错后数据 [10], \CRC编码 [15], nor_6_out);
  xor xor_12 (\纠错后数据 [11], \CRC编码 [16], nor_5_out);
  Multiplexer #(.select(1), .width(5), .disabled("Z"), .enable("false")) multiplexer_11 (
    .in0({5{1'b0}}), .in1(5'b10001), .out(multiplexer_11_out), .sel(\CRC编码 [10]));
  Multiplexer #(.select(1), .width(5), .disabled("Z"), .enable("false")) multiplexer_12 (
    .in0({5{1'b0}}), .in1(5'b11010), .out(multiplexer_12_out), .sel(\CRC编码 [9]));
  assign xor_13_out = xor_23_out ^ 5'b11101;  // XOR_Gate xor_13, 5 bits wide
  nor nor_7 (nor_7_out, xor_13_out[4], xor_13_out[3], xor_13_out[2], xor_13_out[1], xor_13_out[0]);
  xor xor_14 (\纠错后数据 [9], \CRC编码 [14], nor_7_out);
  Multiplexer #(.select(1), .width(5), .disabled("Z"), .enable("false")) multiplexer_13 (
    .in0({5{1'b0}}), .in1(5'b01101), .out(multiplexer_13_out), .sel(\CRC编码 [8]));
  Multiplexer #(.select(1), .width(5), .disabled("Z"), .enable("false")) multiplexer_14 (
    .in0({5{1'b0}}), .in1(5'b10100), .out(multiplexer_14_out), .sel(\CRC编码 [7]));
  assign xor_15_out = xor_23_out ^ 5'b11100;  // XOR_Gate xor_15, 5 bits wide
  assign xor_16_out = xor_23_out ^ 5'b01110;  // XOR_Gate xor_16, 5 bits wide
  nor nor_8 (nor_8_out, xor_15_out[4], xor_15_out[3], xor_15_out[2], xor_15_out[1], xor_15_out[0]);
  nor nor_9 (nor_9_out, xor_16_out[4], xor_16_out[3], xor_16_out[2], xor_16_out[1], xor_16_out[0]);
  xor xor_17 (\纠错后数据 [7], \CRC编码 [12], nor_9_out);
  xor xor_18 (\纠错后数据 [8], \CRC编码 [13], nor_8_out);
  // Probe on 5'b01010
  Multiplexer #(.select(1), .width(5), .disabled("Z"), .enable("false")) multiplexer_15 (
    .in0({5{1'b0}}), .in1(5'b01010), .out(multiplexer_15_out), .sel(\CRC编码 [6]));
  assign xor_19_out = multiplexer_15_out ^ multiplexer_13_out ^ multiplexer_11_out ^ multiplexer_7_out ^ multiplexer_8_out ^ multiplexer_5_out ^ multiplexer_3_out ^ multiplexer_1_out ^ multiplexer_2_out ^ multiplexer_4_out ^ multiplexer_6_out ^ multiplexer_10_out ^ multiplexer_9_out ^ multiplexer_12_out ^ multiplexer_14_out ^ multiplexer_16_out;  // XOR_Gate xor_19, 5 bits wide
  // Probe on \CRC编码 [4:0]
  Multiplexer #(.select(1), .width(5), .disabled("Z"), .enable("false")) multiplexer_16 (
    .in0({5{1'b0}}), .in1(5'b00101), .out(multiplexer_16_out), .sel(\CRC编码 [5]));
  assign xor_20_out = xor_23_out ^ 5'b00111;  // XOR_Gate xor_20, 5 bits wide
  nor nor_10 (nor_10_out, xor_20_out[4], xor_20_out[3], xor_20_out[2], xor_20_out[1], xor_20_out[0]);
  xor xor_21 (\纠错后数据 [6], \CRC编码 [11], nor_10_out);
  xor xor_22 (\纠错后数据 [5], \CRC编码 [10], nor_11_out);
  // Probe on xor_19_out
  assign xor_23_out = xor_19_out ^ \CRC编码 [4:0];  // XOR_Gate xor_23, 5 bits wide
  // Probe on xor_23_out
  assign xor_24_out = xor_23_out ^ 5'b10001;  // XOR_Gate xor_24, 5 bits wide
  assign xor_25_out = xor_23_out ^ 5'b11010;  // XOR_Gate xor_25, 5 bits wide
  nor nor_11 (nor_11_out, xor_24_out[4], xor_24_out[3], xor_24_out[2], xor_24_out[1], xor_24_out[0]);
  nor nor_12 (nor_12_out, xor_25_out[4], xor_25_out[3], xor_25_out[2], xor_25_out[1], xor_25_out[0]);
  xor xor_26 (\纠错后数据 [4], \CRC编码 [9], nor_12_out);
  xor xor_27 (\总校验位错 , \CRC编码 [0], \CRC编码 [1], \CRC编码 [2], \CRC编码 [3], \CRC编码 [4], \CRC编码 [5], \CRC编码 [6], \CRC编码 [7], \CRC编码 [8], \CRC编码 [9], \CRC编码 [10], \CRC编码 [12], \CRC编码 [13], \CRC编码 [14], \CRC编码 [15], \CRC编码 [16], \CRC编码 [17], \CRC编码 [18], \CRC编码 [19], \CRC编码 [20], \CRC编码 [21], \CRC编码 [11]);
  or or_1 (or_1_out, xor_23_out[0], xor_23_out[1], xor_23_out[2], xor_23_out[3], xor_23_out[4]);
  // Probe on 5'b01101
  assign xor_28_out = xor_23_out ^ 5'b01101;  // XOR_Gate xor_28, 5 bits wide
  assign xor_29_out = xor_23_out ^ 5'b10100;  // XOR_Gate xor_29, 5 bits wide
  nor nor_13 (nor_13_out, xor_28_out[4], xor_28_out[3], xor_28_out[2], xor_28_out[1], xor_28_out[0]);
  nor nor_14 (nor_14_out, xor_29_out[4], xor_29_out[3], xor_29_out[2], xor_29_out[1], xor_29_out[0]);
  xor xor_30 (\纠错后数据 [2], \CRC编码 [7], nor_14_out);
  xor xor_31 (\纠错后数据 [3], \CRC编码 [8], nor_13_out);
  and and_1 (and_1_out, \总校验位错 , or_1_out);
  and and_2 (and_2_out, \总校验位错 , ~or_1_out);  // AND_Gate
  assign xor_32_out = xor_23_out ^ 5'b01010;  // XOR_Gate xor_32, 5 bits wide
  nor nor_15 (nor_15_out, xor_32_out[4], xor_32_out[3], xor_32_out[2], xor_32_out[1], xor_32_out[0]);
  xor xor_33 (\纠错后数据 [1], \CRC编码 [6], nor_15_out);
  or or_2 (\_1位错 , and_1_out, and_2_out);
  and and_3 (\无错误 , ~or_1_out, ~\总校验位错 );  // AND_Gate
  and and_4 (\_2位错 , ~\总校验位错 , or_1_out);  // AND_Gate
  assign xor_34_out = xor_23_out ^ 5'b00101;  // XOR_Gate xor_34, 5 bits wide
  nor nor_16 (nor_16_out, xor_34_out[4], xor_34_out[3], xor_34_out[2], xor_34_out[1], xor_34_out[0]);
  xor xor_35 (\纠错后数据 [0], \CRC编码 [5], nor_16_out);

  // Other names for the same wires on the sheet: CRC[21:0] = \CRC编码 ; P1 = \CRC编码 [0]; P2 = \CRC编码 [1];
  //   P3 = \CRC编码 [2]; P4 = \CRC编码 [3]; P5 = \CRC编码 [4]; D1 = \CRC编码 [5]; D2 = \CRC编码 [6]; D3 = \CRC编码 [7];
  //   D4 = \CRC编码 [8]; D5 = \CRC编码 [9]; D6 = \CRC编码 [10]; D7 = \CRC编码 [11]; D8 = \CRC编码 [12]; D9 = \CRC编码 [13];
  //   D10 = \CRC编码 [14]; D11 = \CRC编码 [15]; D12 = \CRC编码 [16]; D13 = \CRC编码 [17]; D14 = \CRC编码 [18];
  //   D15 = \CRC编码 [19]; D16 = \CRC编码 [20]; P6 = \CRC编码 [21]

  // Notes on the sheet:
  //   输入引脚区
  //   输出引脚区
  //   CRC校验和
  //   CRC校验和
  //   数据位
  //   数据位
  //   22位CRC编码
  //   CRC  校验和
  //   请勿增改引脚，请勿修改子电路封装
  //   输入：22位CRC编码；输出：纠错后的数据、错误模式
  //   请在下方利用上方输入输出引脚的隧道信号构建电路，ctrl+d复制选择部件
  //   电路功能：实现22位海CRC编码的数据解码，能判断1位错，2位错，无错误，1位错自动纠错。
endmodule

module \偶校验传输测试  (
);

  wire and_1_out, button_1_out, comparator_1_eq, \偶校验检错_1_检错位 , \时钟_out ;
  wire [6:0] \国标转区位码_1_位号 , \国标转区位码_1_区号 , \国标转区位码_2_位号 , \国标转区位码_2_区号 ;
  wire [7:0] counter_1_q;
  wire [15:0] \发送 , \接收 ;
  wire [16:0] \n17位随机干扰_1_加扰后数据 , \n17位随机干扰_1_随机加扰屏蔽字 , \偶校验编码_1_偶校验编码 ;
  wire [31:0] \字库_1_out_3 , \字库_1_out_4 , \字库_1_out_5 , \字库_1_out_6 , \字库_1_out_7 , \字库_1_out_8 ,
       \字库_1_out_9 , \字库_1_out_10 , \字库_1_out_11 , \字库_1_out_12 , \字库_1_out_13 , \字库_1_out_14 ,
       \字库_1_out_15 , \字库_1_out_16 , \字库_1_out_17 , \字库_1_out_18 , \字库_1_out_19 , \字库_1_out_20 ,
       \字库_1_out_21 , \字库_1_out_22 , \字库_1_out_23 , \字库_1_out_24 , \字库_1_out_25 , \字库_1_out_26 ,
       \字库_1_out_27 , \字库_1_out_28 , \字库_1_out_29 , \字库_1_out_30 , \字库_1_out_31 , \字库_1_out_32 ,
       \字库_1_out_33 , \字库_1_out_34 , \字库_2_out_3 , \字库_2_out_4 , \字库_2_out_5 , \字库_2_out_6 , \字库_2_out_7 ,
       \字库_2_out_8 , \字库_2_out_9 , \字库_2_out_10 , \字库_2_out_11 , \字库_2_out_12 , \字库_2_out_13 , \字库_2_out_14 ,
       \字库_2_out_15 , \字库_2_out_16 , \字库_2_out_17 , \字库_2_out_18 , \字库_2_out_19 , \字库_2_out_20 ,
       \字库_2_out_21 , \字库_2_out_22 , \字库_2_out_23 , \字库_2_out_24 , \字库_2_out_25 , \字库_2_out_26 ,
       \字库_2_out_27 , \字库_2_out_28 , \字库_2_out_29 , \字库_2_out_30 , \字库_2_out_31 , \字库_2_out_32 ,
       \字库_2_out_33 , \字库_2_out_34 ;

  Counter #(.width(8), .max('hff), .ongoal("wrap"), .trigger("rising"), .behavior("old")) counter_1 (
    .Q(counter_1_q), .clk(\时钟_out ), .clr(button_1_out));  // open: load, D, count, carry, preset
  Button button_1 (.out(button_1_out));
  Clock #(.highDuration(1), .lowDuration(1)) \u_时钟  (.out(\时钟_out ));
  \国标转区位码  \u_国标转区位码_1  (.\位号 (\国标转区位码_1_位号 ), .\区号 (\国标转区位码_1_区号 ), .GB2312(\发送 ));
  ROM #(.addrWidth(8), .dataWidth(16), .Select("high")) rom_1 (.addr(counter_1_q), .data(\发送 ));
  DotMatrix #(.inputtype("row"), .matrixcols(32), .matrixrows(32), .persist(0), .dotshape("circle")) dotmatrix_1 (
    .row0(\字库_1_out_3 ), .row1(\字库_1_out_4 ), .row2(\字库_1_out_5 ), .row3(\字库_1_out_6 ), .row4(\字库_1_out_7 ),
    .row5(\字库_1_out_8 ), .row6(\字库_1_out_9 ), .row7(\字库_1_out_10 ), .row8(\字库_1_out_11 ),
    .row9(\字库_1_out_12 ), .row10(\字库_1_out_13 ), .row11(\字库_1_out_14 ), .row12(\字库_1_out_15 ),
    .row13(\字库_1_out_16 ), .row14(\字库_1_out_17 ), .row15(\字库_1_out_18 ), .row16(\字库_1_out_19 ),
    .row17(\字库_1_out_20 ), .row18(\字库_1_out_21 ), .row19(\字库_1_out_22 ), .row20(\字库_1_out_23 ),
    .row21(\字库_1_out_24 ), .row22(\字库_1_out_25 ), .row23(\字库_1_out_26 ), .row24(\字库_1_out_27 ),
    .row25(\字库_1_out_28 ), .row26(\字库_1_out_29 ), .row27(\字库_1_out_30 ), .row28(\字库_1_out_31 ),
    .row29(\字库_1_out_32 ), .row30(\字库_1_out_33 ), .row31(\字库_1_out_34 ));
  \字库  \u_字库_1  (
    .out_3(\字库_1_out_3 ), .out_4(\字库_1_out_4 ), .out_5(\字库_1_out_5 ), .out_6(\字库_1_out_6 ),
    .out_7(\字库_1_out_7 ), .out_8(\字库_1_out_8 ), .out_9(\字库_1_out_9 ), .out_10(\字库_1_out_10 ),
    .out_11(\字库_1_out_11 ), .out_12(\字库_1_out_12 ), .out_13(\字库_1_out_13 ), .out_14(\字库_1_out_14 ),
    .out_15(\字库_1_out_15 ), .out_16(\字库_1_out_16 ), .out_17(\字库_1_out_17 ), .out_18(\字库_1_out_18 ),
    .out_19(\字库_1_out_19 ), .out_20(\字库_1_out_20 ), .out_21(\字库_1_out_21 ), .out_22(\字库_1_out_22 ),
    .out_23(\字库_1_out_23 ), .out_24(\字库_1_out_24 ), .out_25(\字库_1_out_25 ), .out_26(\字库_1_out_26 ),
    .out_27(\字库_1_out_27 ), .out_28(\字库_1_out_28 ), .out_29(\字库_1_out_29 ), .out_30(\字库_1_out_30 ),
    .out_31(\字库_1_out_31 ), .out_32(\字库_1_out_32 ), .out_33(\字库_1_out_33 ), .out_34(\字库_1_out_34 ),
    .\区号 (\国标转区位码_1_区号 ), .\位号 (\国标转区位码_1_位号 ));
  // Probe on \发送 
  \偶校验编码  \u_偶校验编码_1  (.\原始数据 (\发送 ), .\偶校验编码 (\偶校验编码_1_偶校验编码 ));
  // Probe on \偶校验编码_1_偶校验编码 
  // Probe on \偶校验编码_1_偶校验编码 
  // Probe on \n17位随机干扰_1_随机加扰屏蔽字 
  \_17位随机干扰  \u_17位随机干扰_1  (.\_17位输入 (\偶校验编码_1_偶校验编码 ), .\随机加扰屏蔽字 (\n17位随机干扰_1_随机加扰屏蔽字 ), .\加扰后数据 (\n17位随机干扰_1_加扰后数据 ));
  // Probe on \n17位随机干扰_1_加扰后数据 
  // Probe on \n17位随机干扰_1_加扰后数据 
  \国标转区位码  \u_国标转区位码_2  (.\位号 (\国标转区位码_2_位号 ), .\区号 (\国标转区位码_2_区号 ), .GB2312(\接收 ));
  DotMatrix #(.inputtype("row"), .matrixcols(32), .matrixrows(32), .persist(0), .dotshape("circle")) dotmatrix_2 (
    .row0(\字库_2_out_3 ), .row1(\字库_2_out_4 ), .row2(\字库_2_out_5 ), .row3(\字库_2_out_6 ), .row4(\字库_2_out_7 ),
    .row5(\字库_2_out_8 ), .row6(\字库_2_out_9 ), .row7(\字库_2_out_10 ), .row8(\字库_2_out_11 ),
    .row9(\字库_2_out_12 ), .row10(\字库_2_out_13 ), .row11(\字库_2_out_14 ), .row12(\字库_2_out_15 ),
    .row13(\字库_2_out_16 ), .row14(\字库_2_out_17 ), .row15(\字库_2_out_18 ), .row16(\字库_2_out_19 ),
    .row17(\字库_2_out_20 ), .row18(\字库_2_out_21 ), .row19(\字库_2_out_22 ), .row20(\字库_2_out_23 ),
    .row21(\字库_2_out_24 ), .row22(\字库_2_out_25 ), .row23(\字库_2_out_26 ), .row24(\字库_2_out_27 ),
    .row25(\字库_2_out_28 ), .row26(\字库_2_out_29 ), .row27(\字库_2_out_30 ), .row28(\字库_2_out_31 ),
    .row29(\字库_2_out_32 ), .row30(\字库_2_out_33 ), .row31(\字库_2_out_34 ));
  \字库  \u_字库_2  (
    .out_3(\字库_2_out_3 ), .out_4(\字库_2_out_4 ), .out_5(\字库_2_out_5 ), .out_6(\字库_2_out_6 ),
    .out_7(\字库_2_out_7 ), .out_8(\字库_2_out_8 ), .out_9(\字库_2_out_9 ), .out_10(\字库_2_out_10 ),
    .out_11(\字库_2_out_11 ), .out_12(\字库_2_out_12 ), .out_13(\字库_2_out_13 ), .out_14(\字库_2_out_14 ),
    .out_15(\字库_2_out_15 ), .out_16(\字库_2_out_16 ), .out_17(\字库_2_out_17 ), .out_18(\字库_2_out_18 ),
    .out_19(\字库_2_out_19 ), .out_20(\字库_2_out_20 ), .out_21(\字库_2_out_21 ), .out_22(\字库_2_out_22 ),
    .out_23(\字库_2_out_23 ), .out_24(\字库_2_out_24 ), .out_25(\字库_2_out_25 ), .out_26(\字库_2_out_26 ),
    .out_27(\字库_2_out_27 ), .out_28(\字库_2_out_28 ), .out_29(\字库_2_out_29 ), .out_30(\字库_2_out_30 ),
    .out_31(\字库_2_out_31 ), .out_32(\字库_2_out_32 ), .out_33(\字库_2_out_33 ), .out_34(\字库_2_out_34 ),
    .\区号 (\国标转区位码_2_区号 ), .\位号 (\国标转区位码_2_位号 ));
  LED #(.active("true")) \u_检错位  (.in(\偶校验检错_1_检错位 ));
  \偶校验检错  \u_偶校验检错_1  (.\检错位 (\偶校验检错_1_检错位 ), .\偶校验编码 (\n17位随机干扰_1_加扰后数据 ), .\数据位 (\接收 ));
  Comparator #(.width(16), .mode("twosComplement")) comparator_1 (
    .a(\发送 ), .b(\接收 ), .eq(comparator_1_eq));  // open: gt, lt
  // Probe on \接收 
  and and_1 (and_1_out, ~comparator_1_eq, ~\偶校验检错_1_检错位 );  // AND_Gate
  LED #(.active("true")) \u_数据正确  (.in(comparator_1_eq));
  LED #(.active("true")) \u_误报  (.in(and_1_out));

  // Notes on the sheet:
  //   发送方
  //   计数器
  //   发送方
  //   汉字显示
  //   GB2312
  //   contents of rom_1 (hex, n*v repeats v):
  //   bbaa d6d0 bfc6 bcbc b4f3 d1a7 cac7 b9fa bcd2 bdcc d3fd b2bf d6b1 caf4 b5c4 c8ab b9fa d6d8 b5e3 b4f3
  //   d1a7 a3ac d3c9 d4ad bbaa d6d0 c0ed b9a4 b4f3 d1a7 a1a2 cdac bcc3 d2bd bfc6 b4f3 d1a7 a1a2 cee4 baba
  //   b3c7 cad0 bda8 c9e8 d1a7 d4ba d3da a3b2 a3b0 a3b0 a3b0 c4ea a3b5 d4c2 a3b2 a3b6 c8d5 bacf b2a2 b3c9
  //   c1a2 a3ac cac7 cad7 c5fa c1d0 c8eb b9fa bcd2 a1b0 a3b2 a3b1 a3b1 b9a4 b3cc a1b1 d6d8 b5e3 bda8 c9e8
  //   bacd b9fa bcd2 a1b0 a3b9 a3b8 a3b5 b9a4 b3cc a1b1 bda8 c9e8 b8df d0a3 d6ae d2bb a1a3 d1a7 d0a3 d0a3
  //   d4b0 d5bc b5d8 c6df c7a7 d3e0 c4b6 a3ac d4b0 c4da caf7 c4be b4d0 dcd7 a3ac b1cc b2dd c8e7 d2f0 a3ac
  //   bbb7 beb3 d3c5 d1c5 a3ac beb0 c9ab d0e3 c0f6 a3ac c2cc bbaf b8b2 b8c7 c2ca 3732 25a3 acb1 bbd3 fece
  //   aaa1 b0c9 adc1 d6ca bdb4 f3d1 a7a1 b1a1
  //   电路功能：测试偶校验编解码电路正确性，仿真时设置加扰控制位和原始数据，按CTRL+T触发不同的干扰，检验编解码电路功能
  //   发送方在ROM预存了一段中文文字，通过计数器驱动电路每个时钟传输一个汉字到接收方
  //   用户实现了国标转区位码电路后，可在中间窗口观察发送方和接收方汉字显示是否一致以观察检错性能
  //   偶校验编解码传输电路
  //   接收方
  //   汉字显示
  //   Ctrl+T Ctrl+K驱动时钟触发随机干扰变化
  //   接收方
  //   请将时钟频率调到8Hz
endmodule

module \海明传输测试1  (
  input  [15:0] \原始数据 ,
  input  [1:0] \加扰控制 
);

  wire comparator_1_eq, \海明解码_1__1位错 , \海明解码_1__2位错 , \海明解码_1_无错误 ;
  wire [15:0] \海明解码_1_纠错后数据 ;
  wire [21:0] \n22位随机干扰_1_加扰后数据 , \n22位随机干扰_1_随机加扰屏蔽字 , \海明编码_1_海明码 ;

  // Probe on \原始数据 
  // Probe on \海明编码_1_海明码 
  \海明编码  \u_海明编码_1  (.\原始数据 (\原始数据 ), .\海明码 (\海明编码_1_海明码 ));
  // Probe on \海明编码_1_海明码 
  // Probe on \n22位随机干扰_1_随机加扰屏蔽字 
  // Probe on \n22位随机干扰_1_加扰后数据 
  \_22位随机干扰  \u_22位随机干扰_1  (
    .\加扰模式 (\加扰控制 ), .\随机加扰屏蔽字 (\n22位随机干扰_1_随机加扰屏蔽字 ), .\_22位输入 (\海明编码_1_海明码 ), .\加扰后数据 (\n22位随机干扰_1_加扰后数据 ));  // open: 增加三位错
  // Probe on \n22位随机干扰_1_加扰后数据 
  LED #(.active("true")) \u_两位错  (.in(\海明解码_1__2位错 ));
  LED #(.active("true")) \u_一位错  (.in(\海明解码_1__1位错 ));
  LED #(.active("true")) \u_无错误  (.in(\海明解码_1_无错误 ));
  \海明解码  \u_海明解码_1  (
    .\_1位错 (\海明解码_1__1位错 ), .\_2位错 (\海明解码_1__2位错 ), .\无错误 (\海明解码_1_无错误 ), .\海明码 (\n22位随机干扰_1_加扰后数据 ),
    .\纠错后数据 (\海明解码_1_纠错后数据 ));
  // Probe on \海明解码_1_纠错后数据 
  Comparator #(.width(16), .mode("twosComplement")) comparator_1 (
    .a(\原始数据 ), .b(\海明解码_1_纠错后数据 ), .eq(comparator_1_eq));  // open: gt, lt
  LED #(.active("true")) \u_数据正确  (.in(comparator_1_eq));

  // Notes on the sheet:
  //   发送方
  //   电路功能：测试海明编解码电路正确性，仿真时设置加扰控制位和原始数据，按CTRL+T触发不同的干扰，检验编解码电路功能
  //   Ctrl+T 驱动时钟触发随机干扰变化
  //   海明编解码传输电路
  //   加扰控制00：不加扰  01:1位加扰 10:2位加扰 11：随机加扰
  //   接收方
endmodule

module \海明传输测试2  (
  input  [1:0] \加扰控制 
);

  wire button_1_out, comparator_1_eq, \时钟_out , \海明解码_1__1位错 , \海明解码_1__2位错 , \海明解码_1_无错误 ;
  wire [6:0] \国标转区位码_1_位号 , \国标转区位码_1_区号 , \国标转区位码_2_位号 , \国标转区位码_2_区号 ;
  wire [7:0] counter_1_q;
  wire [15:0] \发送 , \接收 ;
  wire [21:0] \n22位随机干扰_1_加扰后数据 , \n22位随机干扰_1_随机加扰屏蔽字 , \海明编码_1_海明码 ;
  wire [31:0] \字库_1_out_3 , \字库_1_out_4 , \字库_1_out_5 , \字库_1_out_6 , \字库_1_out_7 , \字库_1_out_8 ,
       \字库_1_out_9 , \字库_1_out_10 , \字库_1_out_11 , \字库_1_out_12 , \字库_1_out_13 , \字库_1_out_14 ,
       \字库_1_out_15 , \字库_1_out_16 , \字库_1_out_17 , \字库_1_out_18 , \字库_1_out_19 , \字库_1_out_20 ,
       \字库_1_out_21 , \字库_1_out_22 , \字库_1_out_23 , \字库_1_out_24 , \字库_1_out_25 , \字库_1_out_26 ,
       \字库_1_out_27 , \字库_1_out_28 , \字库_1_out_29 , \字库_1_out_30 , \字库_1_out_31 , \字库_1_out_32 ,
       \字库_1_out_33 , \字库_1_out_34 , \字库_2_out_3 , \字库_2_out_4 , \字库_2_out_5 , \字库_2_out_6 , \字库_2_out_7 ,
       \字库_2_out_8 , \字库_2_out_9 , \字库_2_out_10 , \字库_2_out_11 , \字库_2_out_12 , \字库_2_out_13 , \字库_2_out_14 ,
       \字库_2_out_15 , \字库_2_out_16 , \字库_2_out_17 , \字库_2_out_18 , \字库_2_out_19 , \字库_2_out_20 ,
       \字库_2_out_21 , \字库_2_out_22 , \字库_2_out_23 , \字库_2_out_24 , \字库_2_out_25 , \字库_2_out_26 ,
       \字库_2_out_27 , \字库_2_out_28 , \字库_2_out_29 , \字库_2_out_30 , \字库_2_out_31 , \字库_2_out_32 ,
       \字库_2_out_33 , \字库_2_out_34 ;

  Clock #(.highDuration(1), .lowDuration(1)) \u_时钟  (.out(\时钟_out ));
  Counter #(.width(8), .max('hff), .ongoal("wrap"), .trigger("rising"), .behavior("old")) counter_1 (
    .Q(counter_1_q), .clk(\时钟_out ), .clr(button_1_out));  // open: load, D, count, carry, preset
  Button button_1 (.out(button_1_out));
  \国标转区位码  \u_国标转区位码_1  (.\位号 (\国标转区位码_1_位号 ), .\区号 (\国标转区位码_1_区号 ), .GB2312(\发送 ));
  DotMatrix #(.inputtype("row"), .matrixcols(32), .matrixrows(32), .persist(0), .dotshape("circle")) dotmatrix_1 (
    .row0(\字库_1_out_3 ), .row1(\字库_1_out_4 ), .row2(\字库_1_out_5 ), .row3(\字库_1_out_6 ), .row4(\字库_1_out_7 ),
    .row5(\字库_1_out_8 ), .row6(\字库_1_out_9 ), .row7(\字库_1_out_10 ), .row8(\字库_1_out_11 ),
    .row9(\字库_1_out_12 ), .row10(\字库_1_out_13 ), .row11(\字库_1_out_14 ), .row12(\字库_1_out_15 ),
    .row13(\字库_1_out_16 ), .row14(\字库_1_out_17 ), .row15(\字库_1_out_18 ), .row16(\字库_1_out_19 ),
    .row17(\字库_1_out_20 ), .row18(\字库_1_out_21 ), .row19(\字库_1_out_22 ), .row20(\字库_1_out_23 ),
    .row21(\字库_1_out_24 ), .row22(\字库_1_out_25 ), .row23(\字库_1_out_26 ), .row24(\字库_1_out_27 ),
    .row25(\字库_1_out_28 ), .row26(\字库_1_out_29 ), .row27(\字库_1_out_30 ), .row28(\字库_1_out_31 ),
    .row29(\字库_1_out_32 ), .row30(\字库_1_out_33 ), .row31(\字库_1_out_34 ));
  \字库  \u_字库_1  (
    .out_3(\字库_1_out_3 ), .out_4(\字库_1_out_4 ), .out_5(\字库_1_out_5 ), .out_6(\字库_1_out_6 ),
    .out_7(\字库_1_out_7 ), .out_8(\字库_1_out_8 ), .out_9(\字库_1_out_9 ), .out_10(\字库_1_out_10 ),
    .out_11(\字库_1_out_11 ), .out_12(\字库_1_out_12 ), .out_13(\字库_1_out_13 ), .out_14(\字库_1_out_14 ),
    .out_15(\字库_1_out_15 ), .out_16(\字库_1_out_16 ), .out_17(\字库_1_out_17 ), .out_18(\字库_1_out_18 ),
    .out_19(\字库_1_out_19 ), .out_20(\字库_1_out_20 ), .out_21(\字库_1_out_21 ), .out_22(\字库_1_out_22 ),
    .out_23(\字库_1_out_23 ), .out_24(\字库_1_out_24 ), .out_25(\字库_1_out_25 ), .out_26(\字库_1_out_26 ),
    .out_27(\字库_1_out_27 ), .out_28(\字库_1_out_28 ), .out_29(\字库_1_out_29 ), .out_30(\字库_1_out_30 ),
    .out_31(\字库_1_out_31 ), .out_32(\字库_1_out_32 ), .out_33(\字库_1_out_33 ), .out_34(\字库_1_out_34 ),
    .\区号 (\国标转区位码_1_区号 ), .\位号 (\国标转区位码_1_位号 ));
  ROM #(.addrWidth(8), .dataWidth(16), .Select("high")) rom_1 (.addr(counter_1_q), .data(\发送 ));
  // Probe on \发送 
  // Probe on \海明编码_1_海明码 
  \海明编码  \u_海明编码_1  (.\原始数据 (\发送 ), .\海明码 (\海明编码_1_海明码 ));
  // Probe on \海明编码_1_海明码 
  // Probe on \n22位随机干扰_1_随机加扰屏蔽字 
  \_22位随机干扰  \u_22位随机干扰_1  (
    .\加扰模式 (\加扰控制 ), .\随机加扰屏蔽字 (\n22位随机干扰_1_随机加扰屏蔽字 ), .\_22位输入 (\海明编码_1_海明码 ), .\加扰后数据 (\n22位随机干扰_1_加扰后数据 ));  // open: 增加三位错
  // Probe on \n22位随机干扰_1_加扰后数据 
  // Probe on \n22位随机干扰_1_加扰后数据 
  \字库  \u_字库_2  (
    .out_3(\字库_2_out_3 ), .out_4(\字库_2_out_4 ), .out_5(\字库_2_out_5 ), .out_6(\字库_2_out_6 ),
    .out_7(\字库_2_out_7 ), .out_8(\字库_2_out_8 ), .out_9(\字库_2_out_9 ), .out_10(\字库_2_out_10 ),
    .out_11(\字库_2_out_11 ), .out_12(\字库_2_out_12 ), .out_13(\字库_2_out_13 ), .out_14(\字库_2_out_14 ),
    .out_15(\字库_2_out_15 ), .out_16(\字库_2_out_16 ), .out_17(\字库_2_out_17 ), .out_18(\字库_2_out_18 ),
    .out_19(\字库_2_out_19 ), .out_20(\字库_2_out_20 ), .out_21(\字库_2_out_21 ), .out_22(\字库_2_out_22 ),
    .out_23(\字库_2_out_23 ), .out_24(\字库_2_out_24 ), .out_25(\字库_2_out_25 ), .out_26(\字库_2_out_26 ),
    .out_27(\字库_2_out_27 ), .out_28(\字库_2_out_28 ), .out_29(\字库_2_out_29 ), .out_30(\字库_2_out_30 ),
    .out_31(\字库_2_out_31 ), .out_32(\字库_2_out_32 ), .out_33(\字库_2_out_33 ), .out_34(\字库_2_out_34 ),
    .\区号 (\国标转区位码_2_区号 ), .\位号 (\国标转区位码_2_位号 ));
  \国标转区位码  \u_国标转区位码_2  (.\位号 (\国标转区位码_2_位号 ), .\区号 (\国标转区位码_2_区号 ), .GB2312(\接收 ));
  LED #(.active("true")) \u_一位错  (.in(\海明解码_1__1位错 ));
  LED #(.active("true")) \u_无错误  (.in(\海明解码_1_无错误 ));
  LED #(.active("true")) \u_两位错  (.in(\海明解码_1__2位错 ));
  DotMatrix #(.inputtype("row"), .matrixcols(32), .matrixrows(32), .persist(0), .dotshape("circle")) dotmatrix_2 (
    .row0(\字库_2_out_3 ), .row1(\字库_2_out_4 ), .row2(\字库_2_out_5 ), .row3(\字库_2_out_6 ), .row4(\字库_2_out_7 ),
    .row5(\字库_2_out_8 ), .row6(\字库_2_out_9 ), .row7(\字库_2_out_10 ), .row8(\字库_2_out_11 ),
    .row9(\字库_2_out_12 ), .row10(\字库_2_out_13 ), .row11(\字库_2_out_14 ), .row12(\字库_2_out_15 ),
    .row13(\字库_2_out_16 ), .row14(\字库_2_out_17 ), .row15(\字库_2_out_18 ), .row16(\字库_2_out_19 ),
    .row17(\字库_2_out_20 ), .row18(\字库_2_out_21 ), .row19(\字库_2_out_22 ), .row20(\字库_2_out_23 ),
    .row21(\字库_2_out_24 ), .row22(\字库_2_out_25 ), .row23(\字库_2_out_26 ), .row24(\字库_2_out_27 ),
    .row25(\字库_2_out_28 ), .row26(\字库_2_out_29 ), .row27(\字库_2_out_30 ), .row28(\字库_2_out_31 ),
    .row29(\字库_2_out_32 ), .row30(\字库_2_out_33 ), .row31(\字库_2_out_34 ));
  \海明解码  \u_海明解码_1  (
    .\_1位错 (\海明解码_1__1位错 ), .\_2位错 (\海明解码_1__2位错 ), .\无错误 (\海明解码_1_无错误 ), .\海明码 (\n22位随机干扰_1_加扰后数据 ),
    .\纠错后数据 (\接收 ));
  // Probe on \接收 
  Comparator #(.width(16), .mode("twosComplement")) comparator_1 (
    .a(\发送 ), .b(\接收 ), .eq(comparator_1_eq));  // open: gt, lt
  LED #(.active("true")) \u_数据正确  (.in(comparator_1_eq));

  // Notes on the sheet:
  //   发送方
  //   计数器
  //   发送方
  //   汉字显示
  //   GB2312
  //   Ctrl+T 驱动时钟触发随机干扰变化
  //   contents of rom_1 (hex, n*v repeats v):
  //   bbaa d6d0 bfc6 bcbc b4f3 d1a7 cac7 b9fa bcd2 bdcc d3fd b2bf d6b1 caf4 b5c4 c8ab b9fa d6d8 b5e3 b4f3
  //   d1a7 a3ac d3c9 d4ad bbaa d6d0 c0ed b9a4 b4f3 d1a7 a1a2 cdac bcc3 d2bd bfc6 b4f3 d1a7 a1a2 cee4 baba
  //   b3c7 cad0 bda8 c9e8 d1a7 d4ba d3da a3b2 a3b0 a3b0 a3b0 c4ea a3b5 d4c2 a3b2 a3b6 c8d5 bacf b2a2 b3c9
  //   c1a2 a3ac cac7 cad7 c5fa c1d0 c8eb b9fa bcd2 a1b0 a3b2 a3b1 a3b1 b9a4 b3cc a1b1 d6d8 b5e3 bda8 c9e8
  //   bacd b9fa bcd2 a1b0 a3b9 a3b8 a3b5 b9a4 b3cc a1b1 bda8 c9e8 b8df d0a3 d6ae d2bb a1a3 d1a7 d0a3 d0a3
  //   d4b0 d5bc b5d8 c6df c7a7 d3e0 c4b6 a3ac d4b0 c4da caf7 c4be b4d0 dcd7 a3ac b1cc b2dd c8e7 d2f0 a3ac
  //   bbb7 beb3 d3c5 d1c5 a3ac beb0 c9ab d0e3 c0f6 a3ac c2cc bbaf b8b2 b8c7 c2ca 3732 25a3 acb1 bbd3 fece
  //   aaa1 b0c9 adc1 d6ca bdb4 f3d1 a7a1 b1a1
  //   电路功能：测试海明编解码电路正确性，仿真时设置加扰控制位和原始数据，按CTRL+T触发不同的干扰，检验编解码电路功能
  //   发送方在ROM预存了一段中文文字，通过计数器驱动电路每个时钟传输一个汉字到接收方
  //   用户实现了国标转区位码电路后，可在中间窗口观察发送方和接收方汉字显示是否一致以观察海明检错纠错性能
  //   海明编解码传输电路
  //   接收方
  //   汉字显示
  //   Ctrl+T 驱动时钟触发随机干扰变化
  //   加扰控制00：不加扰  01:1位加扰 10:2位加扰 11：随机加扰
  //   加扰控制00：不加扰  01:1位加扰 10:2位加扰 11：随机加扰
  //   接收方
  //   请将时钟频率调到8Hz
endmodule

module \海明编码流水传输  (
  input  \加噪 
);

  wire button_1_out, \n16位流水接口_1_传输状态out_表明当前传输数据有效 , \n22位流水接口_1_传输状态out_表明当前传输数据有效 ,
       \n22位流水接口_2_传输状态out_表明当前传输数据有效 , or_1_out, \stall信号控制_1_out_4 , \时钟_out , \海明解码_1__1位错 ,
       \海明解码_1__2位错 , \海明解码_1_无错误 ;
  wire [6:0] \国标转区位码_1_位号 , \国标转区位码_1_区号 , \国标转区位码_2_位号 , \国标转区位码_2_区号 ;
  wire [7:0] adder_1_out, register_1_q, \地址回滚器_1_输出 ;
  wire [15:0] \n16位流水接口_1_dout16 , \发送 , \接收 , \海明解码_1_纠错后数据 ;
  wire [21:0] \n22位流水接口_1_dout22 , \n22位流水接口_2_dout22 , \n22位随机干扰_1_加扰后数据 , \海明编码_1_海明码 ;
  wire [31:0] \字库_1_out_3 , \字库_1_out_4 , \字库_1_out_5 , \字库_1_out_6 , \字库_1_out_7 , \字库_1_out_8 ,
       \字库_1_out_9 , \字库_1_out_10 , \字库_1_out_11 , \字库_1_out_12 , \字库_1_out_13 , \字库_1_out_14 ,
       \字库_1_out_15 , \字库_1_out_16 , \字库_1_out_17 , \字库_1_out_18 , \字库_1_out_19 , \字库_1_out_20 ,
       \字库_1_out_21 , \字库_1_out_22 , \字库_1_out_23 , \字库_1_out_24 , \字库_1_out_25 , \字库_1_out_26 ,
       \字库_1_out_27 , \字库_1_out_28 , \字库_1_out_29 , \字库_1_out_30 , \字库_1_out_31 , \字库_1_out_32 ,
       \字库_1_out_33 , \字库_1_out_34 , \字库_2_out_3 , \字库_2_out_4 , \字库_2_out_5 , \字库_2_out_6 , \字库_2_out_7 ,
       \字库_2_out_8 , \字库_2_out_9 , \字库_2_out_10 , \字库_2_out_11 , \字库_2_out_12 , \字库_2_out_13 , \字库_2_out_14 ,
       \字库_2_out_15 , \字库_2_out_16 , \字库_2_out_17 , \字库_2_out_18 , \字库_2_out_19 , \字库_2_out_20 ,
       \字库_2_out_21 , \字库_2_out_22 , \字库_2_out_23 , \字库_2_out_24 , \字库_2_out_25 , \字库_2_out_26 ,
       \字库_2_out_27 , \字库_2_out_28 , \字库_2_out_29 , \字库_2_out_30 , \字库_2_out_31 , \字库_2_out_32 ,
       \字库_2_out_33 , \字库_2_out_34 ;

  Clock #(.highDuration(1), .lowDuration(1)) \u_时钟  (.out(\时钟_out ));
  \地址回滚器  \u_地址回滚器_1  (
    .\高电平回滚 (\海明解码_1__2位错 ), .\正常地址 (adder_1_out), .CLK(\时钟_out ), .\清零 (button_1_out), .\输出 (\地址回滚器_1_输出 ));
  Register #(.width(8), .trigger("rising"), .Select("low")) register_1 (
    .D(\地址回滚器_1_输出 ), .Q(register_1_q), .clk(\时钟_out ), .clr(button_1_out));  // open: en
  Button button_1 (.out(button_1_out));
  \国标转区位码  \u_国标转区位码_1  (.\位号 (\国标转区位码_1_位号 ), .\区号 (\国标转区位码_1_区号 ), .GB2312(\发送 ));
  Adder #(.width(8)) adder_1 (.a(8'h1), .b(register_1_q), .out(adder_1_out));  // open: cin, cout
  DotMatrix #(.inputtype("row"), .matrixcols(32), .matrixrows(32), .persist(0), .dotshape("circle")) dotmatrix_1 (
    .row0(\字库_1_out_3 ), .row1(\字库_1_out_4 ), .row2(\字库_1_out_5 ), .row3(\字库_1_out_6 ), .row4(\字库_1_out_7 ),
    .row5(\字库_1_out_8 ), .row6(\字库_1_out_9 ), .row7(\字库_1_out_10 ), .row8(\字库_1_out_11 ),
    .row9(\字库_1_out_12 ), .row10(\字库_1_out_13 ), .row11(\字库_1_out_14 ), .row12(\字库_1_out_15 ),
    .row13(\字库_1_out_16 ), .row14(\字库_1_out_17 ), .row15(\字库_1_out_18 ), .row16(\字库_1_out_19 ),
    .row17(\字库_1_out_20 ), .row18(\字库_1_out_21 ), .row19(\字库_1_out_22 ), .row20(\字库_1_out_23 ),
    .row21(\字库_1_out_24 ), .row22(\字库_1_out_25 ), .row23(\字库_1_out_26 ), .row24(\字库_1_out_27 ),
    .row25(\字库_1_out_28 ), .row26(\字库_1_out_29 ), .row27(\字库_1_out_30 ), .row28(\字库_1_out_31 ),
    .row29(\字库_1_out_32 ), .row30(\字库_1_out_33 ), .row31(\字库_1_out_34 ));
  \字库  \u_字库_1  (
    .out_3(\字库_1_out_3 ), .out_4(\字库_1_out_4 ), .out_5(\字库_1_out_5 ), .out_6(\字库_1_out_6 ),
    .out_7(\字库_1_out_7 ), .out_8(\字库_1_out_8 ), .out_9(\字库_1_out_9 ), .out_10(\字库_1_out_10 ),
    .out_11(\字库_1_out_11 ), .out_12(\字库_1_out_12 ), .out_13(\字库_1_out_13 ), .out_14(\字库_1_out_14 ),
    .out_15(\字库_1_out_15 ), .out_16(\字库_1_out_16 ), .out_17(\字库_1_out_17 ), .out_18(\字库_1_out_18 ),
    .out_19(\字库_1_out_19 ), .out_20(\字库_1_out_20 ), .out_21(\字库_1_out_21 ), .out_22(\字库_1_out_22 ),
    .out_23(\字库_1_out_23 ), .out_24(\字库_1_out_24 ), .out_25(\字库_1_out_25 ), .out_26(\字库_1_out_26 ),
    .out_27(\字库_1_out_27 ), .out_28(\字库_1_out_28 ), .out_29(\字库_1_out_29 ), .out_30(\字库_1_out_30 ),
    .out_31(\字库_1_out_31 ), .out_32(\字库_1_out_32 ), .out_33(\字库_1_out_33 ), .out_34(\字库_1_out_34 ),
    .\区号 (\国标转区位码_1_区号 ), .\位号 (\国标转区位码_1_位号 ));
  ROM #(.addrWidth(8), .dataWidth(16), .Select("high")) rom_1 (.addr(register_1_q), .data(\发送 ));
  or or_1 (or_1_out, button_1_out, \海明解码_1__2位错 );
  \_16位流水接口  \u_16位流水接口_1  (
    .Din16(\发送 ), .\传输状态In_表明当前传输数据有效 (1'b1), .CLK(\时钟_out ), .Dout16(\n16位流水接口_1_dout16 ),
    .\传输状态Out_表明当前传输数据有效 (\n16位流水接口_1_传输状态out_表明当前传输数据有效 ), .\同步清零_气泡_高电平有效 (or_1_out));  // open: 使能端_低电平有效_stall_高电平有效
  // Probe on \n16位流水接口_1_dout16 
  \海明编码  \u_海明编码_1  (.\原始数据 (\n16位流水接口_1_dout16 ), .\海明码 (\海明编码_1_海明码 ));
  \_22位流水接口  \u_22位流水接口_1  (
    .Din22(\海明编码_1_海明码 ), .\传输状态In_表明当前传输数据有效 (\n16位流水接口_1_传输状态out_表明当前传输数据有效 ), .CLK(\时钟_out ),
    .Dout22(\n22位流水接口_1_dout22 ), .\传输状态Out_表明当前传输数据有效 (\n22位流水接口_1_传输状态out_表明当前传输数据有效 ),
    .\同步清零_气泡_高电平有效 (or_1_out));  // open: 使能端_低电平有效_stall_高电平有效
  \_22位随机干扰  \u_22位随机干扰_1  (
    .\加扰模式 (2'b00), .\_22位输入 (\n22位流水接口_1_dout22 ), .\加扰后数据 (\n22位随机干扰_1_加扰后数据 ), .\增加三位错 (\加噪 ));  // open: 随机加扰屏蔽字
  \字库  \u_字库_2  (
    .out_3(\字库_2_out_3 ), .out_4(\字库_2_out_4 ), .out_5(\字库_2_out_5 ), .out_6(\字库_2_out_6 ),
    .out_7(\字库_2_out_7 ), .out_8(\字库_2_out_8 ), .out_9(\字库_2_out_9 ), .out_10(\字库_2_out_10 ),
    .out_11(\字库_2_out_11 ), .out_12(\字库_2_out_12 ), .out_13(\字库_2_out_13 ), .out_14(\字库_2_out_14 ),
    .out_15(\字库_2_out_15 ), .out_16(\字库_2_out_16 ), .out_17(\字库_2_out_17 ), .out_18(\字库_2_out_18 ),
    .out_19(\字库_2_out_19 ), .out_20(\字库_2_out_20 ), .out_21(\字库_2_out_21 ), .out_22(\字库_2_out_22 ),
    .out_23(\字库_2_out_23 ), .out_24(\字库_2_out_24 ), .out_25(\字库_2_out_25 ), .out_26(\字库_2_out_26 ),
    .out_27(\字库_2_out_27 ), .out_28(\字库_2_out_28 ), .out_29(\字库_2_out_29 ), .out_30(\字库_2_out_30 ),
    .out_31(\字库_2_out_31 ), .out_32(\字库_2_out_32 ), .out_33(\字库_2_out_33 ), .out_34(\字库_2_out_34 ),
    .\区号 (\国标转区位码_2_区号 ), .\位号 (\国标转区位码_2_位号 ));
  \国标转区位码  \u_国标转区位码_2  (.\位号 (\国标转区位码_2_位号 ), .\区号 (\国标转区位码_2_区号 ), .GB2312(\接收 ));
  \_22位流水接口  \u_22位流水接口_2  (
    .Din22(\n22位随机干扰_1_加扰后数据 ), .\传输状态In_表明当前传输数据有效 (\n22位流水接口_1_传输状态out_表明当前传输数据有效 ), .CLK(\时钟_out ),
    .Dout22(\n22位流水接口_2_dout22 ), .\传输状态Out_表明当前传输数据有效 (\n22位流水接口_2_传输状态out_表明当前传输数据有效 ),
    .\同步清零_气泡_高电平有效 (or_1_out));  // open: 使能端_低电平有效_stall_高电平有效
  DotMatrix #(.inputtype("row"), .matrixcols(32), .matrixrows(32), .persist(0), .dotshape("circle")) dotmatrix_2 (
    .row0(\字库_2_out_3 ), .row1(\字库_2_out_4 ), .row2(\字库_2_out_5 ), .row3(\字库_2_out_6 ), .row4(\字库_2_out_7 ),
    .row5(\字库_2_out_8 ), .row6(\字库_2_out_9 ), .row7(\字库_2_out_10 ), .row8(\字库_2_out_11 ),
    .row9(\字库_2_out_12 ), .row10(\字库_2_out_13 ), .row11(\字库_2_out_14 ), .row12(\字库_2_out_15 ),
    .row13(\字库_2_out_16 ), .row14(\字库_2_out_17 ), .row15(\字库_2_out_18 ), .row16(\字库_2_out_19 ),
    .row17(\字库_2_out_20 ), .row18(\字库_2_out_21 ), .row19(\字库_2_out_22 ), .row20(\字库_2_out_23 ),
    .row21(\字库_2_out_24 ), .row22(\字库_2_out_25 ), .row23(\字库_2_out_26 ), .row24(\字库_2_out_27 ),
    .row25(\字库_2_out_28 ), .row26(\字库_2_out_29 ), .row27(\字库_2_out_30 ), .row28(\字库_2_out_31 ),
    .row29(\字库_2_out_32 ), .row30(\字库_2_out_33 ), .row31(\字库_2_out_34 ));
  LED #(.active("true")) \u_一位错  (.in(\海明解码_1__1位错 ));
  LED #(.active("true")) \u_两位错  (.in(\海明解码_1__2位错 ));
  LED #(.active("true")) \u_无错误  (.in(\海明解码_1_无错误 ));
  \海明解码  \u_海明解码_1  (
    .\_1位错 (\海明解码_1__1位错 ), .\_2位错 (\海明解码_1__2位错 ), .\无错误 (\海明解码_1_无错误 ), .\海明码 (\n22位流水接口_2_dout22 ),
    .\纠错后数据 (\海明解码_1_纠错后数据 ));
  // Probe on \海明解码_1_纠错后数据 
  \Stall信号控制  \stall信号控制_1  (.\高电平暂停 (\海明解码_1__2位错 ), .CLK(\时钟_out ), .\清零 (button_1_out), .out_4(\stall信号控制_1_out_4 ));
  \_16位流水接口  \u_16位流水接口_2  (
    .Din16(\海明解码_1_纠错后数据 ), .\传输状态In_表明当前传输数据有效 (\n22位流水接口_2_传输状态out_表明当前传输数据有效 ), .CLK(\时钟_out ),
    .Dout16(\接收 ), .\使能端_低电平有效_stall_高电平有效 (\stall信号控制_1_out_4 ));  // open: 传输状态Out_表明当前传输数据有效, 同步清零_气泡_高电平有效
  // Probe on \接收 

  // Notes on the sheet:
  //   海明码流水传输电路
  //   寄存器
  //   发送方
  //   汉字显示
  //   加法器
  //   GB2312
  //   1.取数阶段
  //   contents of rom_1 (hex, n*v repeats v):
  //   bbaa d6d0 bfc6 bcbc b4f3 d1a7 cac7 b9fa bcd2 bdcc d3fd b2bf d6b1 caf4 b5c4 c8ab b9fa d6d8 b5e3 b4f3
  //   d1a7 a3ac d3c9 d4ad bbaa d6d0 c0ed b9a4 b4f3 d1a7 a1a2 cdac bcc3 d2bd bfc6 b4f3 d1a7 a1a2 cee4 baba
  //   b3c7 cad0 bda8 c9e8 d1a7 d4ba d3da a3b2 a3b0 a3b0 a3b0 c4ea a3b5 d4c2 a3b2 a3b6 c8d5 bacf b2a2 b3c9
  //   c1a2 a3ac cac7 cad7 c5fa c1d0 c8eb b9fa bcd2 a1b0 a3b2 a3b1 a3b1 b9a4 b3cc a1b1 d6d8 b5e3 bda8 c9e8
  //   bacd b9fa bcd2 a1b0 a3b9 a3b8 a3b5 b9a4 b3cc a1b1 bda8 c9e8 b8df d0a3 d6ae d2bb a1a3 d1a7 d0a3 d0a3
  //   d4b0 d5bc b5d8 c6df c7a7 d3e0 c4b6 a3ac d4b0 c4da caf7 c4be b4d0 dcd7 a3ac b1cc b2dd c8e7 d2f0 a3ac
  //   bbb7 beb3 d3c5 d1c5 a3ac beb0 c9ab d0e3 c0f6 a3ac c2cc bbaf b8b2 b8c7 c2ca 3732 25a3 acb1 bbd3 fece
  //   aaa1 b0c9 adc1 d6ca bdb4 f3d1 a7a1 b1a1
  //   ~使能/Stall
  //   发送方在ROM预存了一段中文文字，通过计数器驱动电路每个时钟传输一个汉字
  //   同步清零信号，气泡
  //   用户实现了国标转区位码电路后，可在中间窗口观察发送方和接收方汉字显示是否一致以观察海明检错纠错性能
  //   数据状态：高电平有效
  //   2.编码阶段
  //   电路功能：采用流水分段方式进行数据编码传输，测试海明编码检错纠错能力，当出现2位错时，发送重传信号要求发送方重传，保证接收方按ROM中的地址顺序接受所有汉字
  //   接收方
  //   汉字显示
  //   3.传输阶段
  //   4.解码阶段
  //   此电路可帮助学生理解指令流水线工作原理，重传类似指令流水线中的分支指令
  //   5.显示阶段
  //   请将时钟频率调到8Hz
  //   Ctrl+ K启动电路自动仿真
endmodule

module \CRC传输测试1  (
  input  [15:0] \原始数据 ,
  input  [1:0] \加扰控制 
);

  wire comparator_1_eq, \crc解码_1__1位错 , \crc解码_1__2位错 , \crc解码_1_无错误 ;
  wire [15:0] \crc解码_1_纠错后数据 ;
  wire [21:0] \crc编码_1_crc校验码 , \n22位随机干扰_1_加扰后数据 , \n22位随机干扰_1_随机加扰屏蔽字 ;

  // Probe on \原始数据 
  // Probe on \crc编码_1_crc校验码 
  \CRC编码  \crc编码_1  (.\原始数据 (\原始数据 ), .\CRC校验码 (\crc编码_1_crc校验码 ));
  // Probe on \crc编码_1_crc校验码 
  // Probe on \n22位随机干扰_1_随机加扰屏蔽字 
  // Probe on \n22位随机干扰_1_加扰后数据 
  \_22位随机干扰  \u_22位随机干扰_1  (
    .\加扰模式 (\加扰控制 ), .\随机加扰屏蔽字 (\n22位随机干扰_1_随机加扰屏蔽字 ), .\_22位输入 (\crc编码_1_crc校验码 ),
    .\加扰后数据 (\n22位随机干扰_1_加扰后数据 ));  // open: 增加三位错
  // Probe on \n22位随机干扰_1_加扰后数据 
  LED #(.active("true")) \u_一位错  (.in(\crc解码_1__1位错 ));
  LED #(.active("true")) \u_无错误  (.in(\crc解码_1_无错误 ));
  LED #(.active("true")) \u_两位错  (.in(\crc解码_1__2位错 ));
  \CRC解码  \crc解码_1  (
    .\CRC编码 (\n22位随机干扰_1_加扰后数据 ), .\无错误 (\crc解码_1_无错误 ), .\_1位错 (\crc解码_1__1位错 ), .\_2位错 (\crc解码_1__2位错 ),
    .\纠错后数据 (\crc解码_1_纠错后数据 ));
  // Probe on \crc解码_1_纠错后数据 
  LED #(.active("true")) \u_数据正确  (.in(comparator_1_eq));
  Comparator #(.width(16), .mode("twosComplement")) comparator_1 (
    .a(\原始数据 ), .b(\crc解码_1_纠错后数据 ), .eq(comparator_1_eq));  // open: gt, lt

  // Notes on the sheet:
  //   发送方
  //   电路功能：测试CRC编解码电路正确性，仿真时设置加扰控制位和原始数据，按CTRL+T触发不同的干扰，检验编解码电路功能
  //   Ctrl+T 驱动时钟触发随机干扰变化
  //   CRC编解码传输电路
  //   加扰控制00：不加扰  01:1位加扰 10:2位加扰 11：随机加扰
  //   接收方
endmodule

module \CRC传输测试2  (
  input  [1:0] \加扰控制 
);

  wire button_1_out, comparator_1_eq, \crc解码_1__1位错 , \crc解码_1__2位错 , \crc解码_1_无错误 , \时钟_out ;
  wire [6:0] \国标转区位码_1_位号 , \国标转区位码_1_区号 , \国标转区位码_2_位号 , \国标转区位码_2_区号 ;
  wire [7:0] counter_1_q;
  wire [15:0] \发送 , \接收 ;
  wire [21:0] \crc编码_1_crc校验码 , \n22位随机干扰_1_加扰后数据 , \n22位随机干扰_1_随机加扰屏蔽字 ;
  wire [31:0] \字库_1_out_3 , \字库_1_out_4 , \字库_1_out_5 , \字库_1_out_6 , \字库_1_out_7 , \字库_1_out_8 ,
       \字库_1_out_9 , \字库_1_out_10 , \字库_1_out_11 , \字库_1_out_12 , \字库_1_out_13 , \字库_1_out_14 ,
       \字库_1_out_15 , \字库_1_out_16 , \字库_1_out_17 , \字库_1_out_18 , \字库_1_out_19 , \字库_1_out_20 ,
       \字库_1_out_21 , \字库_1_out_22 , \字库_1_out_23 , \字库_1_out_24 , \字库_1_out_25 , \字库_1_out_26 ,
       \字库_1_out_27 , \字库_1_out_28 , \字库_1_out_29 , \字库_1_out_30 , \字库_1_out_31 , \字库_1_out_32 ,
       \字库_1_out_33 , \字库_1_out_34 , \字库_2_out_3 , \字库_2_out_4 , \字库_2_out_5 , \字库_2_out_6 , \字库_2_out_7 ,
       \字库_2_out_8 , \字库_2_out_9 , \字库_2_out_10 , \字库_2_out_11 , \字库_2_out_12 , \字库_2_out_13 , \字库_2_out_14 ,
       \字库_2_out_15 , \字库_2_out_16 , \字库_2_out_17 , \字库_2_out_18 , \字库_2_out_19 , \字库_2_out_20 ,
       \字库_2_out_21 , \字库_2_out_22 , \字库_2_out_23 , \字库_2_out_24 , \字库_2_out_25 , \字库_2_out_26 ,
       \字库_2_out_27 , \字库_2_out_28 , \字库_2_out_29 , \字库_2_out_30 , \字库_2_out_31 , \字库_2_out_32 ,
       \字库_2_out_33 , \字库_2_out_34 ;

  Clock #(.highDuration(1), .lowDuration(1)) \u_时钟  (.out(\时钟_out ));
  Counter #(.width(8), .max('hff), .ongoal("wrap"), .trigger("rising"), .behavior("old")) counter_1 (
    .Q(counter_1_q), .clk(\时钟_out ), .clr(button_1_out));  // open: load, D, count, carry, preset
  Button button_1 (.out(button_1_out));
  \国标转区位码  \u_国标转区位码_1  (.\位号 (\国标转区位码_1_位号 ), .\区号 (\国标转区位码_1_区号 ), .GB2312(\发送 ));
  DotMatrix #(.inputtype("row"), .matrixcols(32), .matrixrows(32), .persist(0), .dotshape("circle")) dotmatrix_1 (
    .row0(\字库_1_out_3 ), .row1(\字库_1_out_4 ), .row2(\字库_1_out_5 ), .row3(\字库_1_out_6 ), .row4(\字库_1_out_7 ),
    .row5(\字库_1_out_8 ), .row6(\字库_1_out_9 ), .row7(\字库_1_out_10 ), .row8(\字库_1_out_11 ),
    .row9(\字库_1_out_12 ), .row10(\字库_1_out_13 ), .row11(\字库_1_out_14 ), .row12(\字库_1_out_15 ),
    .row13(\字库_1_out_16 ), .row14(\字库_1_out_17 ), .row15(\字库_1_out_18 ), .row16(\字库_1_out_19 ),
    .row17(\字库_1_out_20 ), .row18(\字库_1_out_21 ), .row19(\字库_1_out_22 ), .row20(\字库_1_out_23 ),
    .row21(\字库_1_out_24 ), .row22(\字库_1_out_25 ), .row23(\字库_1_out_26 ), .row24(\字库_1_out_27 ),
    .row25(\字库_1_out_28 ), .row26(\字库_1_out_29 ), .row27(\字库_1_out_30 ), .row28(\字库_1_out_31 ),
    .row29(\字库_1_out_32 ), .row30(\字库_1_out_33 ), .row31(\字库_1_out_34 ));
  \字库  \u_字库_1  (
    .out_3(\字库_1_out_3 ), .out_4(\字库_1_out_4 ), .out_5(\字库_1_out_5 ), .out_6(\字库_1_out_6 ),
    .out_7(\字库_1_out_7 ), .out_8(\字库_1_out_8 ), .out_9(\字库_1_out_9 ), .out_10(\字库_1_out_10 ),
    .out_11(\字库_1_out_11 ), .out_12(\字库_1_out_12 ), .out_13(\字库_1_out_13 ), .out_14(\字库_1_out_14 ),
    .out_15(\字库_1_out_15 ), .out_16(\字库_1_out_16 ), .out_17(\字库_1_out_17 ), .out_18(\字库_1_out_18 ),
    .out_19(\字库_1_out_19 ), .out_20(\字库_1_out_20 ), .out_21(\字库_1_out_21 ), .out_22(\字库_1_out_22 ),
    .out_23(\字库_1_out_23 ), .out_24(\字库_1_out_24 ), .out_25(\字库_1_out_25 ), .out_26(\字库_1_out_26 ),
    .out_27(\字库_1_out_27 ), .out_28(\字库_1_out_28 ), .out_29(\字库_1_out_29 ), .out_30(\字库_1_out_30 ),
    .out_31(\字库_1_out_31 ), .out_32(\字库_1_out_32 ), .out_33(\字库_1_out_33 ), .out_34(\字库_1_out_34 ),
    .\区号 (\国标转区位码_1_区号 ), .\位号 (\国标转区位码_1_位号 ));
  ROM #(.addrWidth(8), .dataWidth(16), .Select("high")) rom_1 (.addr(counter_1_q), .data(\发送 ));
  // Probe on \发送 
  // Probe on \crc编码_1_crc校验码 
  \CRC编码  \crc编码_1  (.\原始数据 (\发送 ), .\CRC校验码 (\crc编码_1_crc校验码 ));
  // Probe on \crc编码_1_crc校验码 
  // Probe on \n22位随机干扰_1_随机加扰屏蔽字 
  \_22位随机干扰  \u_22位随机干扰_1  (
    .\加扰模式 (\加扰控制 ), .\随机加扰屏蔽字 (\n22位随机干扰_1_随机加扰屏蔽字 ), .\_22位输入 (\crc编码_1_crc校验码 ),
    .\加扰后数据 (\n22位随机干扰_1_加扰后数据 ));  // open: 增加三位错
  // Probe on \n22位随机干扰_1_加扰后数据 
  // Probe on \n22位随机干扰_1_加扰后数据 
  \字库  \u_字库_2  (
    .out_3(\字库_2_out_3 ), .out_4(\字库_2_out_4 ), .out_5(\字库_2_out_5 ), .out_6(\字库_2_out_6 ),
    .out_7(\字库_2_out_7 ), .out_8(\字库_2_out_8 ), .out_9(\字库_2_out_9 ), .out_10(\字库_2_out_10 ),
    .out_11(\字库_2_out_11 ), .out_12(\字库_2_out_12 ), .out_13(\字库_2_out_13 ), .out_14(\字库_2_out_14 ),
    .out_15(\字库_2_out_15 ), .out_16(\字库_2_out_16 ), .out_17(\字库_2_out_17 ), .out_18(\字库_2_out_18 ),
    .out_19(\字库_2_out_19 ), .out_20(\字库_2_out_20 ), .out_21(\字库_2_out_21 ), .out_22(\字库_2_out_22 ),
    .out_23(\字库_2_out_23 ), .out_24(\字库_2_out_24 ), .out_25(\字库_2_out_25 ), .out_26(\字库_2_out_26 ),
    .out_27(\字库_2_out_27 ), .out_28(\字库_2_out_28 ), .out_29(\字库_2_out_29 ), .out_30(\字库_2_out_30 ),
    .out_31(\字库_2_out_31 ), .out_32(\字库_2_out_32 ), .out_33(\字库_2_out_33 ), .out_34(\字库_2_out_34 ),
    .\区号 (\国标转区位码_2_区号 ), .\位号 (\国标转区位码_2_位号 ));
  \国标转区位码  \u_国标转区位码_2  (.\位号 (\国标转区位码_2_位号 ), .\区号 (\国标转区位码_2_区号 ), .GB2312(\接收 ));
  LED #(.active("true")) \u_无错误  (.in(\crc解码_1_无错误 ));
  LED #(.active("true")) \u_两位错  (.in(\crc解码_1__2位错 ));
  LED #(.active("true")) \u_一位错  (.in(\crc解码_1__1位错 ));
  DotMatrix #(.inputtype("row"), .matrixcols(32), .matrixrows(32), .persist(0), .dotshape("circle")) dotmatrix_2 (
    .row0(\字库_2_out_3 ), .row1(\字库_2_out_4 ), .row2(\字库_2_out_5 ), .row3(\字库_2_out_6 ), .row4(\字库_2_out_7 ),
    .row5(\字库_2_out_8 ), .row6(\字库_2_out_9 ), .row7(\字库_2_out_10 ), .row8(\字库_2_out_11 ),
    .row9(\字库_2_out_12 ), .row10(\字库_2_out_13 ), .row11(\字库_2_out_14 ), .row12(\字库_2_out_15 ),
    .row13(\字库_2_out_16 ), .row14(\字库_2_out_17 ), .row15(\字库_2_out_18 ), .row16(\字库_2_out_19 ),
    .row17(\字库_2_out_20 ), .row18(\字库_2_out_21 ), .row19(\字库_2_out_22 ), .row20(\字库_2_out_23 ),
    .row21(\字库_2_out_24 ), .row22(\字库_2_out_25 ), .row23(\字库_2_out_26 ), .row24(\字库_2_out_27 ),
    .row25(\字库_2_out_28 ), .row26(\字库_2_out_29 ), .row27(\字库_2_out_30 ), .row28(\字库_2_out_31 ),
    .row29(\字库_2_out_32 ), .row30(\字库_2_out_33 ), .row31(\字库_2_out_34 ));
  \CRC解码  \crc解码_1  (
    .\CRC编码 (\n22位随机干扰_1_加扰后数据 ), .\无错误 (\crc解码_1_无错误 ), .\_1位错 (\crc解码_1__1位错 ), .\_2位错 (\crc解码_1__2位错 ),
    .\纠错后数据 (\接收 ));
  // Probe on \接收 
  Comparator #(.width(16), .mode("twosComplement")) comparator_1 (
    .a(\发送 ), .b(\接收 ), .eq(comparator_1_eq));  // open: gt, lt
  LED #(.active("true")) \u_数据正确  (.in(comparator_1_eq));

  // Notes on the sheet:
  //   发送方
  //   计数器
  //   发送方
  //   汉字显示
  //   GB2312
  //   Ctrl+T 驱动时钟触发随机干扰变化
  //   contents of rom_1 (hex, n*v repeats v):
  //   bbaa d6d0 bfc6 bcbc b4f3 d1a7 cac7 b9fa bcd2 bdcc d3fd b2bf d6b1 caf4 b5c4 c8ab b9fa d6d8 b5e3 b4f3
  //   d1a7 a3ac d3c9 d4ad bbaa d6d0 c0ed b9a4 b4f3 d1a7 a1a2 cdac bcc3 d2bd bfc6 b4f3 d1a7 a1a2 cee4 baba
  //   b3c7 cad0 bda8 c9e8 d1a7 d4ba d3da a3b2 a3b0 a3b0 a3b0 c4ea a3b5 d4c2 a3b2 a3b6 c8d5 bacf b2a2 b3c9
  //   c1a2 a3ac cac7 cad7 c5fa c1d0 c8eb b9fa bcd2 a1b0 a3b2 a3b1 a3b1 b9a4 b3cc a1b1 d6d8 b5e3 bda8 c9e8
  //   bacd b9fa bcd2 a1b0 a3b9 a3b8 a3b5 b9a4 b3cc a1b1 bda8 c9e8 b8df d0a3 d6ae d2bb a1a3 d1a7 d0a3 d0a3
  //   d4b0 d5bc b5d8 c6df c7a7 d3e0 c4b6 a3ac d4b0 c4da caf7 c4be b4d0 dcd7 a3ac b1cc b2dd c8e7 d2f0 a3ac
  //   bbb7 beb3 d3c5 d1c5 a3ac beb0 c9ab d0e3 c0f6 a3ac c2cc bbaf b8b2 b8c7 c2ca 3732 25a3 acb1 bbd3 fece
  //   aaa1 b0c9 adc1 d6ca bdb4 f3d1 a7a1 b1a1
  //   电路功能：测试CRC编解码电路正确性，仿真时设置加扰控制位和原始数据，按CTRL+T触发不同的干扰，检验编解码电路功能
  //   发送方在ROM预存了一段中文文字，通过计数器驱动电路每个时钟传输一个汉字到接收方
  //   用户实现了国标转区位码电路后，可在中间窗口观察发送方和接收方汉字显示是否一致以观察海明检错纠错性能
  //   CRC编解码传输电路
  //   接收方
  //   汉字显示
  //   Ctrl+T 驱动时钟触发随机干扰变化
  //   加扰控制00：不加扰  01:1位加扰 10:2位加扰 11：随机加扰
  //   加扰控制00：不加扰  01:1位加扰 10:2位加扰 11：随机加扰
  //   接收方
  //   请将时钟频率调到8Hz
endmodule

module \CRC编码流水传输  (
  input  \加噪 
);

  wire \crc解码_1__1位错 , \crc解码_1__2位错 , \crc解码_1_无错误 , \n16位流水接口_1_传输状态out_表明当前传输数据有效 ,
       \n22位流水接口_1_传输状态out_表明当前传输数据有效 , \n22位流水接口_2_传输状态out_表明当前传输数据有效 , undriven, \时钟_out ;
  wire [6:0] \国标转区位码_1_位号 , \国标转区位码_1_区号 , \国标转区位码_2_位号 , \国标转区位码_2_区号 ;
  wire [7:0] adder_1_out, register_1_q;
  wire [15:0] \crc解码_1_纠错后数据 , \n16位流水接口_1_dout16 , \发送 , \接收 ;
  wire [21:0] \crc编码_1_crc校验码 , \n22位流水接口_1_dout22 , \n22位流水接口_2_dout22 , \n22位随机干扰_1_加扰后数据 ;
  wire [31:0] \字库_1_out_3 , \字库_1_out_4 , \字库_1_out_5 , \字库_1_out_6 , \字库_1_out_7 , \字库_1_out_8 ,
       \字库_1_out_9 , \字库_1_out_10 , \字库_1_out_11 , \字库_1_out_12 , \字库_1_out_13 , \字库_1_out_14 ,
       \字库_1_out_15 , \字库_1_out_16 , \字库_1_out_17 , \字库_1_out_18 , \字库_1_out_19 , \字库_1_out_20 ,
       \字库_1_out_21 , \字库_1_out_22 , \字库_1_out_23 , \字库_1_out_24 , \字库_1_out_25 , \字库_1_out_26 ,
       \字库_1_out_27 , \字库_1_out_28 , \字库_1_out_29 , \字库_1_out_30 , \字库_1_out_31 , \字库_1_out_32 ,
       \字库_1_out_33 , \字库_1_out_34 , \字库_2_out_3 , \字库_2_out_4 , \字库_2_out_5 , \字库_2_out_6 , \字库_2_out_7 ,
       \字库_2_out_8 , \字库_2_out_9 , \字库_2_out_10 , \字库_2_out_11 , \字库_2_out_12 , \字库_2_out_13 , \字库_2_out_14 ,
       \字库_2_out_15 , \字库_2_out_16 , \字库_2_out_17 , \字库_2_out_18 , \字库_2_out_19 , \字库_2_out_20 ,
       \字库_2_out_21 , \字库_2_out_22 , \字库_2_out_23 , \字库_2_out_24 , \字库_2_out_25 , \字库_2_out_26 ,
       \字库_2_out_27 , \字库_2_out_28 , \字库_2_out_29 , \字库_2_out_30 , \字库_2_out_31 , \字库_2_out_32 ,
       \字库_2_out_33 , \字库_2_out_34 ;

  Register #(.width(8), .trigger("rising"), .Select("low")) register_1 (
    .D(adder_1_out), .Q(register_1_q), .clk(\时钟_out ));  // open: en, clr
  Clock #(.highDuration(1), .lowDuration(1)) \u_时钟  (.out(\时钟_out ));
  \国标转区位码  \u_国标转区位码_1  (.\位号 (\国标转区位码_1_位号 ), .\区号 (\国标转区位码_1_区号 ), .GB2312(\发送 ));
  Adder #(.width(8)) adder_1 (.a(8'h1), .b(register_1_q), .out(adder_1_out));  // open: cin, cout
  \字库  \u_字库_1  (
    .out_3(\字库_1_out_3 ), .out_4(\字库_1_out_4 ), .out_5(\字库_1_out_5 ), .out_6(\字库_1_out_6 ),
    .out_7(\字库_1_out_7 ), .out_8(\字库_1_out_8 ), .out_9(\字库_1_out_9 ), .out_10(\字库_1_out_10 ),
    .out_11(\字库_1_out_11 ), .out_12(\字库_1_out_12 ), .out_13(\字库_1_out_13 ), .out_14(\字库_1_out_14 ),
    .out_15(\字库_1_out_15 ), .out_16(\字库_1_out_16 ), .out_17(\字库_1_out_17 ), .out_18(\字库_1_out_18 ),
    .out_19(\字库_1_out_19 ), .out_20(\字库_1_out_20 ), .out_21(\字库_1_out_21 ), .out_22(\字库_1_out_22 ),
    .out_23(\字库_1_out_23 ), .out_24(\字库_1_out_24 ), .out_25(\字库_1_out_25 ), .out_26(\字库_1_out_26 ),
    .out_27(\字库_1_out_27 ), .out_28(\字库_1_out_28 ), .out_29(\字库_1_out_29 ), .out_30(\字库_1_out_30 ),
    .out_31(\字库_1_out_31 ), .out_32(\字库_1_out_32 ), .out_33(\字库_1_out_33 ), .out_34(\字库_1_out_34 ),
    .\区号 (\国标转区位码_1_区号 ), .\位号 (\国标转区位码_1_位号 ));
  DotMatrix #(.inputtype("row"), .matrixcols(32), .matrixrows(32), .persist(0), .dotshape("circle")) dotmatrix_1 (
    .row0(\字库_1_out_3 ), .row1(\字库_1_out_4 ), .row2(\字库_1_out_5 ), .row3(\字库_1_out_6 ), .row4(\字库_1_out_7 ),
    .row5(\字库_1_out_8 ), .row6(\字库_1_out_9 ), .row7(\字库_1_out_10 ), .row8(\字库_1_out_11 ),
    .row9(\字库_1_out_12 ), .row10(\字库_1_out_13 ), .row11(\字库_1_out_14 ), .row12(\字库_1_out_15 ),
    .row13(\字库_1_out_16 ), .row14(\字库_1_out_17 ), .row15(\字库_1_out_18 ), .row16(\字库_1_out_19 ),
    .row17(\字库_1_out_20 ), .row18(\字库_1_out_21 ), .row19(\字库_1_out_22 ), .row20(\字库_1_out_23 ),
    .row21(\字库_1_out_24 ), .row22(\字库_1_out_25 ), .row23(\字库_1_out_26 ), .row24(\字库_1_out_27 ),
    .row25(\字库_1_out_28 ), .row26(\字库_1_out_29 ), .row27(\字库_1_out_30 ), .row28(\字库_1_out_31 ),
    .row29(\字库_1_out_32 ), .row30(\字库_1_out_33 ), .row31(\字库_1_out_34 ));
  ROM #(.addrWidth(8), .dataWidth(16), .Select("high")) rom_1 (.addr(register_1_q), .data(\发送 ));
  \_16位流水接口  \u_16位流水接口_1  (
    .Din16(\发送 ), .\传输状态In_表明当前传输数据有效 (1'b1), .CLK(\时钟_out ), .Dout16(\n16位流水接口_1_dout16 ),
    .\传输状态Out_表明当前传输数据有效 (\n16位流水接口_1_传输状态out_表明当前传输数据有效 ), .\使能端_低电平有效_stall_高电平有效 (undriven));  // open: 同步清零_气泡_高电平有效
  \CRC编码  \crc编码_1  (.\原始数据 (\n16位流水接口_1_dout16 ), .\CRC校验码 (\crc编码_1_crc校验码 ));
  \_22位流水接口  \u_22位流水接口_1  (
    .Din22(\crc编码_1_crc校验码 ), .\传输状态In_表明当前传输数据有效 (\n16位流水接口_1_传输状态out_表明当前传输数据有效 ), .CLK(\时钟_out ),
    .Dout22(\n22位流水接口_1_dout22 ), .\传输状态Out_表明当前传输数据有效 (\n22位流水接口_1_传输状态out_表明当前传输数据有效 ));  // open: 同步清零_气泡_高电平有效, 使能端_低电平有效_stall_高电平有效
  \_22位随机干扰  \u_22位随机干扰_1  (
    .\加扰模式 (2'b00), .\_22位输入 (\n22位流水接口_1_dout22 ), .\加扰后数据 (\n22位随机干扰_1_加扰后数据 ), .\增加三位错 (\加噪 ));  // open: 随机加扰屏蔽字
  \字库  \u_字库_2  (
    .out_3(\字库_2_out_3 ), .out_4(\字库_2_out_4 ), .out_5(\字库_2_out_5 ), .out_6(\字库_2_out_6 ),
    .out_7(\字库_2_out_7 ), .out_8(\字库_2_out_8 ), .out_9(\字库_2_out_9 ), .out_10(\字库_2_out_10 ),
    .out_11(\字库_2_out_11 ), .out_12(\字库_2_out_12 ), .out_13(\字库_2_out_13 ), .out_14(\字库_2_out_14 ),
    .out_15(\字库_2_out_15 ), .out_16(\字库_2_out_16 ), .out_17(\字库_2_out_17 ), .out_18(\字库_2_out_18 ),
    .out_19(\字库_2_out_19 ), .out_20(\字库_2_out_20 ), .out_21(\字库_2_out_21 ), .out_22(\字库_2_out_22 ),
    .out_23(\字库_2_out_23 ), .out_24(\字库_2_out_24 ), .out_25(\字库_2_out_25 ), .out_26(\字库_2_out_26 ),
    .out_27(\字库_2_out_27 ), .out_28(\字库_2_out_28 ), .out_29(\字库_2_out_29 ), .out_30(\字库_2_out_30 ),
    .out_31(\字库_2_out_31 ), .out_32(\字库_2_out_32 ), .out_33(\字库_2_out_33 ), .out_34(\字库_2_out_34 ),
    .\区号 (\国标转区位码_2_区号 ), .\位号 (\国标转区位码_2_位号 ));
  \国标转区位码  \u_国标转区位码_2  (.\位号 (\国标转区位码_2_位号 ), .\区号 (\国标转区位码_2_区号 ), .GB2312(\接收 ));
  \_22位流水接口  \u_22位流水接口_2  (
    .Din22(\n22位随机干扰_1_加扰后数据 ), .\传输状态In_表明当前传输数据有效 (\n22位流水接口_1_传输状态out_表明当前传输数据有效 ), .CLK(\时钟_out ),
    .Dout22(\n22位流水接口_2_dout22 ), .\传输状态Out_表明当前传输数据有效 (\n22位流水接口_2_传输状态out_表明当前传输数据有效 ));  // open: 同步清零_气泡_高电平有效, 使能端_低电平有效_stall_高电平有效
  DotMatrix #(.inputtype("row"), .matrixcols(32), .matrixrows(32), .persist(0), .dotshape("circle")) dotmatrix_2 (
    .row0(\字库_2_out_3 ), .row1(\字库_2_out_4 ), .row2(\字库_2_out_5 ), .row3(\字库_2_out_6 ), .row4(\字库_2_out_7 ),
    .row5(\字库_2_out_8 ), .row6(\字库_2_out_9 ), .row7(\字库_2_out_10 ), .row8(\字库_2_out_11 ),
    .row9(\字库_2_out_12 ), .row10(\字库_2_out_13 ), .row11(\字库_2_out_14 ), .row12(\字库_2_out_15 ),
    .row13(\字库_2_out_16 ), .row14(\字库_2_out_17 ), .row15(\字库_2_out_18 ), .row16(\字库_2_out_19 ),
    .row17(\字库_2_out_20 ), .row18(\字库_2_out_21 ), .row19(\字库_2_out_22 ), .row20(\字库_2_out_23 ),
    .row21(\字库_2_out_24 ), .row22(\字库_2_out_25 ), .row23(\字库_2_out_26 ), .row24(\字库_2_out_27 ),
    .row25(\字库_2_out_28 ), .row26(\字库_2_out_29 ), .row27(\字库_2_out_30 ), .row28(\字库_2_out_31 ),
    .row29(\字库_2_out_32 ), .row30(\字库_2_out_33 ), .row31(\字库_2_out_34 ));
  LED #(.active("true")) \u_一位错  (.in(\crc解码_1__1位错 ));
  LED #(.active("true")) \u_两位错  (.in(\crc解码_1__2位错 ));
  LED #(.active("true")) \u_无错误  (.in(\crc解码_1_无错误 ));
  \CRC解码  \crc解码_1  (
    .\CRC编码 (\n22位流水接口_2_dout22 ), .\无错误 (\crc解码_1_无错误 ), .\_1位错 (\crc解码_1__1位错 ), .\_2位错 (\crc解码_1__2位错 ),
    .\纠错后数据 (\crc解码_1_纠错后数据 ));
  \_16位流水接口  \u_16位流水接口_2  (
    .Din16(\crc解码_1_纠错后数据 ), .\传输状态In_表明当前传输数据有效 (\n22位流水接口_2_传输状态out_表明当前传输数据有效 ), .CLK(\时钟_out ),
    .Dout16(\接收 ));  // open: 传输状态Out_表明当前传输数据有效, 同步清零_气泡_高电平有效, 使能端_低电平有效_stall_高电平有效
  // Probe on \接收 

  // Notes on the sheet:
  //   CRC编码流水传输电路
  //   寄存器
  //   发送方
  //   汉字显示
  //   加法器
  //   GB2312
  //   1.取数阶段
  //   contents of rom_1 (hex, n*v repeats v):
  //   bbaa d6d0 bfc6 bcbc b4f3 d1a7 cac7 b9fa bcd2 bdcc d3fd b2bf d6b1 caf4 b5c4 c8ab b9fa d6d8 b5e3 b4f3
  //   d1a7 a3ac d3c9 d4ad bbaa d6d0 c0ed b9a4 b4f3 d1a7 a1a2 cdac bcc3 d2bd bfc6 b4f3 d1a7 a1a2 cee4 baba
  //   b3c7 cad0 bda8 c9e8 d1a7 d4ba d3da a3b2 a3b0 a3b0 a3b0 c4ea a3b5 d4c2 a3b2 a3b6 c8d5 bacf b2a2 b3c9
  //   c1a2 a3ac cac7 cad7 c5fa c1d0 c8eb b9fa bcd2 a1b0 a3b2 a3b1 a3b1 b9a4 b3cc a1b1 d6d8 b5e3 bda8 c9e8
  //   bacd b9fa bcd2 a1b0 a3b9 a3b8 a3b5 b9a4 b3cc a1b1 bda8 c9e8 b8df d0a3 d6ae d2bb a1a3 d1a7 d0a3 d0a3
  //   d4b0 d5bc b5d8 c6df c7a7 d3e0 c4b6 a3ac d4b0 c4da caf7 c4be b4d0 dcd7 a3ac b1cc b2dd c8e7 d2f0 a3ac
  //   bbb7 beb3 d3c5 d1c5 a3ac beb0 c9ab d0e3 c0f6 a3ac c2cc bbaf b8b2 b8c7 c2ca 3732 25a3 acb1 bbd3 fece
  //   aaa1 b0c9 adc1 d6ca bdb4 f3d1 a7a1 b1a1
  //   ~使能/Stall
  //   发送方在ROM预存了一段中文文字，通过计数器驱动电路每个时钟传输一个汉字
  //   同步清零信号，气泡
  //   用户实现了国标转区位码电路后，可在中间窗口观察发送方和接收方汉字显示是否一致以观察海明检错纠错性能
  //   数据状态：高电平有效
  //   2.编码阶段
  //   电路功能：采用流水分段方式进行数据编码传输，测试海明编码检错纠错能力，当出现2位错时，发送重传信号要求发送方重传，保证接收方按ROM中的地址顺序接受所有汉字
  //   接收方
  //   汉字显示
  //   3.传输阶段
  //   此电路可帮助学生理解指令流水线工作原理，重传类似指令流水线中的分支指令
  //   4.解码阶段
  //   5.显示阶段
  //   请将时钟频率调到8Hz
  //   Ctrl+ K启动电路自动仿真
endmodule

// 随机干扰
module \_22位随机干扰  (
  input  [21:0] \_22位输入 ,
  input  [1:0] \加扰模式 ,
  input  \增加三位错 ,
  output [21:0] \随机加扰屏蔽字 ,
  output [21:0] \加扰后数据 
);

  wire clock_1_out, comparator_1_eq, not_1_out, \随机信号_5_out ;
  wire [1:0] \随机信号_4_out ;
  wire [3:0] \随机信号_2_out , \随机信号_3_out , \随机信号_out ;
  wire [15:0] \_1位加扰A ;
  wire [21:0] \_1位加扰 , \_2位加扰 , \_3位加扰 , multiplexer_1_out, multiplexer_4_out, \随机加扰 ;
  wire [21:6] \_1位加扰B , \_1位加扰C ;

  Clock #(.highDuration(1), .lowDuration(1)) clock_1 (.out(clock_1_out));
  Decoder #(.select(4), .tristate("false"), .disabled("Z"), .enable("false")) decoder_1 (
    .out0(\_1位加扰A [0]), .out1(\_1位加扰A [1]), .out2(\_1位加扰A [2]), .out3(\_1位加扰A [3]), .out4(\_1位加扰A [4]),
    .out5(\_1位加扰A [5]), .out6(\_1位加扰A [6]), .out7(\_1位加扰A [7]), .out8(\_1位加扰A [8]), .out9(\_1位加扰A [9]),
    .out10(\_1位加扰A [10]), .out11(\_1位加扰A [11]), .out12(\_1位加扰A [12]), .out13(\_1位加扰A [13]),
    .out14(\_1位加扰A [14]), .out15(\_1位加扰A [15]), .sel(\随机信号_out ));
  Random #(.width(4), .seed(0), .trigger("rising")) \u_随机信号  (.clk(clock_1_out), .out(\随机信号_out ));  // open: next, clr
  Random #(.width(4), .seed(18), .trigger("rising")) \u_随机信号_2  (
    .clk(clock_1_out), .out(\随机信号_2_out ));  // open: next, clr
  Decoder #(.select(4), .tristate("false"), .disabled("Z"), .enable("false")) decoder_2 (
    .out0(\_1位加扰B [6]), .out1(\_1位加扰B [7]), .out2(\_1位加扰B [8]), .out3(\_1位加扰B [9]), .out4(\_1位加扰B [10]),
    .out5(\_1位加扰B [11]), .out6(\_1位加扰B [12]), .out7(\_1位加扰B [13]), .out8(\_1位加扰B [14]), .out9(\_1位加扰B [15]),
    .out10(\_1位加扰B [16]), .out11(\_1位加扰B [17]), .out12(\_1位加扰B [18]), .out13(\_1位加扰B [19]),
    .out14(\_1位加扰B [20]), .out15(\_1位加扰B [21]), .sel(\随机信号_2_out ));
  Random #(.width(4), .seed(3), .trigger("rising")) \u_随机信号_3  (
    .clk(clock_1_out), .out(\随机信号_3_out ));  // open: next, clr
  Random #(.width(2), .seed(21), .trigger("rising")) \u_随机信号_4  (
    .clk(clock_1_out), .out(\随机信号_4_out ));  // open: next, clr
  Random #(.width(1), .seed(31), .trigger("rising")) \u_随机信号_5  (
    .clk(clock_1_out), .out(\随机信号_5_out ));  // open: next, clr
  Decoder #(.select(4), .tristate("false"), .disabled("Z"), .enable("false")) decoder_3 (
    .out0(\_1位加扰C [6]), .out1(\_1位加扰C [7]), .out2(\_1位加扰C [8]), .out3(\_1位加扰C [9]), .out4(\_1位加扰C [10]),
    .out5(\_1位加扰C [11]), .out6(\_1位加扰C [12]), .out7(\_1位加扰C [13]), .out8(\_1位加扰C [14]), .out9(\_1位加扰C [15]),
    .out10(\_1位加扰C [16]), .out11(\_1位加扰C [17]), .out12(\_1位加扰C [18]), .out13(\_1位加扰C [19]),
    .out14(\_1位加扰C [20]), .out15(\_1位加扰C [21]), .sel(\随机信号_3_out ));
  Pull_Resistor #(.pull(0)) pull_resistor_1 (.node(\增加三位错 ));
  Multiplexer #(.select(1), .width(22), .disabled("Z"), .enable("false")) multiplexer_1 (
    .in0({\_1位加扰B , {6{1'b0}}}), .in1(\_3位加扰 ), .out(multiplexer_1_out), .sel(\增加三位错 ));
  Multiplexer #(.select(2), .width(22), .disabled("Z"), .enable("false")) multiplexer_2 (
    .in0({22{1'b0}}), .in1({{6{1'b0}}, \_1位加扰A }), .in2(\_2位加扰 ), .in3(multiplexer_1_out), .out(\随机加扰 ),
    .sel(\随机信号_4_out ));
  Pull_Resistor #(.pull(1)) pull_resistor_2 (.node(\加扰模式 ));
  Comparator #(.width(22), .mode("unsigned")) comparator_1 (
    .a({{6{1'b0}}, \_1位加扰A }), .b({\_1位加扰B , {6{1'b0}}}), .eq(comparator_1_eq));  // open: gt, lt
  Multiplexer #(.select(2), .width(22), .disabled("Z"), .enable("false")) multiplexer_3 (
    .in0({22{1'b0}}), .in1(\_1位加扰 ), .in2(\_2位加扰 ), .in3(\随机加扰 ), .out(\随机加扰屏蔽字 ), .sel(\加扰模式 ));
  Multiplexer #(.select(1), .width(22), .disabled("Z"), .enable("false")) multiplexer_4 (
    .in0(22'h1), .in1({{6{1'b0}}, \_1位加扰A }), .out(multiplexer_4_out), .sel(not_1_out));
  not not_1 (not_1_out, comparator_1_eq);
  assign \_2位加扰  = multiplexer_4_out ^ {\_1位加扰B , {6{1'b0}}};  // XOR_Gate xor_1, 22 bits wide
  assign \_3位加扰  = \_2位加扰  ^ {\_1位加扰C , {6{1'b0}}};  // XOR_Gate xor_2, 22 bits wide
  Multiplexer #(.select(1), .width(22), .disabled("Z"), .enable("false")) multiplexer_5 (
    .in0(multiplexer_4_out), .in1({\_1位加扰B , {6{1'b0}}}), .out(\_1位加扰 ), .sel(\随机信号_5_out ));
  assign \加扰后数据  = \随机加扰屏蔽字  ^ \_22位输入 ;  // XOR_Gate xor_3, 22 bits wide

  // Notes on the sheet:
  //   在随机加扰模式中增加三位错
  //   两个随机信号分别负责高16位和第16位
  //   22位信道加扰屏蔽字生成电路，加扰模式引脚00：不加扰  01:1位加扰 10:2位加扰 11：0-2位随机加扰
  //   如果两个信号相同，换一个信号
endmodule

// 随机加扰
module \_17位随机干扰  (
  input  [16:0] \_17位输入 ,
  output [16:0] \随机加扰屏蔽字 ,
  output [16:0] \加扰后数据 
);

  wire clock_1_out;
  wire [4:0] \随机数_2_out , \随机数_3_out , \随机数_out ;
  wire [16:0] or_1_out;
  wire [31:0] decoder_1_out31, decoder_2_out31, decoder_3_out31;

  Clock #(.highDuration(1), .lowDuration(1)) clock_1 (.out(clock_1_out));
  Random #(.width(5), .seed(0), .trigger("rising")) \u_随机数  (.clk(clock_1_out), .out(\随机数_out ));  // open: next, clr
  Decoder #(.select(5), .tristate("false"), .disabled("Z"), .enable("false")) decoder_1 (
    .out0(decoder_1_out31[31]), .out1(decoder_1_out31[30]), .out2(decoder_1_out31[29]),
    .out3(decoder_1_out31[28]), .out4(decoder_1_out31[27]), .out5(decoder_1_out31[26]),
    .out6(decoder_1_out31[25]), .out7(decoder_1_out31[24]), .out8(decoder_1_out31[23]),
    .out9(decoder_1_out31[22]), .out10(decoder_1_out31[21]), .out11(decoder_1_out31[20]),
    .out12(decoder_1_out31[19]), .out13(decoder_1_out31[18]), .out14(decoder_1_out31[17]),
    .out15(decoder_1_out31[16]), .out16(decoder_1_out31[15]), .out17(decoder_1_out31[14]),
    .out18(decoder_1_out31[13]), .out19(decoder_1_out31[12]), .out20(decoder_1_out31[11]),
    .out21(decoder_1_out31[10]), .out22(decoder_1_out31[9]), .out23(decoder_1_out31[8]),
    .out24(decoder_1_out31[7]), .out25(decoder_1_out31[6]), .out26(decoder_1_out31[5]),
    .out27(decoder_1_out31[4]), .out28(decoder_1_out31[3]), .out29(decoder_1_out31[2]),
    .out30(decoder_1_out31[1]), .out31(decoder_1_out31[0]), .sel(\随机数_out ));
  Random #(.width(5), .seed(18), .trigger("rising")) \u_随机数_2  (
    .clk(clock_1_out), .out(\随机数_2_out ));  // open: next, clr
  Decoder #(.select(5), .tristate("false"), .disabled("Z"), .enable("false")) decoder_2 (
    .out0(decoder_2_out31[31]), .out1(decoder_2_out31[30]), .out2(decoder_2_out31[29]),
    .out3(decoder_2_out31[28]), .out4(decoder_2_out31[27]), .out5(decoder_2_out31[26]),
    .out6(decoder_2_out31[25]), .out7(decoder_2_out31[24]), .out8(decoder_2_out31[23]),
    .out9(decoder_2_out31[22]), .out10(decoder_2_out31[21]), .out11(decoder_2_out31[20]),
    .out12(decoder_2_out31[19]), .out13(decoder_2_out31[18]), .out14(decoder_2_out31[17]),
    .out15(decoder_2_out31[16]), .out16(decoder_2_out31[15]), .out17(decoder_2_out31[14]),
    .out18(decoder_2_out31[13]), .out19(decoder_2_out31[12]), .out20(decoder_2_out31[11]),
    .out21(decoder_2_out31[10]), .out22(decoder_2_out31[9]), .out23(decoder_2_out31[8]),
    .out24(decoder_2_out31[7]), .out25(decoder_2_out31[6]), .out26(decoder_2_out31[5]),
    .out27(decoder_2_out31[4]), .out28(decoder_2_out31[3]), .out29(decoder_2_out31[2]),
    .out30(decoder_2_out31[1]), .out31(decoder_2_out31[0]), .sel(\随机数_2_out ));
  Random #(.width(5), .seed(3), .trigger("rising")) \u_随机数_3  (
    .clk(clock_1_out), .out(\随机数_3_out ));  // open: next, clr
  Decoder #(.select(5), .tristate("false"), .disabled("Z"), .enable("false")) decoder_3 (
    .out0(decoder_3_out31[31]), .out1(decoder_3_out31[30]), .out2(decoder_3_out31[29]),
    .out3(decoder_3_out31[28]), .out4(decoder_3_out31[27]), .out5(decoder_3_out31[26]),
    .out6(decoder_3_out31[25]), .out7(decoder_3_out31[24]), .out8(decoder_3_out31[23]),
    .out9(decoder_3_out31[22]), .out10(decoder_3_out31[21]), .out11(decoder_3_out31[20]),
    .out12(decoder_3_out31[19]), .out13(decoder_3_out31[18]), .out14(decoder_3_out31[17]),
    .out15(decoder_3_out31[16]), .out16(decoder_3_out31[15]), .out17(decoder_3_out31[14]),
    .out18(decoder_3_out31[13]), .out19(decoder_3_out31[12]), .out20(decoder_3_out31[11]),
    .out21(decoder_3_out31[10]), .out22(decoder_3_out31[9]), .out23(decoder_3_out31[8]),
    .out24(decoder_3_out31[7]), .out25(decoder_3_out31[6]), .out26(decoder_3_out31[5]),
    .out27(decoder_3_out31[4]), .out28(decoder_3_out31[3]), .out29(decoder_3_out31[2]),
    .out30(decoder_3_out31[1]), .out31(decoder_3_out31[0]), .sel(\随机数_3_out ));
  assign or_1_out = decoder_1_out31[16:0] | decoder_2_out31[16:0];  // OR_Gate or_1, 17 bits wide
  assign \随机加扰屏蔽字  = or_1_out | decoder_3_out31[16:0];  // OR_Gate or_2, 17 bits wide
  assign \加扰后数据  = \随机加扰屏蔽字  ^ \_17位输入 ;  // XOR_Gate xor_1, 17 bits wide
endmodule
// 字库
module \字库  (
  input  [6:0] \区号 ,
  input  [6:0] \位号 ,
  output [31:0] out_3,
  output [31:0] out_4,
  output [31:0] out_5,
  output [31:0] out_6,
  output [31:0] out_7,
  output [31:0] out_8,
  output [31:0] out_9,
  output [31:0] out_10,
  output [31:0] out_11,
  output [31:0] out_12,
  output [31:0] out_13,
  output [31:0] out_14,
  output [31:0] out_15,
  output [31:0] out_16,
  output [31:0] out_17,
  output [31:0] out_18,
  output [31:0] out_19,
  output [31:0] out_20,
  output [31:0] out_21,
  output [31:0] out_22,
  output [31:0] out_23,
  output [31:0] out_24,
  output [31:0] out_25,
  output [31:0] out_26,
  output [31:0] out_27,
  output [31:0] out_28,
  output [31:0] out_29,
  output [31:0] out_30,
  output [31:0] out_31,
  output [31:0] out_32,
  output [31:0] out_33,
  output [31:0] out_34
);

  wire [6:0] multiplier_1_cout, multiplier_1_out, subtractor_1_out;
  wire [13:0] adder_1_out, bit_extender_1_out, subtractor_2_out;

  ROM #(.addrWidth(14), .dataWidth(32), .Select("high")) rom_1 (.addr(subtractor_2_out), .data(out_3));
  ROM #(.addrWidth(14), .dataWidth(32), .Select("high")) rom_2 (.addr(subtractor_2_out), .data(out_4));
  ROM #(.addrWidth(14), .dataWidth(32), .Select("high")) rom_3 (.addr(subtractor_2_out), .data(out_5));
  ROM #(.addrWidth(14), .dataWidth(32), .Select("high")) rom_4 (.addr(subtractor_2_out), .data(out_6));
  ROM #(.addrWidth(14), .dataWidth(32), .Select("high")) rom_5 (.addr(subtractor_2_out), .data(out_7));
  ROM #(.addrWidth(14), .dataWidth(32), .Select("high")) rom_6 (.addr(subtractor_2_out), .data(out_8));
  ROM #(.addrWidth(14), .dataWidth(32), .Select("high")) rom_7 (.addr(subtractor_2_out), .data(out_9));
  ROM #(.addrWidth(14), .dataWidth(32), .Select("high")) rom_8 (.addr(subtractor_2_out), .data(out_10));
  Subtractor #(.width(7)) subtractor_1 (.a(\区号 ), .b(7'b0000001), .out(subtractor_1_out));  // open: bin, bout
  Multiplier #(.width(7)) multiplier_1 (
    .a(subtractor_1_out), .b(7'b1011110), .out(multiplier_1_out), .cout(multiplier_1_cout));  // open: cin
  ROM #(.addrWidth(14), .dataWidth(32), .Select("high")) rom_9 (.addr(subtractor_2_out), .data(out_11));
  ROM #(.addrWidth(14), .dataWidth(32), .Select("high")) rom_10 (.addr(subtractor_2_out), .data(out_12));
  ROM #(.addrWidth(14), .dataWidth(32), .Select("high")) rom_11 (.addr(subtractor_2_out), .data(out_13));
  ROM #(.addrWidth(14), .dataWidth(32), .Select("high")) rom_12 (.addr(subtractor_2_out), .data(out_14));
  ROM #(.addrWidth(14), .dataWidth(32), .Select("high")) rom_13 (.addr(subtractor_2_out), .data(out_15));
  ROM #(.addrWidth(14), .dataWidth(32), .Select("high")) rom_14 (.addr(subtractor_2_out), .data(out_16));
  ROM #(.addrWidth(14), .dataWidth(32), .Select("high")) rom_15 (.addr(subtractor_2_out), .data(out_17));
  ROM #(.addrWidth(14), .dataWidth(32), .Select("high")) rom_16 (.addr(subtractor_2_out), .data(out_18));
  assign bit_extender_1_out = {{7{1'b0}}, \位号 };  // Bit_Extender bit_extender_1
  Adder #(.width(14)) adder_1 (
    .a({multiplier_1_cout, multiplier_1_out}), .b(bit_extender_1_out), .out(adder_1_out));  // open: cin, cout
  ROM #(.addrWidth(14), .dataWidth(32), .Select("high")) rom_17 (.addr(subtractor_2_out), .data(out_19));
  ROM #(.addrWidth(14), .dataWidth(32), .Select("high")) rom_18 (.addr(subtractor_2_out), .data(out_20));
  ROM #(.addrWidth(14), .dataWidth(32), .Select("high")) rom_19 (.addr(subtractor_2_out), .data(out_21));
  ROM #(.addrWidth(14), .dataWidth(32), .Select("high")) rom_20 (.addr(subtractor_2_out), .data(out_22));
  ROM #(.addrWidth(14), .dataWidth(32), .Select("high")) rom_21 (.addr(subtractor_2_out), .data(out_23));
  ROM #(.addrWidth(14), .dataWidth(32), .Select("high")) rom_22 (.addr(subtractor_2_out), .data(out_24));
  ROM #(.addrWidth(14), .dataWidth(32), .Select("high")) rom_23 (.addr(subtractor_2_out), .data(out_25));
  ROM #(.addrWidth(14), .dataWidth(32), .Select("high")) rom_24 (.addr(subtractor_2_out), .data(out_26));
  Subtractor #(.width(14)) subtractor_2 (.a(adder_1_out), .b(14'h1), .out(subtractor_2_out));  // open: bin, bout
  ROM #(.addrWidth(14), .dataWidth(32), .Select("high")) rom_25 (.addr(subtractor_2_out), .data(out_27));
  ROM #(.addrWidth(14), .dataWidth(32), .Select("high")) rom_26 (.addr(subtractor_2_out), .data(out_28));
  ROM #(.addrWidth(14), .dataWidth(32), .Select("high")) rom_27 (.addr(subtractor_2_out), .data(out_29));
  ROM #(.addrWidth(14), .dataWidth(32), .Select("high")) rom_28 (.addr(subtractor_2_out), .data(out_30));
  ROM #(.addrWidth(14), .dataWidth(32), .Select("high")) rom_29 (.addr(subtractor_2_out), .data(out_31));
  ROM #(.addrWidth(14), .dataWidth(32), .Select("high")) rom_30 (.addr(subtractor_2_out), .data(out_32));
  ROM #(.addrWidth(14), .dataWidth(32), .Select("high")) rom_31 (.addr(subtractor_2_out), .data(out_33));
  ROM #(.addrWidth(14), .dataWidth(32), .Select("high")) rom_32 (.addr(subtractor_2_out), .data(out_34));
  DotMatrix #(.inputtype("row"), .matrixcols(32), .matrixrows(32), .persist(0), .dotshape("circle")) dotmatrix_1 (
    .row0(out_3), .row1(out_4), .row2(out_5), .row3(out_6), .row4(out_7), .row5(out_8), .row6(out_9),
    .row7(out_10), .row8(out_11), .row9(out_12), .row10(out_13), .row11(out_14), .row12(out_15),
    .row13(out_16), .row14(out_17), .row15(out_18), .row16(out_19), .row17(out_20), .row18(out_21),
    .row19(out_22), .row20(out_23), .row21(out_24), .row22(out_25), .row23(out_26), .row24(out_27),
    .row25(out_28), .row26(out_29), .row27(out_30), .row28(out_31), .row29(out_32), .row30(out_33),
    .row31(out_34));

  // Other names for the same wires on the sheet: D0[31:0] = out_3; D1[31:0] = out_4; D2[31:0] = out_5;
  //   D3[31:0] = out_6; D4[31:0] = out_7; D5[31:0] = out_8; D6[31:0] = out_9; D7[31:0] = out_10; D8[31:0] = out_11;
  //   D9[31:0] = out_12; D10[31:0] = out_13; D11[31:0] = out_14; D12[31:0] = out_15; D13[31:0] = out_16;
  //   D14[31:0] = out_17; D15[31:0] = out_18; D16[31:0] = out_19; D17[31:0] = out_20; D18[31:0] = out_21;
  //   D19[31:0] = out_22; D20[31:0] = out_23; D21[31:0] = out_24; D22[31:0] = out_25; D23[31:0] = out_26;
  //   D24[31:0] = out_27; D25[31:0] = out_28; D26[31:0] = out_29; D27[31:0] = out_30; D28[31:0] = out_31;
  //   D29[31:0] = out_32; D30[31:0] = out_33; D31[31:0] = out_34

  // Notes on the sheet:
  //   contents of rom_1 (hex, n*v repeats v):
  //   281*0 ffffffff 272*0 60000000 202*0 18000 3c000 0 0 18000 3c000 0 0 18000 3c000 8*0 18000 18000
  //   3c000 3c000 18000 18000 3c000 3c000 18000 18000 3c000 18000 3c000 3c000 18000 3c000 18000 18000
  //   3c000 18000 3c000 3c000 18000 3c000 8*0 4*18000 4*3c000 4*18000 3c000 18000 3c000 3c000 3c000 18000
  //   18000 3c000 18000 3c000 3c000 3c000
  //   contents of rom_2 (hex, n*v repeats v):
  //   150*0 1c000 9*18000 121*0 ffffffff 269*0 10000 0 60000000 60000000 202*0 3c000 3c000 0 0 3c000 3c000
  //   0 0 3c000 3c000 8*0 24*3c000 8*0 24*3c000 587*0 8000 11*0 2000 124*0 8000 28*0 8000 291*0 400000
  //   742*0 1000 189*0 80 822*0 10000 654*0 40000 50*0 20000 64*0 4000 252*0 20000 56*0 40000 51*0 2000
  //   74*0 1000000 18*0 8000 74*0 2000 8*0 800000 400*0 40000 676*0 20 393*0 20000 31*0 2000 547*0 100
  //   58*0 800000 200 1000000 200200 387*0 1000000 5*0 800000 26*0 800000 22*0 8000 22*0 10000 0 8000 10*0
  //   10000 241*0 800000 0 0 1000000 7*0 1000000 1000000 10*0 1000000 9*0 20000 41*0 1000 301*0 20000 18*0
  //   800000 800000
  //   contents of rom_3 (hex, n*v repeats v):
  //   150*0 1ffc00 9*3ffc00 59*0 ff000 26*0 7ff0 0 ffe0000 30*0 10000 109*0 1c0000 144*0 60000006 0
  //   60000006 13*0 40000002 38000 0 60000000 e0000000 15*0 181800 0 0 0 e6000 182*0 3c000 3c000 0 0 3c000
  //   3c000 0 0 3c000 3c000 8*0 24*3c000 8*0 24*3c000 581*0 1800 1801800 8100 3000 60000 c00 c000 383800
  //   7000020 181800 0 e0 0 c200c00 1800000 30000 c06000 1003000 3000 1c000 1000 70000 2000 0 18000 0
  //   600c00 e00800 e00000 3000020 1040300 60000 6007000 6000 181800 3000018 1800000 0 0 3801800 0 8000 0
  //   3006000 2000 6100000 1800000 1800000 3000000 80 0 100800 20000 1800c00 0 3000000 800000 1800 80000
  //   301800 0 8000 30000 1800020 c00000 8 3800040 e00020 1000400 1801800 603000 c000100 30000 60000 1c00
  //   700000 300000 3818000 3803800 1800 18000 3803800 1800 1000c00 6003800 c06000 3000 181000 4000 200000
  //   30000 10 181c00 80 e00000 0 300c000 60000 3006000 1000000 100 181800 3001800 6040020 c00000 1c00
  //   1c3800 60000 102000 c3000 182000 0 2000000 602000 0 180000 c0000 2002000 6000c00 30000 380c00 18000
  //   1003000 1c000 0 8 0 c00 40180 0 70000 4000 0 1801000 1001c00 600 383000 381800 600c000 6004000
  //   c00c000 c0 18000 e000 1800000 400600 600c00 0 1800 c00 c00 200 400 c606000 3000 3000 30 18000 800000
  //   70000 40000 600c200 6000300 4018200 3000 3800000 300000 0 30000 c00800 400800 20 e000 180c000 200
  //   70000 3000 30000 3001000 0 2000 3000000 0 380 60000c0 2000000 c000 400400 c00 101000 10000c0 1001800
  //   3001800 1c00 4003300 e00e00 3801b80 3000c00 1800c00 c03000 30000 c00600 c00 1900 30100 0 0 3001000
  //   60000 3000 1000800 1c00 0 30000 1c000 3803000 c00000 2000000 3003000 1c00 603800 1c001c0 3000 1c0 20
  //   0 1e0 1c000 183000 1c1c00 300000 20000 c0 3000 6020000 6006000 1000c00 301800 800800 18000 6000
  //   183000 2000000 3000300 3806300 c3000 181800 0 c01800 1800000 0 0 0 c0 3000000 0 101800 301c00 1c000
  //   1800 1018300 38000 6000 800400 2000 3000020 202000 100180 380c000 3803000 30080c0 2004000 8000 1800
  //   3001800 30000 6000000 c00000 100 0 3000000 18000 18200 800000 1803000 0 0 600700 1800000 0 400000
  //   c00000 1800800 2000600 600000 30000 40000 60c080 1c00 3000800 60000 1000800 2020080 1380030 1040000
  //   40100 2010000 0 0 18000 1000080 6001800 0 3000 c00c00 2000180 3000c00 3000 600 3000000 8000 0 380
  //   100000 400000 0 c00 0 0 c00 100000 6000 c000 3001800 0 8000000 0 0 c00 300 1c000 403000 0 1c000
  //   3000000 180 3800000 60000 1800 18000 1c000 70000 3000800 10 1c00 c00 100000 1c00 1c00c00 0 800000 0
  //   0 60000 3000000 10000 7000000 10 c180 180 3000400 8000400 1800 600e00 400 800 18000 3006000 1800200
  //   0 3800c00 0 30000 3006000 601000 c00000 1800 18000 c000 38000 2003000 18000 0 400000 6000 1002000
  //   3000000 2000040 100 70000 3807000 800 0 6000 1800 70000 600 1800 c000 101000 c0 3200 1800 200c00
  //   18000 0 3800 300010 0 c000 80 181800 30000 200000 401000 201800 4000 1c00000 30c0 1c00800 c00000
  //   1800 1801800 30000 1000800 18000 c01c00 6000 c000 1803000 6000 60 1c001c0 70000 1800 8080 2000000
  //   1000080 300c300 3001000 200e100 1008100 4003000 1801800 6000 800000 38000 0 0 806000 300c00 418400
  //   c00 600000 e1ee00 408000 c03800 3000 30000 1800 1000000 800100 600c00 60000 3810180 0 0 1800000 0
  //   2020180 0 0 10180 20 10000 1000800 18000 181800 3801800 0 3003000 30 1800000 e0000 3000c00 100 10
  //   100010 2001800 8060180 c000 1001800 400000 c01800 0 1000000 0 1800c00 0 4100 0 2000000 c00000 e000
  //   1000 1800 800800 1000 8000 20020 3003000 1000000 30000 1800 381c00 1801800 30000 400c00 20100 3000
  //   e00000 1001000 1000 6600 38000 c6000 1800800 c03000 30000 400000 600000 18000 6001800 300c00 6000 0
  //   0 0 100 0 0 3001800 0 1000 0 c00 181800 1880 3001840 1000 3180 200 0 0 0 2000000 8 200 3001800 20000
  //   0 100 30000 80000 183800 300c700 800 3801000 1800000 6000000 2000 8000000 10000 1800100 1000 1c00 0
  //   0 c000 600000 600000 38000 1801c00 800 3000 3000 3000 1800 1800000 3001800 800 18000 2000 1800800
  //   c00 3000000 6002000 40000 300000 1000000 2000c00 400c00 1000 0 20300c0 1000 8080 c00e00 1800008 0
  //   3000c00 180 c0 3000000 1000 18000 30000 2000000 e00000 0 0 c00 0 3007000 3000 600 200 200600 1800c00
  //   1800008 8600 3000700 0 0 1000000 0 0 6000200 4*0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
  //   contents of rom_4 (hex, n*v repeats v):
  //   11*0 c3000 5*0 40 2000000 10 8000000 80 0 1ff0 100000 1ff0 f80000 1fff0 fff8000 1ffe0 7ff0000 18*0
  //   800 3800 13*0 10000 18000 0 c00000 c20000 0 18000 0 0 0 400 3e000 0 10000 10000 13*0 18000 57*0
  //   10*f00f00 34*0 c00000 24*0 3ffe00 26*0 7ff0 1800000 ffe0000 0 0 300 26*0 1c0 18000 3c00000 49*0 1c0
  //   57*0 80000 1e0380 0 0 0 180 11*0 70 11*0 20000 0 0 18000 0 0 80 0 0 0 3c0 0 0 1e0 5*0 c0 18*0 6000 0
  //   0 0 e0000 74*0 3800001c 0 7000000e 13*0 60000006 38000 0 60000000 e0000000 15*0 1c1c00 0 0 0 e7000
  //   104*0 200000 18180000 6000000 13*0 60000 0 0 300000 0 0 6000 6*0 30000 3000 0 0 0 20000 0 300 0
  //   38000 3000 0 0 30000 0 0 2000000 60000 31*0 3c000 3c000 0 0 3c000 3c000 0 0 3c000 3c000 8*0 24*3c000
  //   8*0 24*3c000 579*0 218008 30600008 3801c00 1c01c00 e380 3800 38000 1800e00 6000 383010 78001f0
  //   1c1c00 18030 1ff0 2301c0 e380600 3c00000 18000 e07000 3c01800 1800 301e000 1800 38000 8103000
  //   3ffff80 1c000 0 700e00 e00e00 e00000 18000f0 1ce0700 70000 7007000 800e000 1c1c00 380001c 1c00700
  //   600 0 3803c00 2000 e000 0 3807200 3800 7180000 1c00000 1c00000 3800000 3ffffc0 6000060 380f00 38000
  //   1c00e00 10 3840010 1e00000 83c00 3c0000 f83800 60000 e000 3038000 1c000e0 c04080 41fffc 38001e0
  //   e00070 1c00600 1c01c00 703800 6000180 38000 70000 1801c00 601008 300010 3818000 3801c00 8200c00
  //   3018000 3803800 e00 1c00e00 7001c00 e03800 8003800 1c3800 7000 780000 18000 1001c 1c1c00 3ffffc0
  //   e40040 e40080 780f000 38000 380f000 1c30060 1ffff80 3c3800 3801c00 70ffff0 e00000 1c00 1c3800 70000
  //   3c3800 c3810 1c3800 800080 3800000 f03000 180000 1c0000 1e0200 3803800 3000c00 38000 380e00 1c000
  //   3c03800 381c060 1800008 18 18 10230c30 c0301c0 8000030 60200 6007000 c018808 1c01c00 1801c00 600
  //   383800 381c00 700e000 700e000 e00e000 fe0 c000 7000 1c00000 700700 8710e00 c0000 e00 e00 8040600
  //   8000380 10270700 e706000 6003800 1801c00 800f0 1c000 e00008 38000 70000 300e380 3000380 701c380
  //   c003800 3800000 380000 8 38000 8e60c00 8720c00 4010038 7000 1c0e000 4000380 18060008 c001800 18000
  //   3801c00 700 10003800 3800000 10 1f80 70180e0 3800000 e000 300e00 c00 1c1c00 18007e0 1c01c00 7801c00
  //   c001c00 70039c0 e00e00 3801dc0 3800e00 1c01e00 f03c00 30000 e00700 8000e00 c201cc0 18030180 4001c00
  //   180070 3801d00 70000 3b00 1801c00 3801c00 18 38000 1c000 3803800 600000 7807000 3801800 301c00
  //   703c00 1e001e0 3800 100c01c0 1f0 f0 7ff0 fe030 183800 181c00 380000 70000 7ffffe0 3800 7070008
  //   7007000 1c00e00 381c00 e01e00 3c000 c007000 1c3000 7020100 3000380 3007380 c3800 1c1c00 4000008
  //   e01c00 1c00018 2040040 c202038 6000060 c0e0 38000e0 80 381c00 381c00 1c000 1c00 381c380 1c000 c2000
  //   600f00 8003800 38000e0 303800 3801c0 380e000 3807000 38060e0 700e000 601c000 1000c00 3800e00 38000
  //   3000000 e00018 ffff80 180000 3800180 1c100 c18300 e00300 1e03800 c1000c0 18 700700 1c00040 20020
  //   700000 e00000 1c00e00 3800700 700000 30400 18060000 70e1c0 1e00 3800e00 f0000 1c00e00 30301c0
  //   1b80038 3870000 8060180 3018000 4000030 20 1c000 1ffffc0 7001c00 c000000 10203800 e00e00 18001c0
  //   3800e00 383800 3800680 3004840 e600 1800100 7fc0 790010 e00020 c004840 6000ec0 300 c0600c0 e00
  //   380000 7000 e000 3801c00 6061000 e003800 4000000 1c00 e00 380 1c000 603800 0 1c000 3800000 7c0
  //   3c00000 30000 1c00 1c000 301c060 38000 3800e00 301c 1e00 18180e00 7a0008 381e00 1c01e00 71c000
  //   1e00008 6180 0 70000 1c00000 1c000 7000000 6000038 e180 60001c0 7806700 c000700 10203800 700e00 700
  //   1c01c00 38030 3803800 1c00380 c00c00 3c00e00 1c00070 1c000 3806000 701c00 e06040 1c00 18000 e000
  //   1c000 3801800 1c000 1800000 f00018 7800 1c07800 38000e0 38001e0 1f80 78000 3007800 e00 30 8007000
  //   3801c00 70040 c0c700 3801c00 6000 1c1c00 80e0 3303b00 180c00 380e00 c01c000 c000010 383c00 300038
  //   10118030 1800f000 880e0 1c1c00 38000 380000 701c00 701c00 f000 1c00000 38c0 1c01c00 e00040 10300c00
  //   1c03c00 18000 3800e00 301c040 1ec1c00 7000 e000 1c01800 3000 ffe7ff0 1e001c0 78000 1c00 c1c0 383ffe0
  //   38081c0 380e380 3801c00 380e380 381c380 6003800 1c01c00 7000 1c00000 38000 1ffff80 10 e07000 380e80
  //   71c700 e00 706000 f0c780 e0ee00 1e03800 c003800 78000 41c00 1c00000 ffff00 300e00 3070000 381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
  //   contents of rom_5 (hex, n*v repeats v):
  //   8*0 40000 0 0 c3000 0 20 3c00000 1820 3c70000 e0 6000000 30 18000000 198 19800000 1800 100000 1830
  //   d80000 1ffe0 7ff8000 1ffc0 7ff0000 18000 0 0 0 18000 12*0 7e000 3c00 7c00 6*0 30000 c000 10 4000000
  //   0 0 0 18000 ff000 800000 1c00000 1c70000 2000000 18000 18000018 0 c000 7000c00 ff800 0 18000 18000
  //   3c000 7e000 7e000 18000 18000 0 0 18000 18000 0 0 0 18000 18000 3ffffff8 18000 301c00 4008060
  //   3000000 0 180 820 8000 2000000 7*0 4000 1c000 c000 0 c0e00 0 0 8000 0 1000 0 1000 0 0 10300 0 1ff00
  //   3000 0 1c01000 7*1000080 1000180 12*1000080 1c00180 9*1c00380 0 0 10*1000080 0 0 1ff800 1fe7fc0
  //   7fdffbfe 1fffc0fc 7f81fe0 7fc1fffc 7f07fffe 7e0ffffe 3fffc1fc 7fc1fc0 1fe0fffc 7f83fffe 7*0 1f8000
  //   1c00000 20 4000000 5*0 c00 16*0 f80700 26*0 7000 c00000 e0000 18000 0 700 9*0 38000 16*0 780 18000
  //   e00000 0 30000 70000 0 0 0 80000 18*0 1c000 30000 0 0 0 e000 0 0 c0000 180000 0 0 180 0 0 0 80000 0
  //   0 0 300000 0 0 180 260 12*0 30000 19*0 10000 14*0 c000 3000 0 20000 4*0 c000 0 e0000 e0980 70000
  //   601c0 40000 1800c0 0 c0 7000 6040 0 0 0 180 0 300 600 38 38000 100 7000 6000 0 e0400 30 c00 30 e0000
  //   0 38000 0 0 1e000 2000 0 60 0 300000 0 240 0 60 120 0 100 200 18000 40180 1e0 0 f0000 30000 3000 c00
  //   0 780000 6*0 18000 0 0 0 c00 7000 0 c00 3c0000 700c0 18000 e0000 41*0 10000 0 7f000 28*0 1e000078 0
  //   3000000c 13*0 3000000c 38000 0 60000000 60000000 15*0 181c00 0 0 0 7e000 104*0 600000 c300000
  //   7000000 12*0 300000 70000 0 0 380000 60000 3000 7000 100400 0 0 3800 10000 0 38000 3000 400 0 200
  //   38000 18000 300 0 1c000 c03c00 7f0 0 38000 0 7c00 3800000 78000 60000 c000 70000 300 27*0 3c000
  //   3c000 0 0 3c000 3c000 0 0 3c000 3c000 8*0 24*3c000 8*0 24*3c000 579*0 3ffffc 3ff3fffc 3803800
  //   1803800 c380 7000 1c000 3800c00 7010 383038 7003ff0 181c00 dfff8 7ffff0 1ff181c0 c300700 3800020
  //   1c000 c0e000 3801c00 1c00 381c070 1fe00c00 18000 ff81c00 3ffffc0 18000 10 600e00 e10c00 c00000
  //   1c007f0 38e0700 40000 7006000 600c000 181800 38c1018 1c08600 8600 60 3023810 103000 6000 0 3806380
  //   8183300 6184010 1800010 1818030 383fff0 18000 7fffff0 7003c0 78000 1800c00 1ffffff8 387fff8 1c00018
  //   1ffc3800 1fc0018 7f83000 330018 30c008 3030420 18003f0 1807fc0 221fffc 3800ff0 18c003f0 1804600
  //   1801800 e03000 70030c0 38000 60000 1c01c20 601ffc 309ff8 3018618 3000c00 1ff00e08 3818010 3803000
  //   100e10 1800c00 7000c00 1c01800 6001c10 1c3800 c10e000 700000 1c018 fff8018 181c08 3ffffc0 c7ffe0
  //   e7ffc0 700e000 38000 300e000 183fff0 1c00180 703800 3003800 70e0060 c00018 181800 1c3000 c0000
  //   383800 c3ff8 1c3070 ffffc0 383fff0 e01800 101d0018 380200 1fff00 3801800 3800c00 30000 380c00 18000
  //   3803800 381c070 38ff7fc 1ffffffc 3ffffffc 1ff30c38 7018380 c1ffff8 ffff00 7007000 fffcffc 3803808
  //   3c01800 60c00 383818 381808 700e000 600e060 e00e060 1ffe0 e000 3008 e00030 10620e00 e638c00 60300
  //   c040600 c040600 ffe0610 e10c180 1ff60600 c60e008 3003000 3800c00 1ffc0ff8 c000 1e0001c 1c008 38000
  //   380c180 3860180 3018180 6001800 3800070 304030 1feffffc 38000 ee71c00 c671c00 7ff8038 3008 180c030
  //   6000340 c06001c 6081800 1c000 3000c00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
  //   contents of rom_6 (hex, n*v repeats v):
  //   4*0 1ff800 300c00 181800 0 70000 0 0 c3000 0 c0 3c00000 20c0 3cf8000 1c0 3000000 30 c000000 1b0
  //   18c00000 1800 100000 1bf0 d80000 180c0 3018000 1ffc0 3ff0000 18000 0 0 0 18000 c000030 7ffff80
  //   1ffffff8 4*0 180 18000 8060 0 0 3ffc00 6e00 ce00 5*0 300 30000 c000 70 7800000 0 0 0 18000 1e7800
  //   7e00000 1c0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
  //   contents of rom_7 (hex, n*v repeats v):
  //   4*0 3ffc00 1c3800 3c3c00 0 60000 0 0 c3000 0 180 3c00000 6180 3cf8000 180 1800000 60 c000000 330
  //   cc00000 1800 100000 1be0 d80000 18180 1818000 1ff80 1ff0000 18000 80 38000 18000 3c000 c000030
  //   3ffff80 ffffff0 0 3c000 0 1800180 180 18000 c060 18 0 780e00 ce00 cc00 5*0 300 30000 c000 3e0
  //   3e00000 0 1c00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
  //   contents of rom_8 (hex, n*v repeats v):
  //   5*0 77000 3c3c00 0 60000 0 0 c3000 0 180 3c00000 c180 3c78000 300 c00000 60 6000000 320 c600000 1800
  //   100000 1a00 d80000 18180 1c18000 1ff00 ff0000 18000 30001c0 7c000 3c000 3c000 6000060 3800380
  //   1c00380 1800180 1ff800 0 3c003c0 180 18000 180c0 70 0 1c00300 c000 c000 5*0 600 30000 c000 1f00
  //   7c0000 0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
  //   contents of rom_9 (hex, n*v repeats v):
  //   5*0 3c000 181800 0 c0000 0 0 c3000 0 300 c00000 1c300 c30000 600 600000 c0 6000000 660 6600000 1800
  //   100000 1a00 d80000 18300 c18000 1ff00 ff0000 18000 1800380 7c000 7e000 66000 6000060 1c00080 1c00380
  //   1800180 7ffe00 3fffc0 3e007c0 300 18000 380c0 e0 7e000 3800180 c000 c000 0 1800f80 0 0 0 c00 30038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
  //   contents of rom_10 (hex, n*v repeats v):
  //   5*0 18000 0 0 c0300 0 0 c3000 0 3c0 1800000 1e3c0 1830000 400 600000 c0 3000000 660 6300000 1800
  //   100000 1a00 d80000 18600 618000 1fe00 7f0000 18000 c00700 7c000 3c000 66000 30000c0 e000c0 1c00380
  //   1800180 e00700 7fffc0 3e007c0 300 18000 30180 1c0 3ffc00 30000c0 18000 1c000 0 7803fe0 0 0 0 c00
  //   301f0 f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
  //   contents of rom_11 (hex, n*v repeats v):
  //   8*0 187f80 0 0 c3000 0 7c0 1000000 1f7c0 1060000 400 600000 180 3000000 cc0 3300000 1800 100000 1a00
  //   d80000 18600 618000 1fc00 7f0000 18000 600e00 38000 3c000 63000 30000c0 e00040 1c00380 1800180
  //   c00300 e00000 3c003c0 300 18000 60180 380 f00f00 6000060 18000 1c000 ffffff0 e007070 f00000 0 0 1800
  //   30f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
  //   contents of rom_12 (hex, n*v repeats v):
  //   7*0 31c00 1ff700 0 0 c3000 0 3c0 2000000 1f3c0 20c0000 400 600000 180 1800000 cc0 3180000 1800
  //   100000 1a00 d80000 18c00 318000 1fc00 3f0000 18000 301c00 0 0 c3000 1800180 700000 1c00380 1800180
  //   1c00380 1800000 800100 600 18000 60300 700 1c00380 e000060 18000 1c000 1ffffff8 c00c030 3fc0000
  //   800700 f00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
  //   contents of rom_13 (hex, n*v repeats v):
  //   7*0 71c00 360600 0 0 c3000 0 3c0 4000000 1e3c0 4180000 400 600000 300 1800000 1980 1980000 1800
  //   100000 1a00 d80000 18c00 318000 1fc00 3f0000 18000 183800 0 0 c1800 1800180 780000 1c00380 1800180
  //   1800180 3800000 0 600 18000 c0300 e00 38001c0 c000030 18000 7f000 0 1c018038 70f0018 7803fc0 3fc07f0
  //   1fff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
  //   contents of rom_14 (hex, n*v repeats v):
  //   0 0 0 3c000 0 0 0 73800 200600 0 1e00000 c3000 0 80 0 4080 0 400 600000 300 c00000 1980 18c0000 1800
  //   100000 1a00 d80000 18800 318000 1f800 3f0000 18000 c7000 0 0 181800 c00300 380000 1c00380 1800180
  //   1800180 3000000 0 600 18000 c0600 1c00 60000e0 c000030 18000 fb800 0 1c030038 c03c030 e0070e0
  //   70f1e00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
  //   contents of rom_15 (hex, n*v repeats v):
  //   0 0 0 7e000 0 0 0 63800 400c00 0 7f80008 c3000 e03c070 4*0 400 600000 600 c00000 3300 cc0000 1800
  //   100000 1a00 d80000 19800 118000 1f800 3f0000 7ffffe0 6e000 0 0 181800 c00300 1c0000 1c00380 1800180
  //   1800180 3000000 0 c00 18000 180600 3800 e000070 1c038030 18000 198c00 0 c070030 1800f0e0 c00c030
  //   c03b0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
  //   contents of rom_16 (hex, n*v repeats v):
  //   0 0 0 ff000 0 0 0 e3000 800c00 0 e1f0018 c3000 1f07c0f8 4*0 400 600000 600 600000 3300 c60000 1800
  //   100000 1a00 d80000 19800 198000 1f800 3f0000 7ffffe0 3c000 0 0 300c00 600600 1e0000 1c00380 1800180
  //   1800180 3ffff80 0 c00 18000 180c00 6000 c000030 1807c030 18000 198c00 0 e0e0070 3fc0 1801c030
  //   1801e00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
  //   contents of rom_17 (hex, n*v repeats v):
  //   0 0 0 ff000 0 0 0 c7000 1800 ffffffff 1803e030 c3000 1f07e1f8 4*0 400 600000 c00 600000 6600 460000
  //   1800 100000 1a00 d80000 19800 198000 1f800 3f0000 18000 38000 ffffff0 0 300c00 600600 e0000 1c00380
  //   1800180 1800180 3ffffc0 0 c00 18000 301c00 c000 18000018 1807e038 18000 198c00 1ffffff8 7fc01e0 f00f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
  //   contents of rom_18 (hex, n*v repeats v):
  //   0 0 0 ff000 0 0 0 c6000 1000 0 10007fe0 c3000 1f07c0f8 4*0 400 600000 600 600000 3300 c60000 1800
  //   100000 1a00 d80000 19800 198000 1f800 3f0000 18000 3c000 7ffffe0 0 600600 300c00 70000 1c00380
  //   1800180 1800180 3ffff80 0 1800 18000 301800 18000 18000018 1807c030 18000 198c00 0 1f00180 3fc0000
  //   1c030030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
  //   contents of rom_19 (hex, n*v repeats v):
  //   0 0 0 fe000 0 0 0 186000 3000 0 20000fc0 c3000 e03c0f0 4*0 400 600000 600 c00000 3300 cc0000 1800
  //   100000 1a00 d80000 19800 118000 1f800 3f0000 18000 6e000 0 0 600600 300c00 60000 1c00380 1800180
  //   1800180 3000000 0 181800 18000 603800 30000 10000008 1c03c030 18000 199c00 0 0 70f0018 c0e0070
  //   e03b800 30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
  //   contents of rom_20 (hex, n*v repeats v):
  //   0 0 0 7e000 0 0 0 18c000 42000 0 100 c3000 5*0 400 600000 300 c00000 3180 18c0000 1800 100000 1a00
  //   d80000 18800 318000 1f800 3f0000 18000 c7000 0 0 c00300 181c00 c0000 1c00380 1800180 1800180 3000000
  //   0 3c1800 18000 603000 60000 0 c000030 18000 db800 0 0 c03c030 7bc01e0 7ff1ff0 1ffffff0 3f0000 f800 1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
  //   contents of rom_21 (hex, n*v repeats v):
  //   7*0 10c000 36000 0 0 c3000 5*0 400 600000 300 1800000 1980 1980000 1800 100000 1a00 d80000 18c00
  //   318000 1fc00 3f0000 18000 183800 0 0 c00300 181800 180000 1c00380 1800180 1800180 3800000 0 6e3000
  //   18000 c06000 c0000 0 c000030 18000 7f000 0 1ffffff8 1800f0e0 3f803c0 3fc07e0 1ffffff0 7e000 7c000
  //   f8001f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
  //   contents of rom_22 (hex, n*v repeats v):
  //   0 1c000000 3c00000 4*0 308000 1c000 0 0 c3000 5*0 400 600000 180 1800000 18c0 3180000 1800 100000
  //   1a00 d80000 18c00 218000 1fc00 7f0000 18000 301c00 0 0 1800180 c3800 380000 1c00380 1800300 1800180
  //   1800000 0 73000 18000 c06000 180000 0 c000070 18000 3c000 1ffffff8 ffffff0 3fc0 0 0 c0000 3fc00
  //   3ec000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
  //   contents of rom_23 (hex, n*v repeats v):
  //   0 f000000 7e00000 4*0 200000 e000 0 0 c3000 5*0 400 600000 180 3000000 cc0 3300000 1800 100000 1a00
  //   d80000 18600 618000 1fc00 7f0000 18000 600e00 38000 38000 1800180 c3000 300000 1c00380 c00300
  //   1800180 e00000 3c003c0 73000 18000 180c000 300000 0 6000060 18000 18000 ffffff0 0 f00 0 0 180000
  //   31f80 1f0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
  //   contents of rom_24 (hex, n*v repeats v):
  //   0 3c00000 c200000 5*0 7000 0 0 c3000 5*0 400 600000 c0 3000000 c60 6300000 1800 100000 1a00 d80000
  //   18600 e18000 1fe00 7f0000 18000 c00700 7c000 7c000 1000180 67000 600040 1c00380 e00600 1800180
  //   7fff80 3c007c0 3f000 18000 180c000 600000 0 70000e0 38000 18000 5*0 300000 303f0 f80c000 fc000 3f000
  //   0 7e0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
  //   contents of rom_25 (hex, n*v repeats v):
  //   0 1e00000 c300000 5*0 7800 0 0 c3000 5*0 400 600000 c0 6000000 660 6600000 1800 100000 1a00 d80000
  //   18300 c18000 1fe00 ff0000 18000 1800380 7c000 7c000 30000c0 66000 c000c0 1c00380 7c3c00 1800180
  //   3fffc0 7e007c0 1e000 18000 3018000 c00000 0 38001c0 30000 18000 5*0 300000 30078 1e00c000 1f800
  //   f8000 0 7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
  //   contents of rom_26 (hex, n*v repeats v):
  //   0 e00000 c300000 5*0 3800 0 0 c3000 5*0 600 c00000 60 6000000 660 c600000 1800 100000 1a00 d80000
  //   18300 1818000 1ff00 1ff0000 0 30001c0 7c000 3c000 30000c0 3e000 1c00180 1c00380 1ff800 1800180 0
  //   3c007c0 e000 18000 7018000 3800000 0 1c00380 30000 30000 0 ffffff0 0 0 0 600000 30000 c000 3f00
  //   7c0000 0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
  //   contents of rom_27 (hex, n*v repeats v):
  //   0 e00000 6600000 5*0 1000 0 0 c3000 5*0 300 1800000 60 c000000 330 cc00000 1800 100000 1a00 fd80000
  //   18180 3818000 1ff80 1ff0000 0 80 38000 38000 6000060 3c000 1ffff80 1c00380 7c000 1800180 0 1800380
  //   e000 18000 6030000 7000000 0 f00f00 330000 3b0000 0 ffffff0 0 0 0 c00000 30000 c000 7e0 3e00000 0
  //   3c0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
  //   contents of rom_28 (hex, n*v repeats v):
  //   0 600000 3c00000 8*0 c3000 5*0 180 3000000 60 c000000 330 18c00000 1800 100000 1a00 fd80000 180c0
  //   3018000 1ff80 3ff0000 7ffffe0 0 0 0 6000060 1c000 3ffff80 ff01ff0 4*0 4000 ffffff0 6030000 fffffe0 0
  //   3ffc00 330000 3f0000 5*0 400000 30000 c000 f0 7000000 0 0 0 1ff800 18000 0 0 0 1fc00 dff800 c1ff830
  //   1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
  //   contents of rom_29 (hex, n*v repeats v):
  //   0 600000 1000000 8*0 c3000 5*0 c0 6000000 30 18000000 198 19800000 1800 100000 1a00 c180000 18060
  //   7ff8000 1ffc0 7ff0000 7ffffe0 0 0 0 c000030 18000 7ffff80 ff01ff0 9*0 ff000 3e0000 3e0000 6*0 30000
  //   c000 10 4*0 fe000 18000 4*0 7e000 18018010 0 0 3c0f0 1c7000 0 1800180 1800180 7e000 3c000 3c000
  //   18000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
  //   contents of rom_30 (hex, n*v repeats v):
  //   11*0 c3000 5*0 40 0 10 8000000 108 10800000 1800 ff00000 1e00 ff80000 1fff0 fff8000 1ffe0 7ff0000
  //   4*0 20 8000 12*0 80000 14*0 18000 5*0 18000 4*0 fe000 0 1000080 1000080 12*0 18000 58*0 f00700
  //   9*e00f00 39*0 8000000 0 0 200000 11*0 3000000 4*0 1ffc00 16*0 700 9*0 7ff0 380 7fe0000 9*0 3ff800 0
  //   0 ff000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
  //   contents of rom_31 (hex, n*v repeats v):
  //   24*0 7f00000 e00 7f00000 0 0 ffe0 7fe0000 119*0 10*3ffc00 54*0 6000000 4*0 3c000 26*0 7ff0 0 ffe0000
  //   9*0 1fe000 0 0 7e0000 5*0 7e0000 7f00 7*0 3c0000 0 0 10000 271*0 38000 0 60000000 70000000 77*0
  //   300000 56*0 38700000 22*0 80000 44*0 3c000 3c000 0 0 3c000 3c000 0 0 10*3c000 8*0 24*3c000 8*0
  //   16*3c000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
  //   contents of rom_32 (hex, n*v repeats v):
  //   150*0 10*7e000 88*0 7fc0000 0 ffffffff 16*0 7e0000 3e00 282*0 10000 0 60000000 70000000 134*0
  //   1fe00000 67*0 3c000 3c000 0 0 3c000 3c000 0 0 10*3c000 8*0 24*3c000 8*0 16*3c000 25*0 3c00 fc0ffff
  //   556*0 1000000 11*0 4 17*0 800000 800000 10*0 80000 4*0 400000 29*0 200000 20*0 20000 0 0 2000 19*0
  //   40000 22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
endmodule

module \_22位流水接口  (
  input  [21:0] Din22,
  input  \传输状态In_表明当前传输数据有效 ,
  input  CLK,
  input  \同步清零_气泡_高电平有效 ,
  input  \使能端_低电平有效_stall_高电平有效 ,
  output [21:0] Dout22,
  output \传输状态Out_表明当前传输数据有效 
);

  wire multiplexer_2_out, pull_resistor_2_node;
  wire [21:0] multiplexer_1_out;

  Multiplexer #(.select(1), .width(22), .disabled("Z"), .enable("false")) multiplexer_1 (
    .in0(Din22), .in1({22{1'b0}}), .out(multiplexer_1_out), .sel(\同步清零_气泡_高电平有效 ));
  Multiplexer #(.select(1), .width(1), .disabled("Z"), .enable("false")) multiplexer_2 (
    .in0(\传输状态In_表明当前传输数据有效 ), .in1(1'b0), .out(multiplexer_2_out), .sel(\同步清零_气泡_高电平有效 ));
  Pull_Resistor #(.pull(0)) pull_resistor_1 (.node(\同步清零_气泡_高电平有效 ));
  Register #(.width(22), .trigger("rising"), .Select("low")) register_1 (
    .D(multiplexer_1_out), .en(pull_resistor_2_node), .Q(Dout22), .clk(CLK));  // open: clr
  Register #(.width(1), .trigger("rising"), .Select("low")) register_2 (
    .D(multiplexer_2_out), .en(pull_resistor_2_node), .Q(\传输状态Out_表明当前传输数据有效 ), .clk(CLK));  // open: clr
  Pull_Resistor #(.pull(0)) pull_resistor_2 (.node(pull_resistor_2_node));
  not not_1 (pull_resistor_2_node, \使能端_低电平有效_stall_高电平有效 );

  // Notes on the sheet:
  //   使能端_低电平有效_stall_高电平有效: pull=down
  //   同步清零_气泡_高电平有效: pull=down
endmodule

module \_16位流水接口  (
  input  [15:0] Din16,
  input  \传输状态In_表明当前传输数据有效 ,
  input  CLK,
  input  \同步清零_气泡_高电平有效 ,
  input  \使能端_低电平有效_stall_高电平有效 ,
  output [15:0] Dout16,
  output \传输状态Out_表明当前传输数据有效 
);

  wire multiplexer_2_out, pull_resistor_2_node;
  wire [15:0] multiplexer_1_out;

  Multiplexer #(.select(1), .width(16), .disabled("Z"), .enable("false")) multiplexer_1 (
    .in0(Din16), .in1({16{1'b0}}), .out(multiplexer_1_out), .sel(\同步清零_气泡_高电平有效 ));
  Multiplexer #(.select(1), .width(1), .disabled("Z"), .enable("false")) multiplexer_2 (
    .in0(\传输状态In_表明当前传输数据有效 ), .in1(1'b0), .out(multiplexer_2_out), .sel(\同步清零_气泡_高电平有效 ));
  Pull_Resistor #(.pull(0)) pull_resistor_1 (.node(\同步清零_气泡_高电平有效 ));
  Register #(.width(16), .trigger("rising"), .Select("low")) register_1 (
    .D(multiplexer_1_out), .en(pull_resistor_2_node), .Q(Dout16), .clk(CLK));  // open: clr
  Register #(.width(1), .trigger("rising"), .Select("low")) register_2 (
    .D(multiplexer_2_out), .en(pull_resistor_2_node), .Q(\传输状态Out_表明当前传输数据有效 ), .clk(CLK));  // open: clr
  Pull_Resistor #(.pull(0)) pull_resistor_2 (.node(pull_resistor_2_node));
  not not_1 (pull_resistor_2_node, \使能端_低电平有效_stall_高电平有效 );
endmodule

module \流水模拟  (
);

  wire button_1_out, \时钟_out ;
  wire [15:0] counter_1_q, \n16位流水接口_1_dout16 , \n16位流水接口_2_dout16 , \n16位流水接口_3_dout16 ,
       \n16位流水接口_4_dout16 , \组合逻辑_1_out_2 , \组合逻辑_2_out_2 , \组合逻辑_3_out_2 ;

  Clock #(.highDuration(1), .lowDuration(1)) \u_时钟  (.out(\时钟_out ));
  Counter #(.width(16), .max('hffff), .ongoal("wrap"), .trigger("rising"), .behavior("old")) counter_1 (
    .Q(counter_1_q), .clk(\时钟_out ), .clr(button_1_out));  // open: load, D, count, carry, preset
  Button button_1 (.out(button_1_out));
  // Probe on counter_1_q
  \_16位流水接口  \u_16位流水接口_1  (
    .Din16(counter_1_q), .CLK(\时钟_out ), .Dout16(\n16位流水接口_1_dout16 ));  // open: 传输状态In_表明当前传输数据有效, 传输状态Out_表明当前传输数据有效, 同步清零_气泡_高电平有效, 使能端_低电平有效_stall_高电平有效
  // Probe on \n16位流水接口_1_dout16 
  \_16位流水接口  \u_16位流水接口_2  (
    .Din16(\组合逻辑_1_out_2 ), .CLK(\时钟_out ), .Dout16(\n16位流水接口_2_dout16 ));  // open: 传输状态In_表明当前传输数据有效, 传输状态Out_表明当前传输数据有效, 同步清零_气泡_高电平有效, 使能端_低电平有效_stall_高电平有效
  \组合逻辑  \u_组合逻辑_1  (.in_1(\n16位流水接口_1_dout16 ), .out_2(\组合逻辑_1_out_2 ));
  // Probe on \n16位流水接口_2_dout16 
  \组合逻辑  \u_组合逻辑_2  (.in_1(\n16位流水接口_2_dout16 ), .out_2(\组合逻辑_2_out_2 ));
  \_16位流水接口  \u_16位流水接口_3  (
    .Din16(\组合逻辑_2_out_2 ), .CLK(\时钟_out ), .Dout16(\n16位流水接口_3_dout16 ));  // open: 传输状态In_表明当前传输数据有效, 传输状态Out_表明当前传输数据有效, 同步清零_气泡_高电平有效, 使能端_低电平有效_stall_高电平有效
  // Probe on \n16位流水接口_3_dout16 
  \组合逻辑  \u_组合逻辑_3  (.in_1(\n16位流水接口_3_dout16 ), .out_2(\组合逻辑_3_out_2 ));
  \_16位流水接口  \u_16位流水接口_4  (
    .Din16(\组合逻辑_3_out_2 ), .CLK(\时钟_out ), .Dout16(\n16位流水接口_4_dout16 ));  // open: 传输状态In_表明当前传输数据有效, 传输状态Out_表明当前传输数据有效, 同步清零_气泡_高电平有效, 使能端_低电平有效_stall_高电平有效
  // Probe on \n16位流水接口_4_dout16 

  // Notes on the sheet:
  //   计数器
  //   阶段1
  //   阶段2
  //   阶段3
  //   利用ctrl+T驱动该电路时钟，观察数据在流水线中传递的过程
  //   阶段4
  //   阶段5
endmodule

module \组合逻辑  (
  input  [15:0] in_1,
  output [15:0] out_2
);


  assign out_2 = in_1;
endmodule

module \CRC串行电路  (
  input  in_1,
  input  [3:0] \初始值 ,
  input  \逆向计数_从最高位输入 ,
  input  [13:0] \初始数据补4位零 ,
  output [3:0] \CRC校验和 
);

  wire bitselector_1_out, button_1_out, clock_1_out, d_ff_1_q, multiplexer_1_out, multiplexer_2_out,
       not_1_out, not_2_out;
  wire [3:0] counter_1_q;

  Clock #(.highDuration(1), .lowDuration(1)) clock_1 (.out(clock_1_out));
  Button button_1 (.out(button_1_out));
  D_Flip_Flop #(.trigger("rising"), .Pre_Clr_Positions("ABOVE_BELOW"), .NegatePresetClear("false"), .enable("false"), .NewFFLayout("true")) d_ff_1 (
    .clk(clock_1_out), .D(\CRC校验和 [3]), .Q(d_ff_1_q), .reset(button_1_out));  // open: Qn, preset
  Counter #(.width(4), .max('hd), .ongoal("stay"), .trigger("rising"), .behavior("new")) counter_1 (
    .load(button_1_out), .D(\初始值 ), .Q(counter_1_q), .clk(clock_1_out), .down(\逆向计数_从最高位输入 ));  // open: count, carry, clr, preset
  D_Flip_Flop #(.trigger("rising"), .Pre_Clr_Positions("ABOVE_BELOW"), .NegatePresetClear("false"), .enable("false"), .NewFFLayout("true")) d_ff_2 (
    .clk(clock_1_out), .D(\CRC校验和 [2]), .Q(\CRC校验和 [3]), .reset(button_1_out));  // open: Qn, preset
  Multiplexer #(.select(1), .width(1), .disabled("Z"), .enable("false")) multiplexer_1 (
    .in0(\CRC校验和 [1]), .in1(not_1_out), .out(multiplexer_1_out), .sel(d_ff_1_q));
  not not_1 (not_1_out, \CRC校验和 [1]);
  D_Flip_Flop #(.trigger("rising"), .Pre_Clr_Positions("ABOVE_BELOW"), .NegatePresetClear("false"), .enable("false"), .NewFFLayout("true")) d_ff_3 (
    .clk(clock_1_out), .D(multiplexer_1_out), .Q(\CRC校验和 [2]), .reset(button_1_out));  // open: Qn, preset
  Multiplexer #(.select(1), .width(1), .disabled("Z"), .enable("false")) multiplexer_2 (
    .in0(\CRC校验和 [0]), .in1(not_2_out), .out(multiplexer_2_out), .sel(d_ff_1_q));
  D_Flip_Flop #(.trigger("rising"), .Pre_Clr_Positions("ABOVE_BELOW"), .NegatePresetClear("false"), .enable("false"), .NewFFLayout("true")) d_ff_4 (
    .clk(clock_1_out), .D(multiplexer_2_out), .Q(\CRC校验和 [1]), .reset(button_1_out));  // open: Qn, preset
  BitSelector #(.width(14), .group(1)) bitselector_1 (.in(\初始数据补4位零 ), .out(bitselector_1_out), .sel(counter_1_q));
  not not_2 (not_2_out, \CRC校验和 [0]);
  D_Flip_Flop #(.trigger("rising"), .Pre_Clr_Positions("ABOVE_BELOW"), .NegatePresetClear("false"), .enable("false"), .NewFFLayout("true")) d_ff_5 (
    .clk(clock_1_out), .D(bitselector_1_out), .Q(\CRC校验和 [0]), .reset(button_1_out));  // open: Qn, preset

  // Notes on the sheet:
  //   1探测器
  //   多项式：10011
  //   Q4
  //   Q3
  //   Q2
  //   Q1
endmodule

module \地址回滚器  (
  input  [7:0] \正常地址 ,
  input  \高电平回滚 ,
  input  CLK,
  input  \清零 ,
  output [7:0] \输出 
);

  wire comparator_1_lt, comparator_2_lt, not_1_out;
  wire [7:0] multiplexer_1_out, multiplexer_2_out, register_1_q, subtractor_1_out;

  Subtractor #(.width(8)) subtractor_1 (.a(\正常地址 ), .b(8'h4), .out(subtractor_1_out));  // open: bin, bout
  Comparator #(.width(8), .mode("unsigned")) comparator_1 (.a(\正常地址 ), .b(8'h4), .lt(comparator_1_lt));  // open: gt, eq
  not not_1 (not_1_out, comparator_1_lt);
  Comparator #(.width(8), .mode("unsigned")) comparator_2 (
    .a(subtractor_1_out), .b(register_1_q), .lt(comparator_2_lt));  // open: gt, eq
  Register #(.width(8), .trigger("rising"), .Select("low")) register_1 (
    .D(multiplexer_2_out), .Q(register_1_q), .clk(CLK), .clr(\清零 ));  // open: en
  Multiplexer #(.select(1), .width(8), .disabled("Z"), .enable("false")) multiplexer_1 (
    .in0(subtractor_1_out), .in1(register_1_q), .out(multiplexer_1_out), .sel(comparator_2_lt));
  Multiplexer #(.select(1), .width(8), .disabled("Z"), .enable("false")) multiplexer_2 (
    .in0({8{1'b0}}), .in1(multiplexer_1_out), .out(multiplexer_2_out), .sel(not_1_out));
  Multiplexer #(.select(1), .width(8), .disabled("Z"), .enable("false")) multiplexer_3 (
    .in0(\正常地址 ), .in1(multiplexer_2_out), .out(\输出 ), .sel(\高电平回滚 ));
endmodule

module \Stall信号控制  (
  input  \高电平暂停 ,
  input  CLK,
  input  \清零 ,
  output out_4
);

  wire [7:0] counter_1_q;

  Counter #(.width(8), .max('hff), .ongoal("stay"), .trigger("rising"), .behavior("new")) counter_1 (
    .load(\高电平暂停 ), .D(8'h3), .Q(counter_1_q), .clk(CLK), .clr(\清零 ), .down(1'b1));  // open: count, carry, preset
  or or_1 (out_4, \高电平暂停 , counter_1_q[0], counter_1_q[1], counter_1_q[2], counter_1_q[3], counter_1_q[4], counter_1_q[5], counter_1_q[6], counter_1_q[7]);
endmodule

module \_520特辑  (
  input  [31:0] in_1,
  input  [31:0] in_2,
  input  [31:0] in_3,
  input  [31:0] in_4,
  input  [31:0] in_5,
  input  [31:0] in_6,
  input  [31:0] in_7,
  input  [31:0] in_8,
  input  [31:0] in_9,
  input  [31:0] in_10,
  input  [31:0] in_11,
  input  [31:0] in_12,
  input  [31:0] in_13,
  input  [31:0] in_14
);

  wire button_1_out, \时钟_out ;
  wire [6:0] \国标转区位码_1_位号 , \国标转区位码_1_区号 , \国标转区位码_2_位号 , \国标转区位码_2_区号 , \国标转区位码_3_位号 , \国标转区位码_3_区号 ,
       \国标转区位码_4_位号 , \国标转区位码_4_区号 , \国标转区位码_5_位号 , \国标转区位码_5_区号 , \国标转区位码_6_位号 , \国标转区位码_6_区号 ,
       \国标转区位码_7_位号 , \国标转区位码_7_区号 , \国标转区位码_8_位号 , \国标转区位码_8_区号 ;
  wire [7:0] counter_1_q;
  wire [15:0] rom_1_data, rom_2_data, rom_3_data, rom_4_data, rom_5_data, rom_6_data, rom_7_data, rom_8_data;
  wire [31:0] \字库_1_out_3 , \字库_1_out_4 , \字库_1_out_5 , \字库_1_out_6 , \字库_1_out_7 , \字库_1_out_8 ,
       \字库_1_out_9 , \字库_1_out_10 , \字库_1_out_11 , \字库_1_out_12 , \字库_1_out_13 , \字库_1_out_14 ,
       \字库_1_out_15 , \字库_1_out_16 , \字库_1_out_17 , \字库_1_out_18 , \字库_1_out_19 , \字库_1_out_20 ,
       \字库_1_out_21 , \字库_1_out_22 , \字库_1_out_23 , \字库_1_out_24 , \字库_1_out_25 , \字库_1_out_26 ,
       \字库_1_out_27 , \字库_1_out_28 , \字库_1_out_29 , \字库_1_out_30 , \字库_1_out_31 , \字库_1_out_32 ,
       \字库_1_out_33 , \字库_1_out_34 , \字库_2_out_3 , \字库_2_out_4 , \字库_2_out_5 , \字库_2_out_6 , \字库_2_out_7 ,
       \字库_2_out_8 , \字库_2_out_9 , \字库_2_out_10 , \字库_2_out_11 , \字库_2_out_12 , \字库_2_out_13 , \字库_2_out_14 ,
       \字库_2_out_15 , \字库_2_out_16 , \字库_2_out_17 , \字库_2_out_18 , \字库_2_out_19 , \字库_2_out_20 ,
       \字库_2_out_21 , \字库_2_out_22 , \字库_2_out_23 , \字库_2_out_24 , \字库_2_out_25 , \字库_2_out_26 ,
       \字库_2_out_27 , \字库_2_out_28 , \字库_2_out_29 , \字库_2_out_30 , \字库_2_out_31 , \字库_2_out_32 ,
       \字库_2_out_33 , \字库_2_out_34 , \字库_3_out_3 , \字库_3_out_4 , \字库_3_out_5 , \字库_3_out_6 , \字库_3_out_7 ,
       \字库_3_out_8 , \字库_3_out_9 , \字库_3_out_10 , \字库_3_out_11 , \字库_3_out_12 , \字库_3_out_13 , \字库_3_out_14 ,
       \字库_3_out_15 , \字库_3_out_16 , \字库_3_out_17 , \字库_3_out_18 , \字库_3_out_19 , \字库_3_out_20 ,
       \字库_3_out_21 , \字库_3_out_22 , \字库_3_out_23 , \字库_3_out_24 , \字库_3_out_25 , \字库_3_out_26 ,
       \字库_3_out_27 , \字库_3_out_28 , \字库_3_out_29 , \字库_3_out_30 , \字库_3_out_31 , \字库_3_out_32 ,
       \字库_3_out_33 , \字库_3_out_34 , \字库_4_out_3 , \字库_4_out_4 , \字库_4_out_5 , \字库_4_out_6 , \字库_4_out_7 ,
       \字库_4_out_8 , \字库_4_out_9 , \字库_4_out_10 , \字库_4_out_11 , \字库_4_out_12 , \字库_4_out_13 , \字库_4_out_14 ,
       \字库_4_out_15 , \字库_4_out_16 , \字库_4_out_17 , \字库_4_out_18 , \字库_4_out_19 , \字库_4_out_20 ,
       \字库_4_out_21 , \字库_4_out_22 , \字库_4_out_23 , \字库_4_out_24 , \字库_4_out_25 , \字库_4_out_26 ,
       \字库_4_out_27 , \字库_4_out_28 , \字库_4_out_29 , \字库_4_out_30 , \字库_4_out_31 , \字库_4_out_32 ,
       \字库_4_out_33 , \字库_4_out_34 , \字库_5_out_3 , \字库_5_out_4 , \字库_5_out_5 , \字库_5_out_6 , \字库_5_out_7 ,
       \字库_5_out_8 , \字库_5_out_9 , \字库_5_out_10 , \字库_5_out_11 , \字库_5_out_12 , \字库_5_out_13 , \字库_5_out_14 ,
       \字库_5_out_15 , \字库_5_out_16 , \字库_5_out_17 , \字库_5_out_18 , \字库_5_out_19 , \字库_5_out_20 ,
       \字库_5_out_21 , \字库_5_out_22 , \字库_5_out_23 , \字库_5_out_24 , \字库_5_out_25 , \字库_5_out_26 ,
       \字库_5_out_27 , \字库_5_out_28 , \字库_5_out_29 , \字库_5_out_30 , \字库_5_out_31 , \字库_5_out_32 ,
       \字库_5_out_33 , \字库_5_out_34 , \字库_6_out_3 , \字库_6_out_4 , \字库_6_out_5 , \字库_6_out_6 , \字库_6_out_7 ,
       \字库_6_out_8 , \字库_6_out_9 , \字库_6_out_10 , \字库_6_out_11 , \字库_6_out_12 , \字库_6_out_13 , \字库_6_out_14 ,
       \字库_6_out_15 , \字库_6_out_16 , \字库_6_out_17 , \字库_6_out_18 , \字库_6_out_19 , \字库_6_out_20 ,
       \字库_6_out_21 , \字库_6_out_22 , \字库_6_out_23 , \字库_6_out_24 , \字库_6_out_25 , \字库_6_out_26 ,
       \字库_6_out_27 , \字库_6_out_28 , \字库_6_out_29 , \字库_6_out_30 , \字库_6_out_31 , \字库_6_out_32 ,
       \字库_6_out_33 , \字库_6_out_34 , \字库_7_out_3 , \字库_7_out_4 , \字库_7_out_5 , \字库_7_out_6 , \字库_7_out_7 ,
       \字库_7_out_8 , \字库_7_out_9 , \字库_7_out_10 , \字库_7_out_11 , \字库_7_out_12 , \字库_7_out_13 , \字库_7_out_14 ,
       \字库_7_out_15 , \字库_7_out_16 , \字库_7_out_17 , \字库_7_out_18 , \字库_7_out_19 , \字库_7_out_20 ,
       \字库_7_out_21 , \字库_7_out_22 , \字库_7_out_23 , \字库_7_out_24 , \字库_7_out_25 , \字库_7_out_26 ,
       \字库_7_out_27 , \字库_7_out_28 , \字库_7_out_29 , \字库_7_out_30 , \字库_7_out_31 , \字库_7_out_32 ,
       \字库_7_out_33 , \字库_7_out_34 , \字库_8_out_3 , \字库_8_out_4 , \字库_8_out_5 , \字库_8_out_6 , \字库_8_out_7 ,
       \字库_8_out_8 , \字库_8_out_9 , \字库_8_out_10 , \字库_8_out_11 , \字库_8_out_12 , \字库_8_out_13 , \字库_8_out_14 ,
       \字库_8_out_15 , \字库_8_out_16 , \字库_8_out_17 , \字库_8_out_18 , \字库_8_out_19 , \字库_8_out_20 ,
       \字库_8_out_21 , \字库_8_out_22 , \字库_8_out_23 , \字库_8_out_24 , \字库_8_out_25 , \字库_8_out_26 ,
       \字库_8_out_27 , \字库_8_out_28 , \字库_8_out_29 , \字库_8_out_30 , \字库_8_out_31 , \字库_8_out_32 ,
       \字库_8_out_33 , \字库_8_out_34 ;

  Counter #(.width(8), .max('h5), .ongoal("wrap"), .trigger("rising"), .behavior("old")) counter_1 (
    .Q(counter_1_q), .clk(\时钟_out ), .clr(button_1_out));  // open: load, D, count, carry, preset
  Clock #(.highDuration(1), .lowDuration(1)) \u_时钟  (.out(\时钟_out ));
  Button button_1 (.out(button_1_out));
  DotMatrix #(.inputtype("row"), .matrixcols(32), .matrixrows(32), .persist(0), .dotshape("circle")) dotmatrix_1 (
    .row0(\字库_1_out_3 ), .row1(\字库_1_out_4 ), .row2(\字库_1_out_5 ), .row3(\字库_1_out_6 ), .row4(\字库_1_out_7 ),
    .row5(\字库_1_out_8 ), .row6(\字库_1_out_9 ), .row7(\字库_1_out_10 ), .row8(\字库_1_out_11 ),
    .row9(\字库_1_out_12 ), .row10(\字库_1_out_13 ), .row11(\字库_1_out_14 ), .row12(\字库_1_out_15 ),
    .row13(\字库_1_out_16 ), .row14(\字库_1_out_17 ), .row15(\字库_1_out_18 ), .row16(\字库_1_out_19 ),
    .row17(\字库_1_out_20 ), .row18(\字库_1_out_21 ), .row19(\字库_1_out_22 ), .row20(\字库_1_out_23 ),
    .row21(\字库_1_out_24 ), .row22(\字库_1_out_25 ), .row23(\字库_1_out_26 ), .row24(\字库_1_out_27 ),
    .row25(\字库_1_out_28 ), .row26(\字库_1_out_29 ), .row27(\字库_1_out_30 ), .row28(\字库_1_out_31 ),
    .row29(\字库_1_out_32 ), .row30(\字库_1_out_33 ), .row31(\字库_1_out_34 ));
  \字库  \u_字库_1  (
    .out_3(\字库_1_out_3 ), .out_4(\字库_1_out_4 ), .out_5(\字库_1_out_5 ), .out_6(\字库_1_out_6 ),
    .out_7(\字库_1_out_7 ), .out_8(\字库_1_out_8 ), .out_9(\字库_1_out_9 ), .out_10(\字库_1_out_10 ),
    .out_11(\字库_1_out_11 ), .out_12(\字库_1_out_12 ), .out_13(\字库_1_out_13 ), .out_14(\字库_1_out_14 ),
    .out_15(\字库_1_out_15 ), .out_16(\字库_1_out_16 ), .out_17(\字库_1_out_17 ), .out_18(\字库_1_out_18 ),
    .out_19(\字库_1_out_19 ), .out_20(\字库_1_out_20 ), .out_21(\字库_1_out_21 ), .out_22(\字库_1_out_22 ),
    .out_23(\字库_1_out_23 ), .out_24(\字库_1_out_24 ), .out_25(\字库_1_out_25 ), .out_26(\字库_1_out_26 ),
    .out_27(\字库_1_out_27 ), .out_28(\字库_1_out_28 ), .out_29(\字库_1_out_29 ), .out_30(\字库_1_out_30 ),
    .out_31(\字库_1_out_31 ), .out_32(\字库_1_out_32 ), .out_33(\字库_1_out_33 ), .out_34(\字库_1_out_34 ),
    .\区号 (\国标转区位码_1_区号 ), .\位号 (\国标转区位码_1_位号 ));
  \国标转区位码  \u_国标转区位码_1  (.\位号 (\国标转区位码_1_位号 ), .\区号 (\国标转区位码_1_区号 ), .GB2312(rom_1_data));
  ROM #(.addrWidth(8), .dataWidth(16), .Select("high")) rom_1 (.addr(counter_1_q), .data(rom_1_data));
  ROM #(.addrWidth(8), .dataWidth(16), .Select("high")) rom_2 (.addr(counter_1_q), .data(rom_2_data));
  \国标转区位码  \u_国标转区位码_2  (.\位号 (\国标转区位码_2_位号 ), .\区号 (\国标转区位码_2_区号 ), .GB2312(rom_2_data));
  DotMatrix #(.inputtype("row"), .matrixcols(32), .matrixrows(32), .persist(0), .dotshape("circle")) dotmatrix_2 (
    .row0(\字库_2_out_3 ), .row1(\字库_2_out_4 ), .row2(\字库_2_out_5 ), .row3(\字库_2_out_6 ), .row4(\字库_2_out_7 ),
    .row5(\字库_2_out_8 ), .row6(\字库_2_out_9 ), .row7(\字库_2_out_10 ), .row8(\字库_2_out_11 ),
    .row9(\字库_2_out_12 ), .row10(\字库_2_out_13 ), .row11(\字库_2_out_14 ), .row12(\字库_2_out_15 ),
    .row13(\字库_2_out_16 ), .row14(\字库_2_out_17 ), .row15(\字库_2_out_18 ), .row16(\字库_2_out_19 ),
    .row17(\字库_2_out_20 ), .row18(\字库_2_out_21 ), .row19(\字库_2_out_22 ), .row20(\字库_2_out_23 ),
    .row21(\字库_2_out_24 ), .row22(\字库_2_out_25 ), .row23(\字库_2_out_26 ), .row24(\字库_2_out_27 ),
    .row25(\字库_2_out_28 ), .row26(\字库_2_out_29 ), .row27(\字库_2_out_30 ), .row28(\字库_2_out_31 ),
    .row29(\字库_2_out_32 ), .row30(\字库_2_out_33 ), .row31(\字库_2_out_34 ));
  \字库  \u_字库_2  (
    .out_3(\字库_2_out_3 ), .out_4(\字库_2_out_4 ), .out_5(\字库_2_out_5 ), .out_6(\字库_2_out_6 ),
    .out_7(\字库_2_out_7 ), .out_8(\字库_2_out_8 ), .out_9(\字库_2_out_9 ), .out_10(\字库_2_out_10 ),
    .out_11(\字库_2_out_11 ), .out_12(\字库_2_out_12 ), .out_13(\字库_2_out_13 ), .out_14(\字库_2_out_14 ),
    .out_15(\字库_2_out_15 ), .out_16(\字库_2_out_16 ), .out_17(\字库_2_out_17 ), .out_18(\字库_2_out_18 ),
    .out_19(\字库_2_out_19 ), .out_20(\字库_2_out_20 ), .out_21(\字库_2_out_21 ), .out_22(\字库_2_out_22 ),
    .out_23(\字库_2_out_23 ), .out_24(\字库_2_out_24 ), .out_25(\字库_2_out_25 ), .out_26(\字库_2_out_26 ),
    .out_27(\字库_2_out_27 ), .out_28(\字库_2_out_28 ), .out_29(\字库_2_out_29 ), .out_30(\字库_2_out_30 ),
    .out_31(\字库_2_out_31 ), .out_32(\字库_2_out_32 ), .out_33(\字库_2_out_33 ), .out_34(\字库_2_out_34 ),
    .\区号 (\国标转区位码_2_区号 ), .\位号 (\国标转区位码_2_位号 ));
  DotMatrix #(.inputtype("row"), .matrixcols(32), .matrixrows(32), .persist(0), .dotshape("circle")) dotmatrix_3 (
    .row0(in_1), .row1(in_1), .row2(in_1), .row3(in_1), .row4(in_1), .row5(in_1), .row6(in_2), .row7(in_3),
    .row8(in_4), .row9(in_5), .row10(in_6), .row11(in_6), .row12(in_10), .row13(in_10), .row14(in_10),
    .row15(in_10), .row16(in_6), .row17(in_6), .row18(in_5), .row19(in_8), .row20(in_7), .row21(in_9),
    .row22(in_12), .row23(in_13), .row24(in_11), .row25(in_14), .row26(in_1), .row27(in_1), .row28(in_1),
    .row29(in_1), .row30(in_1), .row31(in_1));
  ROM #(.addrWidth(8), .dataWidth(16), .Select("high")) rom_3 (.addr(counter_1_q), .data(rom_3_data));
  DotMatrix #(.inputtype("row"), .matrixcols(32), .matrixrows(32), .persist(0), .dotshape("circle")) dotmatrix_4 (
    .row0(\字库_3_out_3 ), .row1(\字库_3_out_4 ), .row2(\字库_3_out_5 ), .row3(\字库_3_out_6 ), .row4(\字库_3_out_7 ),
    .row5(\字库_3_out_8 ), .row6(\字库_3_out_9 ), .row7(\字库_3_out_10 ), .row8(\字库_3_out_11 ),
    .row9(\字库_3_out_12 ), .row10(\字库_3_out_13 ), .row11(\字库_3_out_14 ), .row12(\字库_3_out_15 ),
    .row13(\字库_3_out_16 ), .row14(\字库_3_out_17 ), .row15(\字库_3_out_18 ), .row16(\字库_3_out_19 ),
    .row17(\字库_3_out_20 ), .row18(\字库_3_out_21 ), .row19(\字库_3_out_22 ), .row20(\字库_3_out_23 ),
    .row21(\字库_3_out_24 ), .row22(\字库_3_out_25 ), .row23(\字库_3_out_26 ), .row24(\字库_3_out_27 ),
    .row25(\字库_3_out_28 ), .row26(\字库_3_out_29 ), .row27(\字库_3_out_30 ), .row28(\字库_3_out_31 ),
    .row29(\字库_3_out_32 ), .row30(\字库_3_out_33 ), .row31(\字库_3_out_34 ));
  \字库  \u_字库_3  (
    .out_3(\字库_3_out_3 ), .out_4(\字库_3_out_4 ), .out_5(\字库_3_out_5 ), .out_6(\字库_3_out_6 ),
    .out_7(\字库_3_out_7 ), .out_8(\字库_3_out_8 ), .out_9(\字库_3_out_9 ), .out_10(\字库_3_out_10 ),
    .out_11(\字库_3_out_11 ), .out_12(\字库_3_out_12 ), .out_13(\字库_3_out_13 ), .out_14(\字库_3_out_14 ),
    .out_15(\字库_3_out_15 ), .out_16(\字库_3_out_16 ), .out_17(\字库_3_out_17 ), .out_18(\字库_3_out_18 ),
    .out_19(\字库_3_out_19 ), .out_20(\字库_3_out_20 ), .out_21(\字库_3_out_21 ), .out_22(\字库_3_out_22 ),
    .out_23(\字库_3_out_23 ), .out_24(\字库_3_out_24 ), .out_25(\字库_3_out_25 ), .out_26(\字库_3_out_26 ),
    .out_27(\字库_3_out_27 ), .out_28(\字库_3_out_28 ), .out_29(\字库_3_out_29 ), .out_30(\字库_3_out_30 ),
    .out_31(\字库_3_out_31 ), .out_32(\字库_3_out_32 ), .out_33(\字库_3_out_33 ), .out_34(\字库_3_out_34 ),
    .\区号 (\国标转区位码_3_区号 ), .\位号 (\国标转区位码_3_位号 ));
  \国标转区位码  \u_国标转区位码_3  (.\位号 (\国标转区位码_3_位号 ), .\区号 (\国标转区位码_3_区号 ), .GB2312(rom_3_data));
  ROM #(.addrWidth(8), .dataWidth(16), .Select("high")) rom_4 (.addr(counter_1_q), .data(rom_4_data));
  \国标转区位码  \u_国标转区位码_4  (.\位号 (\国标转区位码_4_位号 ), .\区号 (\国标转区位码_4_区号 ), .GB2312(rom_4_data));
  DotMatrix #(.inputtype("row"), .matrixcols(32), .matrixrows(32), .persist(0), .dotshape("circle")) dotmatrix_5 (
    .row0(\字库_4_out_3 ), .row1(\字库_4_out_4 ), .row2(\字库_4_out_5 ), .row3(\字库_4_out_6 ), .row4(\字库_4_out_7 ),
    .row5(\字库_4_out_8 ), .row6(\字库_4_out_9 ), .row7(\字库_4_out_10 ), .row8(\字库_4_out_11 ),
    .row9(\字库_4_out_12 ), .row10(\字库_4_out_13 ), .row11(\字库_4_out_14 ), .row12(\字库_4_out_15 ),
    .row13(\字库_4_out_16 ), .row14(\字库_4_out_17 ), .row15(\字库_4_out_18 ), .row16(\字库_4_out_19 ),
    .row17(\字库_4_out_20 ), .row18(\字库_4_out_21 ), .row19(\字库_4_out_22 ), .row20(\字库_4_out_23 ),
    .row21(\字库_4_out_24 ), .row22(\字库_4_out_25 ), .row23(\字库_4_out_26 ), .row24(\字库_4_out_27 ),
    .row25(\字库_4_out_28 ), .row26(\字库_4_out_29 ), .row27(\字库_4_out_30 ), .row28(\字库_4_out_31 ),
    .row29(\字库_4_out_32 ), .row30(\字库_4_out_33 ), .row31(\字库_4_out_34 ));
  \字库  \u_字库_4  (
    .out_3(\字库_4_out_3 ), .out_4(\字库_4_out_4 ), .out_5(\字库_4_out_5 ), .out_6(\字库_4_out_6 ),
    .out_7(\字库_4_out_7 ), .out_8(\字库_4_out_8 ), .out_9(\字库_4_out_9 ), .out_10(\字库_4_out_10 ),
    .out_11(\字库_4_out_11 ), .out_12(\字库_4_out_12 ), .out_13(\字库_4_out_13 ), .out_14(\字库_4_out_14 ),
    .out_15(\字库_4_out_15 ), .out_16(\字库_4_out_16 ), .out_17(\字库_4_out_17 ), .out_18(\字库_4_out_18 ),
    .out_19(\字库_4_out_19 ), .out_20(\字库_4_out_20 ), .out_21(\字库_4_out_21 ), .out_22(\字库_4_out_22 ),
    .out_23(\字库_4_out_23 ), .out_24(\字库_4_out_24 ), .out_25(\字库_4_out_25 ), .out_26(\字库_4_out_26 ),
    .out_27(\字库_4_out_27 ), .out_28(\字库_4_out_28 ), .out_29(\字库_4_out_29 ), .out_30(\字库_4_out_30 ),
    .out_31(\字库_4_out_31 ), .out_32(\字库_4_out_32 ), .out_33(\字库_4_out_33 ), .out_34(\字库_4_out_34 ),
    .\区号 (\国标转区位码_4_区号 ), .\位号 (\国标转区位码_4_位号 ));
  ROM #(.addrWidth(8), .dataWidth(16), .Select("high")) rom_5 (.addr(counter_1_q), .data(rom_5_data));
  DotMatrix #(.inputtype("row"), .matrixcols(32), .matrixrows(32), .persist(0), .dotshape("circle")) dotmatrix_6 (
    .row0(\字库_5_out_3 ), .row1(\字库_5_out_4 ), .row2(\字库_5_out_5 ), .row3(\字库_5_out_6 ), .row4(\字库_5_out_7 ),
    .row5(\字库_5_out_8 ), .row6(\字库_5_out_9 ), .row7(\字库_5_out_10 ), .row8(\字库_5_out_11 ),
    .row9(\字库_5_out_12 ), .row10(\字库_5_out_13 ), .row11(\字库_5_out_14 ), .row12(\字库_5_out_15 ),
    .row13(\字库_5_out_16 ), .row14(\字库_5_out_17 ), .row15(\字库_5_out_18 ), .row16(\字库_5_out_19 ),
    .row17(\字库_5_out_20 ), .row18(\字库_5_out_21 ), .row19(\字库_5_out_22 ), .row20(\字库_5_out_23 ),
    .row21(\字库_5_out_24 ), .row22(\字库_5_out_25 ), .row23(\字库_5_out_26 ), .row24(\字库_5_out_27 ),
    .row25(\字库_5_out_28 ), .row26(\字库_5_out_29 ), .row27(\字库_5_out_30 ), .row28(\字库_5_out_31 ),
    .row29(\字库_5_out_32 ), .row30(\字库_5_out_33 ), .row31(\字库_5_out_34 ));
  \字库  \u_字库_5  (
    .out_3(\字库_5_out_3 ), .out_4(\字库_5_out_4 ), .out_5(\字库_5_out_5 ), .out_6(\字库_5_out_6 ),
    .out_7(\字库_5_out_7 ), .out_8(\字库_5_out_8 ), .out_9(\字库_5_out_9 ), .out_10(\字库_5_out_10 ),
    .out_11(\字库_5_out_11 ), .out_12(\字库_5_out_12 ), .out_13(\字库_5_out_13 ), .out_14(\字库_5_out_14 ),
    .out_15(\字库_5_out_15 ), .out_16(\字库_5_out_16 ), .out_17(\字库_5_out_17 ), .out_18(\字库_5_out_18 ),
    .out_19(\字库_5_out_19 ), .out_20(\字库_5_out_20 ), .out_21(\字库_5_out_21 ), .out_22(\字库_5_out_22 ),
    .out_23(\字库_5_out_23 ), .out_24(\字库_5_out_24 ), .out_25(\字库_5_out_25 ), .out_26(\字库_5_out_26 ),
    .out_27(\字库_5_out_27 ), .out_28(\字库_5_out_28 ), .out_29(\字库_5_out_29 ), .out_30(\字库_5_out_30 ),
    .out_31(\字库_5_out_31 ), .out_32(\字库_5_out_32 ), .out_33(\字库_5_out_33 ), .out_34(\字库_5_out_34 ),
    .\区号 (\国标转区位码_5_区号 ), .\位号 (\国标转区位码_5_位号 ));
  \国标转区位码  \u_国标转区位码_5  (.\位号 (\国标转区位码_5_位号 ), .\区号 (\国标转区位码_5_区号 ), .GB2312(rom_5_data));
  ROM #(.addrWidth(8), .dataWidth(16), .Select("high")) rom_6 (.addr(counter_1_q), .data(rom_6_data));
  \国标转区位码  \u_国标转区位码_6  (.\位号 (\国标转区位码_6_位号 ), .\区号 (\国标转区位码_6_区号 ), .GB2312(rom_6_data));
  \字库  \u_字库_6  (
    .out_3(\字库_6_out_3 ), .out_4(\字库_6_out_4 ), .out_5(\字库_6_out_5 ), .out_6(\字库_6_out_6 ),
    .out_7(\字库_6_out_7 ), .out_8(\字库_6_out_8 ), .out_9(\字库_6_out_9 ), .out_10(\字库_6_out_10 ),
    .out_11(\字库_6_out_11 ), .out_12(\字库_6_out_12 ), .out_13(\字库_6_out_13 ), .out_14(\字库_6_out_14 ),
    .out_15(\字库_6_out_15 ), .out_16(\字库_6_out_16 ), .out_17(\字库_6_out_17 ), .out_18(\字库_6_out_18 ),
    .out_19(\字库_6_out_19 ), .out_20(\字库_6_out_20 ), .out_21(\字库_6_out_21 ), .out_22(\字库_6_out_22 ),
    .out_23(\字库_6_out_23 ), .out_24(\字库_6_out_24 ), .out_25(\字库_6_out_25 ), .out_26(\字库_6_out_26 ),
    .out_27(\字库_6_out_27 ), .out_28(\字库_6_out_28 ), .out_29(\字库_6_out_29 ), .out_30(\字库_6_out_30 ),
    .out_31(\字库_6_out_31 ), .out_32(\字库_6_out_32 ), .out_33(\字库_6_out_33 ), .out_34(\字库_6_out_34 ),
    .\区号 (\国标转区位码_6_区号 ), .\位号 (\国标转区位码_6_位号 ));
  DotMatrix #(.inputtype("row"), .matrixcols(32), .matrixrows(32), .persist(0), .dotshape("circle")) dotmatrix_7 (
    .row0(\字库_6_out_3 ), .row1(\字库_6_out_4 ), .row2(\字库_6_out_5 ), .row3(\字库_6_out_6 ), .row4(\字库_6_out_7 ),
    .row5(\字库_6_out_8 ), .row6(\字库_6_out_9 ), .row7(\字库_6_out_10 ), .row8(\字库_6_out_11 ),
    .row9(\字库_6_out_12 ), .row10(\字库_6_out_13 ), .row11(\字库_6_out_14 ), .row12(\字库_6_out_15 ),
    .row13(\字库_6_out_16 ), .row14(\字库_6_out_17 ), .row15(\字库_6_out_18 ), .row16(\字库_6_out_19 ),
    .row17(\字库_6_out_20 ), .row18(\字库_6_out_21 ), .row19(\字库_6_out_22 ), .row20(\字库_6_out_23 ),
    .row21(\字库_6_out_24 ), .row22(\字库_6_out_25 ), .row23(\字库_6_out_26 ), .row24(\字库_6_out_27 ),
    .row25(\字库_6_out_28 ), .row26(\字库_6_out_29 ), .row27(\字库_6_out_30 ), .row28(\字库_6_out_31 ),
    .row29(\字库_6_out_32 ), .row30(\字库_6_out_33 ), .row31(\字库_6_out_34 ));
  ROM #(.addrWidth(8), .dataWidth(16), .Select("high")) rom_7 (.addr(counter_1_q), .data(rom_7_data));
  \字库  \u_字库_7  (
    .out_3(\字库_7_out_3 ), .out_4(\字库_7_out_4 ), .out_5(\字库_7_out_5 ), .out_6(\字库_7_out_6 ),
    .out_7(\字库_7_out_7 ), .out_8(\字库_7_out_8 ), .out_9(\字库_7_out_9 ), .out_10(\字库_7_out_10 ),
    .out_11(\字库_7_out_11 ), .out_12(\字库_7_out_12 ), .out_13(\字库_7_out_13 ), .out_14(\字库_7_out_14 ),
    .out_15(\字库_7_out_15 ), .out_16(\字库_7_out_16 ), .out_17(\字库_7_out_17 ), .out_18(\字库_7_out_18 ),
    .out_19(\字库_7_out_19 ), .out_20(\字库_7_out_20 ), .out_21(\字库_7_out_21 ), .out_22(\字库_7_out_22 ),
    .out_23(\字库_7_out_23 ), .out_24(\字库_7_out_24 ), .out_25(\字库_7_out_25 ), .out_26(\字库_7_out_26 ),
    .out_27(\字库_7_out_27 ), .out_28(\字库_7_out_28 ), .out_29(\字库_7_out_29 ), .out_30(\字库_7_out_30 ),
    .out_31(\字库_7_out_31 ), .out_32(\字库_7_out_32 ), .out_33(\字库_7_out_33 ), .out_34(\字库_7_out_34 ),
    .\区号 (\国标转区位码_7_区号 ), .\位号 (\国标转区位码_7_位号 ));
  DotMatrix #(.inputtype("row"), .matrixcols(32), .matrixrows(32), .persist(0), .dotshape("circle")) dotmatrix_8 (
    .row0(\字库_7_out_3 ), .row1(\字库_7_out_4 ), .row2(\字库_7_out_5 ), .row3(\字库_7_out_6 ), .row4(\字库_7_out_7 ),
    .row5(\字库_7_out_8 ), .row6(\字库_7_out_9 ), .row7(\字库_7_out_10 ), .row8(\字库_7_out_11 ),
    .row9(\字库_7_out_12 ), .row10(\字库_7_out_13 ), .row11(\字库_7_out_14 ), .row12(\字库_7_out_15 ),
    .row13(\字库_7_out_16 ), .row14(\字库_7_out_17 ), .row15(\字库_7_out_18 ), .row16(\字库_7_out_19 ),
    .row17(\字库_7_out_20 ), .row18(\字库_7_out_21 ), .row19(\字库_7_out_22 ), .row20(\字库_7_out_23 ),
    .row21(\字库_7_out_24 ), .row22(\字库_7_out_25 ), .row23(\字库_7_out_26 ), .row24(\字库_7_out_27 ),
    .row25(\字库_7_out_28 ), .row26(\字库_7_out_29 ), .row27(\字库_7_out_30 ), .row28(\字库_7_out_31 ),
    .row29(\字库_7_out_32 ), .row30(\字库_7_out_33 ), .row31(\字库_7_out_34 ));
  \国标转区位码  \u_国标转区位码_7  (.\位号 (\国标转区位码_7_位号 ), .\区号 (\国标转区位码_7_区号 ), .GB2312(rom_7_data));
  ROM #(.addrWidth(8), .dataWidth(16), .Select("high")) rom_8 (.addr(counter_1_q), .data(rom_8_data));
  \国标转区位码  \u_国标转区位码_8  (.\位号 (\国标转区位码_8_位号 ), .\区号 (\国标转区位码_8_区号 ), .GB2312(rom_8_data));
  \字库  \u_字库_8  (
    .out_3(\字库_8_out_3 ), .out_4(\字库_8_out_4 ), .out_5(\字库_8_out_5 ), .out_6(\字库_8_out_6 ),
    .out_7(\字库_8_out_7 ), .out_8(\字库_8_out_8 ), .out_9(\字库_8_out_9 ), .out_10(\字库_8_out_10 ),
    .out_11(\字库_8_out_11 ), .out_12(\字库_8_out_12 ), .out_13(\字库_8_out_13 ), .out_14(\字库_8_out_14 ),
    .out_15(\字库_8_out_15 ), .out_16(\字库_8_out_16 ), .out_17(\字库_8_out_17 ), .out_18(\字库_8_out_18 ),
    .out_19(\字库_8_out_19 ), .out_20(\字库_8_out_20 ), .out_21(\字库_8_out_21 ), .out_22(\字库_8_out_22 ),
    .out_23(\字库_8_out_23 ), .out_24(\字库_8_out_24 ), .out_25(\字库_8_out_25 ), .out_26(\字库_8_out_26 ),
    .out_27(\字库_8_out_27 ), .out_28(\字库_8_out_28 ), .out_29(\字库_8_out_29 ), .out_30(\字库_8_out_30 ),
    .out_31(\字库_8_out_31 ), .out_32(\字库_8_out_32 ), .out_33(\字库_8_out_33 ), .out_34(\字库_8_out_34 ),
    .\区号 (\国标转区位码_8_区号 ), .\位号 (\国标转区位码_8_位号 ));
  DotMatrix #(.inputtype("row"), .matrixcols(32), .matrixrows(32), .persist(0), .dotshape("circle")) dotmatrix_9 (
    .row0(\字库_8_out_3 ), .row1(\字库_8_out_4 ), .row2(\字库_8_out_5 ), .row3(\字库_8_out_6 ), .row4(\字库_8_out_7 ),
    .row5(\字库_8_out_8 ), .row6(\字库_8_out_9 ), .row7(\字库_8_out_10 ), .row8(\字库_8_out_11 ),
    .row9(\字库_8_out_12 ), .row10(\字库_8_out_13 ), .row11(\字库_8_out_14 ), .row12(\字库_8_out_15 ),
    .row13(\字库_8_out_16 ), .row14(\字库_8_out_17 ), .row15(\字库_8_out_18 ), .row16(\字库_8_out_19 ),
    .row17(\字库_8_out_20 ), .row18(\字库_8_out_21 ), .row19(\字库_8_out_22 ), .row20(\字库_8_out_23 ),
    .row21(\字库_8_out_24 ), .row22(\字库_8_out_25 ), .row23(\字库_8_out_26 ), .row24(\字库_8_out_27 ),
    .row25(\字库_8_out_28 ), .row26(\字库_8_out_29 ), .row27(\字库_8_out_30 ), .row28(\字库_8_out_31 ),
    .row29(\字库_8_out_32 ), .row30(\字库_8_out_33 ), .row31(\字库_8_out_34 ));

  // Notes on the sheet:
  //   计数器
  //   contents of rom_1 (hex, n*v repeats v):
  //   a3b5 a3b2 a3b0 ced2 b0ae c4e3
  //   contents of rom_2 (hex, n*v repeats v):
  //   a3b2 a3b0 ced2 b0ae c4e3 a3b5
  //   contents of rom_3 (hex, n*v repeats v):
  //   a3b0 ced2 b0ae c4e3 a3b5 a3b2
  //   contents of rom_4 (hex, n*v repeats v):
  //   ced2 b0ae c4e3 a3b5 a3b2 a3b0
  //   contents of rom_5 (hex, n*v repeats v):
  //   6*c3bb
  //   contents of rom_6 (hex, n*v repeats v):
  //   6*b6d4
  //   contents of rom_7 (hex, n*v repeats v):
  //   6*cff3
  //   contents of rom_8 (hex, n*v repeats v):
  //   6*a3a1
endmodule

module \流水汉字  (
);

  wire button_1_out, \时钟_out ;
  wire [6:0] \国标转区位码_1_位号 , \国标转区位码_1_区号 , \国标转区位码_2_位号 , \国标转区位码_2_区号 ;
  wire [7:0] counter_1_q;
  wire [15:0] \n16位流水接口_1_dout16 , \n16位流水接口_2_dout16 , \n16位流水接口_3_dout16 , rom_1_data;
  wire [31:0] \字库_1_out_3 , \字库_1_out_4 , \字库_1_out_5 , \字库_1_out_6 , \字库_1_out_7 , \字库_1_out_8 ,
       \字库_1_out_9 , \字库_1_out_10 , \字库_1_out_11 , \字库_1_out_12 , \字库_1_out_13 , \字库_1_out_14 ,
       \字库_1_out_15 , \字库_1_out_16 , \字库_1_out_17 , \字库_1_out_18 , \字库_1_out_19 , \字库_1_out_20 ,
       \字库_1_out_21 , \字库_1_out_22 , \字库_1_out_23 , \字库_1_out_24 , \字库_1_out_25 , \字库_1_out_26 ,
       \字库_1_out_27 , \字库_1_out_28 , \字库_1_out_29 , \字库_1_out_30 , \字库_1_out_31 , \字库_1_out_32 ,
       \字库_1_out_33 , \字库_1_out_34 , \字库_2_out_3 , \字库_2_out_4 , \字库_2_out_5 , \字库_2_out_6 , \字库_2_out_7 ,
       \字库_2_out_8 , \字库_2_out_9 , \字库_2_out_10 , \字库_2_out_11 , \字库_2_out_12 , \字库_2_out_13 , \字库_2_out_14 ,
       \字库_2_out_15 , \字库_2_out_16 , \字库_2_out_17 , \字库_2_out_18 , \字库_2_out_19 , \字库_2_out_20 ,
       \字库_2_out_21 , \字库_2_out_22 , \字库_2_out_23 , \字库_2_out_24 , \字库_2_out_25 , \字库_2_out_26 ,
       \字库_2_out_27 , \字库_2_out_28 , \字库_2_out_29 , \字库_2_out_30 , \字库_2_out_31 , \字库_2_out_32 ,
       \字库_2_out_33 , \字库_2_out_34 ;

  Counter #(.width(8), .max('hff), .ongoal("wrap"), .trigger("rising"), .behavior("old")) counter_1 (
    .Q(counter_1_q), .clk(\时钟_out ), .clr(button_1_out));  // open: load, D, count, carry, preset
  Button button_1 (.out(button_1_out));
  Clock #(.highDuration(1), .lowDuration(1)) \u_时钟  (.out(\时钟_out ));
  \国标转区位码  \u_国标转区位码_1  (.\位号 (\国标转区位码_1_位号 ), .\区号 (\国标转区位码_1_区号 ), .GB2312(\n16位流水接口_1_dout16 ));
  ROM #(.addrWidth(8), .dataWidth(16), .Select("high")) rom_1 (.addr(counter_1_q), .data(rom_1_data));
  \字库  \u_字库_1  (
    .out_3(\字库_1_out_3 ), .out_4(\字库_1_out_4 ), .out_5(\字库_1_out_5 ), .out_6(\字库_1_out_6 ),
    .out_7(\字库_1_out_7 ), .out_8(\字库_1_out_8 ), .out_9(\字库_1_out_9 ), .out_10(\字库_1_out_10 ),
    .out_11(\字库_1_out_11 ), .out_12(\字库_1_out_12 ), .out_13(\字库_1_out_13 ), .out_14(\字库_1_out_14 ),
    .out_15(\字库_1_out_15 ), .out_16(\字库_1_out_16 ), .out_17(\字库_1_out_17 ), .out_18(\字库_1_out_18 ),
    .out_19(\字库_1_out_19 ), .out_20(\字库_1_out_20 ), .out_21(\字库_1_out_21 ), .out_22(\字库_1_out_22 ),
    .out_23(\字库_1_out_23 ), .out_24(\字库_1_out_24 ), .out_25(\字库_1_out_25 ), .out_26(\字库_1_out_26 ),
    .out_27(\字库_1_out_27 ), .out_28(\字库_1_out_28 ), .out_29(\字库_1_out_29 ), .out_30(\字库_1_out_30 ),
    .out_31(\字库_1_out_31 ), .out_32(\字库_1_out_32 ), .out_33(\字库_1_out_33 ), .out_34(\字库_1_out_34 ),
    .\区号 (\国标转区位码_1_区号 ), .\位号 (\国标转区位码_1_位号 ));
  DotMatrix #(.inputtype("row"), .matrixcols(32), .matrixrows(32), .persist(0), .dotshape("circle")) dotmatrix_1 (
    .row0(\字库_1_out_3 ), .row1(\字库_1_out_4 ), .row2(\字库_1_out_5 ), .row3(\字库_1_out_6 ), .row4(\字库_1_out_7 ),
    .row5(\字库_1_out_8 ), .row6(\字库_1_out_9 ), .row7(\字库_1_out_10 ), .row8(\字库_1_out_11 ),
    .row9(\字库_1_out_12 ), .row10(\字库_1_out_13 ), .row11(\字库_1_out_14 ), .row12(\字库_1_out_15 ),
    .row13(\字库_1_out_16 ), .row14(\字库_1_out_17 ), .row15(\字库_1_out_18 ), .row16(\字库_1_out_19 ),
    .row17(\字库_1_out_20 ), .row18(\字库_1_out_21 ), .row19(\字库_1_out_22 ), .row20(\字库_1_out_23 ),
    .row21(\字库_1_out_24 ), .row22(\字库_1_out_25 ), .row23(\字库_1_out_26 ), .row24(\字库_1_out_27 ),
    .row25(\字库_1_out_28 ), .row26(\字库_1_out_29 ), .row27(\字库_1_out_30 ), .row28(\字库_1_out_31 ),
    .row29(\字库_1_out_32 ), .row30(\字库_1_out_33 ), .row31(\字库_1_out_34 ));
  \_16位流水接口  \u_16位流水接口_1  (
    .Din16(rom_1_data), .CLK(\时钟_out ), .Dout16(\n16位流水接口_1_dout16 ));  // open: 传输状态In_表明当前传输数据有效, 传输状态Out_表明当前传输数据有效, 同步清零_气泡_高电平有效, 使能端_低电平有效_stall_高电平有效
  \_16位流水接口  \u_16位流水接口_2  (
    .Din16(\n16位流水接口_1_dout16 ), .CLK(\时钟_out ), .Dout16(\n16位流水接口_2_dout16 ));  // open: 传输状态In_表明当前传输数据有效, 传输状态Out_表明当前传输数据有效, 同步清零_气泡_高电平有效, 使能端_低电平有效_stall_高电平有效
  \_16位流水接口  \u_16位流水接口_3  (
    .Din16(\n16位流水接口_2_dout16 ), .CLK(\时钟_out ), .Dout16(\n16位流水接口_3_dout16 ));  // open: 传输状态In_表明当前传输数据有效, 传输状态Out_表明当前传输数据有效, 同步清零_气泡_高电平有效, 使能端_低电平有效_stall_高电平有效
  \_16位流水接口  \u_16位流水接口_4  (
    .Din16(\n16位流水接口_3_dout16 ), .CLK(\时钟_out ));  // open: 传输状态In_表明当前传输数据有效, Dout16, 传输状态Out_表明当前传输数据有效, 同步清零_气泡_高电平有效, 使能端_低电平有效_stall_高电平有效
  \国标转区位码  \u_国标转区位码_2  (.\位号 (\国标转区位码_2_位号 ), .\区号 (\国标转区位码_2_区号 ), .GB2312(\n16位流水接口_2_dout16 ));
  \字库  \u_字库_2  (
    .out_3(\字库_2_out_3 ), .out_4(\字库_2_out_4 ), .out_5(\字库_2_out_5 ), .out_6(\字库_2_out_6 ),
    .out_7(\字库_2_out_7 ), .out_8(\字库_2_out_8 ), .out_9(\字库_2_out_9 ), .out_10(\字库_2_out_10 ),
    .out_11(\字库_2_out_11 ), .out_12(\字库_2_out_12 ), .out_13(\字库_2_out_13 ), .out_14(\字库_2_out_14 ),
    .out_15(\字库_2_out_15 ), .out_16(\字库_2_out_16 ), .out_17(\字库_2_out_17 ), .out_18(\字库_2_out_18 ),
    .out_19(\字库_2_out_19 ), .out_20(\字库_2_out_20 ), .out_21(\字库_2_out_21 ), .out_22(\字库_2_out_22 ),
    .out_23(\字库_2_out_23 ), .out_24(\字库_2_out_24 ), .out_25(\字库_2_out_25 ), .out_26(\字库_2_out_26 ),
    .out_27(\字库_2_out_27 ), .out_28(\字库_2_out_28 ), .out_29(\字库_2_out_29 ), .out_30(\字库_2_out_30 ),
    .out_31(\字库_2_out_31 ), .out_32(\字库_2_out_32 ), .out_33(\字库_2_out_33 ), .out_34(\字库_2_out_34 ),
    .\区号 (\国标转区位码_2_区号 ), .\位号 (\国标转区位码_2_位号 ));
  DotMatrix #(.inputtype("row"), .matrixcols(32), .matrixrows(32), .persist(0), .dotshape("circle")) dotmatrix_2 (
    .row0(\字库_2_out_3 ), .row1(\字库_2_out_4 ), .row2(\字库_2_out_5 ), .row3(\字库_2_out_6 ), .row4(\字库_2_out_7 ),
    .row5(\字库_2_out_8 ), .row6(\字库_2_out_9 ), .row7(\字库_2_out_10 ), .row8(\字库_2_out_11 ),
    .row9(\字库_2_out_12 ), .row10(\字库_2_out_13 ), .row11(\字库_2_out_14 ), .row12(\字库_2_out_15 ),
    .row13(\字库_2_out_16 ), .row14(\字库_2_out_17 ), .row15(\字库_2_out_18 ), .row16(\字库_2_out_19 ),
    .row17(\字库_2_out_20 ), .row18(\字库_2_out_21 ), .row19(\字库_2_out_22 ), .row20(\字库_2_out_23 ),
    .row21(\字库_2_out_24 ), .row22(\字库_2_out_25 ), .row23(\字库_2_out_26 ), .row24(\字库_2_out_27 ),
    .row25(\字库_2_out_28 ), .row26(\字库_2_out_29 ), .row27(\字库_2_out_30 ), .row28(\字库_2_out_31 ),
    .row29(\字库_2_out_32 ), .row30(\字库_2_out_33 ), .row31(\字库_2_out_34 ));

  // Notes on the sheet:
  //   计数器
  //   GB2312
  //   contents of rom_1 (hex, n*v repeats v):
  //   a3b0 a3b2 a3b3 a3b4 a3b5 a3c1 a3c2 a3c3 a3c4 a3c5 a3c6 a3c7 a3e1 a3e2 a3e3 a3e4 a3e5 a3e6 a3e7 c7e1
  //   c7e1 b5c4 ced2 d7df c1cb a3ac d5fd c8e7 ced2 c7e1 c7e1 b5c4 c0b4 a3bb ced2 c7e1 c7e1 b5c4 d5d0 cad6
  //   a3ac d7f7 b1f0 cef7 ccec b5c4 d4c6 b2ca a1a3 c4c7 bad3 c5cf b5c4 bdf0 c1f8 a3ac cac7 cfa6 d1f4 d6d0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
endmodule
